// Logisim project cpu24.circ as structural Verilog: 23 circuits, main circuit ◇单周期MIPS
module \单周期MIPS  (
);

  wire and_1_out, and_2_out, and_3_out, B, BGEZ, CLK, comparator_1_eq, Go, halt, JAL, JMP, JR, LBU, MemWrite,
       mips_alu_1_equal, not_1_out, not_2_out, not_3_out, not_4_out, not_5_out, or_1_out, RST, show,
       SignedExt, SV, Syscall, \硬布线控制器_1_alu_src , \硬布线控制器_1_beq , \硬布线控制器_1_bne , \硬布线控制器_1_memtoreg ,
       \硬布线控制器_1_regdst , \硬布线控制器_1_regwrite ;
  wire [1:1] or_2_out;
  wire [3:0] \硬布线控制器_1_alu_op ;
  wire [4:0] multiplexer_2_out, multiplexer_3_out, multiplexer_4_out, multiplexer_5_out, multiplexer_8_out;
  wire [7:0] multiplexer_9_out;
  wire [15:0] \总周期数 , \无条件分支数 , \条件分支成功数 ;
  wire [31:0] adder_1_out, adder_2_out, bit_extender_1_out, bit_extender_2_out, LedData, mips_alu_1_result,
       multiplexer_1_out, multiplexer_6_out, multiplexer_7_out, multiplexer_10_out, multiplexer_11_out,
       multiplexer_12_out, PC_q, R1, R2, ram_1_data, rom_1_data, shifter_1_out;

  Button \u_总复位  (.out(RST));
  Button \u_继续运行  (.out(Go));
  Clock clock_1 (.out(CLK));
  Hex_Digit_Display hex_digit_display_1 (.value(LedData[31:28]));  // open: dp
  Hex_Digit_Display hex_digit_display_2 (.value(LedData[27:24]));  // open: dp
  not not_1 (not_1_out, halt);
  or or_1 (or_1_out, not_1_out, Go);
  Multiplexer #(.select(2), .width(32), .enable("false")) multiplexer_1 (
    .in0(adder_1_out), .in1({adder_1_out[31:28], rom_1_data[25:0], 2'b00}), .in2(adder_2_out), .in3(R1),
    .out(multiplexer_1_out), .sel({or_2_out[1], JMP}));
  or or_2 (or_2_out[1], B, JR);
  Hex_Digit_Display hex_digit_display_3 (.value(LedData[19:16]));  // open: dp
  Hex_Digit_Display hex_digit_display_4 (.value(LedData[23:20]));  // open: dp
  Register #(.width(32)) PC (.D(multiplexer_1_out), .en(or_1_out), .Q(PC_q), .clk(CLK), .clr(RST));
  Hex_Digit_Display hex_digit_display_5 (.value(LedData[15:12]));  // open: dp
  Hex_Digit_Display hex_digit_display_6 (.value(LedData[11:8]));  // open: dp
  Hex_Digit_Display hex_digit_display_7 (.value(LedData[7:4]));  // open: dp
  Hex_Digit_Display hex_digit_display_8 (.value(LedData[3:0]));  // open: dp
  Adder #(.width(32)) adder_1 (.a(PC_q), .b(32'h4), .out(adder_1_out));  // open: cin, cout
  ROM #(.addrWidth(10), .dataWidth(32)) rom_1 (.addr(PC_q[11:2]), .data(rom_1_data));  // open: sel
  // Probe on \总周期数 
  // Probe on \无条件分支数 
  // Probe on \条件分支成功数 
  \硬布线控制器  \u_硬布线控制器_1  (
    .Func(rom_1_data[5:0]), .OP(rom_1_data[31:26]), .ALU_OP(\硬布线控制器_1_alu_op ),
    .MemToReg(\硬布线控制器_1_memtoreg ), .MemWrite(MemWrite), .ALU_SRC(\硬布线控制器_1_alu_src ),
    .RegWrite(\硬布线控制器_1_regwrite ), .SysCALL(Syscall), .SignedExt(SignedExt), .RegDst(\硬布线控制器_1_regdst ),
    .JR(JR), .JMP(JMP), .Beq(\硬布线控制器_1_beq ), .JAL(JAL), .Bne(\硬布线控制器_1_bne ), .SV(SV), .BGEZ(BGEZ), .LBU(LBU));
  Multiplexer #(.width(5), .enable("false")) multiplexer_2 (
    .in0(rom_1_data[25:21]), .in1(5'b00010), .out(multiplexer_2_out), .sel(Syscall));
  Multiplexer #(.width(5), .enable("false")) multiplexer_3 (
    .in0(rom_1_data[20:16]), .in1(5'b00100), .out(multiplexer_3_out), .sel(Syscall));
  Multiplexer #(.width(5), .enable("false")) multiplexer_4 (
    .in0(rom_1_data[20:16]), .in1(rom_1_data[15:11]), .out(multiplexer_4_out), .sel(\硬布线控制器_1_regdst ));
  Multiplexer #(.width(5), .enable("false")) multiplexer_5 (
    .in0(multiplexer_4_out), .in1({5{1'b1}}), .out(multiplexer_5_out), .sel(JAL));
  assign bit_extender_1_out = {{16{rom_1_data[15]}}, rom_1_data[15:0]};  // Bit_Extender bit_extender_1
  assign bit_extender_2_out = {{16{1'b0}}, rom_1_data[15:0]};  // Bit_Extender bit_extender_2
  MIPS_Regifile mips_regifile_1 (
    .Din(multiplexer_12_out), .Clk(CLK), .R1(R1), .R2(R2), .WE(\硬布线控制器_1_regwrite ),
    .W_num(multiplexer_5_out), .R1_num(multiplexer_2_out), .R2_num(multiplexer_3_out));
  Multiplexer #(.width(32), .enable("false")) multiplexer_6 (
    .in0(bit_extender_2_out), .in1(bit_extender_1_out), .out(multiplexer_6_out), .sel(SignedExt));
  // Probe on \硬布线控制器_1_alu_op 
  Multiplexer #(.width(32), .enable("false")) multiplexer_7 (
    .in0(R2), .in1(multiplexer_6_out), .out(multiplexer_7_out), .sel(\硬布线控制器_1_alu_src ));
  Multiplexer #(.width(5), .enable("false")) multiplexer_8 (
    .in0(rom_1_data[10:6]), .in1(R1[4:0]), .out(multiplexer_8_out), .sel(SV));
  Shifter #(.width(32)) shifter_1 (.in(multiplexer_6_out), .\dist (5'b00010), .out(shifter_1_out));
  not not_2 (not_2_out, mips_alu_1_equal);
  MIPS_ALU mips_alu_1 (
    .X(R1), .Y(multiplexer_7_out), .AluOP(\硬布线控制器_1_alu_op ), .Equal(mips_alu_1_equal),
    .Result(mips_alu_1_result), .shamt(multiplexer_8_out));  // open: Result_2
  Adder #(.width(32)) adder_2 (.a(shifter_1_out), .b(adder_1_out), .out(adder_2_out));  // open: cin, cout
  and and_1 (and_1_out, mips_alu_1_equal, \硬布线控制器_1_beq );
  and and_2 (and_2_out, not_2_out, \硬布线控制器_1_bne );
  and and_3 (and_3_out, BGEZ, not_3_out);
  not not_3 (not_3_out, mips_alu_1_result[0]);
  or or_3 (B, and_1_out, and_3_out, and_2_out);
  RAM #(.addrWidth(10), .dataWidth(32), .bus("separate")) ram_1 (
    .addr(mips_alu_1_result[11:2]), .din(R2), .data(ram_1_data), .str(MemWrite), .clk(CLK), .clr(RST));  // open: sel, ld
  Multiplexer #(.select(2), .width(8), .enable("false")) multiplexer_9 (
    .in0(ram_1_data[7:0]), .in1(ram_1_data[15:8]), .in2(ram_1_data[23:16]), .in3(ram_1_data[31:24]),
    .out(multiplexer_9_out), .sel(mips_alu_1_result[1:0]));
  Multiplexer #(.width(32), .enable("false")) multiplexer_10 (
    .in0(mips_alu_1_result), .in1(multiplexer_11_out), .out(multiplexer_10_out), .sel(\硬布线控制器_1_memtoreg ));
  Multiplexer #(.width(32), .enable("false")) multiplexer_11 (
    .in0(ram_1_data), .in1({{24{1'b0}}, multiplexer_9_out}), .out(multiplexer_11_out), .sel(LBU));
  // Probe on multiplexer_11_out
  Multiplexer #(.width(32), .enable("false")) multiplexer_12 (
    .in0(multiplexer_10_out), .in1(adder_1_out), .out(multiplexer_12_out), .sel(JAL));
  not not_4 (not_4_out, halt);
  Counter #(.width(16), .max('hffff)) counter_1 (
    .count(JMP), .Q(\无条件分支数 ), .clk(CLK), .clr(RST));  // open: load, D, carry
  Counter #(.width(16), .max('hffff)) counter_2 (
    .count(B), .Q(\条件分支成功数 ), .clk(CLK), .clr(RST));  // open: load, D, carry
  Counter #(.width(16), .max('hffff)) counter_3 (
    .count(not_4_out), .Q(\总周期数 ), .clk(CLK), .clr(RST));  // open: load, D, carry
  Comparator #(.width(32)) comparator_1 (.a(R1), .b(32'h22), .eq(comparator_1_eq));  // open: gt, lt
  Register #(.width(32)) register_1 (.D(R2), .en(show), .Q(LedData), .clk(CLK), .clr(RST));
  and and_4 (show, comparator_1_eq, Syscall);
  not not_5 (not_5_out, comparator_1_eq);
  and and_5 (halt, Syscall, not_5_out);

  // Notes on the sheet:
  //   总复位信号应将除ROM以外所有存储组件全部清零
  //   数码管输出应该用寄存器锁存，否则显示数据只能一闪而过
  //   可以通过项目增加Logisim库的方式将前几次实验完成的电路作为子电路引入到本电路中使用
  //   数码管输出
  //   指令存储器
  //   指令字
  //   contents of rom_1 (hex, n*v repeats v):
  //   20110001 8000c05 20110001 20120002 20130003 8000c09 20110001 20120002 20130003 8000c0d 20110001
  //   20120002 20130003 8000c11 20110001 20120002 20130003 c000cfc 20100001 20110001 118fc0 112020
  //   20020022 c 118882 12200001 8000c15 112020 20020022 c 20110001 118880 112020 20020022 c 12200001
  //   8000c1f 20110001 118fc0 112020 20020022 c 1188c3 112020 20020022 c 118903 112020 20020022 c 118903
  //   112020 20020022 c 118903 112020 20020022 c 118903 112020 20020022 c 118903 112020 20020022 c 118903
  //   112020 20020022 c 118903 112020 20020022 c 20100001 109fc0 139fc3 8021 2012000c 24160003 26100001
  //   3210000f 20080008 20090001 139900 2709825 132020 20020022 c 1094022 1500fff9 22100001 2018000f
  //   2188024 108700 20080008 20090001 139902 2709825 132021 20020022 c 1094022 1500fff9 108702 2c9b022
  //   12c00001 8000c50 4020 1084027 84400 3508ffff 82021 20020022 c 2010ffff 20110000 ae300000 22100001
  //   22310004 ae300000 22100001 22310004 ae300000 22100001 22310004 ae300000 22100001 22310004 ae300000
  //   22100001 22310004 ae300000 22100001 22310004 ae300000 22100001 22310004 ae300000 22100001 22310004
  //   ae300000 22100001 22310004 ae300000 22100001 22310004 ae300000 22100001 22310004 ae300000 22100001
  //   22310004 ae300000 22100001 22310004 ae300000 22100001 22310004 ae300000 22100001 22310004 ae300000
  //   22100001 22310004 22100001 8020 2011003c 8e130000 8e340000 274402a 11000002 ae330000 ae140000
  //   2231fffc 1611fff8 102020 20020022 c 22100004 2011003c 1611fff2 20020032 c 20080001 20090003 20110876
  //   118d00 112020 20020022 c 200b0008 1118806 1318806 112020 20020022 c 216bffff 1560fff9 2002000a c
  //   20080001 20090003 20110876 118d00 112020 20020022 c 200b0008 1118807 1318807 112020 20020022 c
  //   216bffff 1560fff9 2002000a c 20090000 200b0010 34118483 20120404 118c00 129400 36318281 22520404
  //   ad310000 2328820 21290004 216bffff 1560fffb 200b0020 20090000 91310000 112020 20020022 c 21290001
  //   216bffff 1560fff9 2002000a c 2011000f 112020 20020022 c 2231ffff 621fffb 2002000a c 2002000a c
  //   20100000 22100001 102020 20020022 c 22100002 102020 20020022 c 22100003 102020 20020022 c 22100004
  //   102020 20020022 c 22100005 102020 20020022 c 22100006 102020 20020022 c 22100007 102020 20020022 c
  //   22100008 102020 20020022 20020022 c 3e00008
  //   JMP
  //   JR
  //   OP
  //   Func
  //   OP
  //   Func
  //   rs
  //   rt
  //   rd
  //   shamt
  //   imm16
  //   imm26
  //   Beq
  //   Bne
  //   MemToReg
  //   MemWrite
  //   AluOP
  //   AluSrcB
  //   RegWrite
  //   JAL
  //   RegDst
  //   Syscall
endmodule

// 单周期硬布线控制器
module \硬布线控制器  (
  input  [5:0] OP,
  input  [5:0] Func,
  output [3:0] ALU_OP,
  output MemToReg,
  output MemWrite,
  output ALU_SRC,
  output RegWrite,
  output SysCALL,
  output SignedExt,
  output RegDst,
  output Beq,
  output Bne,
  output JR,
  output JMP,
  output JAL,
  output SV,
  output LBU,
  output BGEZ
);

  \运算控制器  \u_运算控制器_1  (
    .OP0(OP[0]), .OP1(OP[1]), .OP2(OP[2]), .OP3(OP[3]), .OP4(OP[4]), .OP5(OP[5]), .F0(Func[0]), .F1(Func[1]),
    .F2(Func[2]), .F3(Func[3]), .F4(Func[4]), .F5(Func[5]), .S0(ALU_OP[0]), .S1(ALU_OP[1]), .S2(ALU_OP[2]),
    .S3(ALU_OP[3]));
  \控制信号生成  \u_控制信号生成_1  (
    .OP0(OP[0]), .OP1(OP[1]), .OP2(OP[2]), .MemToReg(MemToReg), .OP3(OP[3]), .OP4(OP[4]), .OP5(OP[5]),
    .MemWrite(MemWrite), .F0(Func[0]), .F1(Func[1]), .F2(Func[2]), .F3(Func[3]), .F4(Func[4]), .F5(Func[5]),
    .ALU_SRC(ALU_SRC), .RegWrite(RegWrite), .SysCALL(SysCALL), .SignedExt(SignedExt), .RegDst(RegDst),
    .BEQ(Beq), .BNE(Bne), .JR(JR), .JMP(JMP), .JAL(JAL), .SV(SV), .BGEZ(BGEZ), .LBU(LBU));

  // Other names for the same wires on the sheet: OP_CODE[5:0] = OP

  // Notes on the sheet:
  //   运算器控制器，根据指令生成运算器功能选择信号
  //   控制信号生成，产生数据通路需要的其他控制信号
endmodule

// 运算器控制器
module \运算控制器  (
  input  OP0,
  input  OP1,
  input  OP2,
  input  OP3,
  input  OP4,
  input  OP5,
  input  F0,
  input  F1,
  input  F2,
  input  F3,
  input  F4,
  input  F5,
  output S0,
  output S1,
  output S2,
  output S3
);

  wire and_1_out, and_2_out, and_3_out, and_4_out, and_5_out, and_6_out, and_7_out, and_8_out, and_9_out,
       and_10_out, and_11_out, and_12_out, and_13_out, and_14_out, and_15_out, and_16_out, and_17_out,
       and_18_out, and_19_out, and_20_out, and_21_out, and_22_out, and_23_out, and_24_out, and_25_out,
       and_26_out, and_27_out, and_28_out, and_29_out, and_30_out, and_31_out, and_32_out, and_33_out,
       and_34_out, and_35_out, and_36_out, and_37_out, and_38_out, and_39_out, and_40_out, and_41_out,
       and_42_out, and_43_out, and_44_out, not_1_out, not_2_out, not_3_out, not_4_out, not_5_out, not_6_out,
       not_7_out, not_8_out, not_9_out, not_10_out, not_11_out, not_12_out, not_13_out, not_14_out,
       not_15_out, not_16_out, not_17_out, not_18_out, not_19_out, not_20_out, not_21_out, not_22_out,
       not_23_out, not_24_out, not_25_out, not_26_out, not_27_out, not_28_out, not_29_out, not_30_out,
       not_31_out, not_32_out, not_33_out, not_34_out, not_35_out, not_36_out, not_37_out, not_38_out,
       not_39_out, not_40_out, not_41_out, not_42_out, not_43_out, not_44_out, not_45_out, not_46_out,
       not_47_out, not_48_out, not_49_out, not_50_out, not_51_out, not_52_out, not_53_out, not_54_out,
       not_55_out, not_56_out, not_57_out, not_58_out, not_59_out, not_60_out, not_61_out, not_62_out,
       not_63_out, not_64_out, not_65_out, not_66_out, not_67_out, not_68_out, not_69_out, not_70_out,
       not_71_out, not_72_out, not_73_out, not_74_out, not_75_out, not_76_out, not_77_out, not_78_out,
       not_79_out, not_80_out, not_81_out, not_82_out, not_83_out, not_84_out, not_85_out, not_86_out,
       not_87_out, not_88_out, not_89_out, not_90_out, not_91_out, not_92_out, not_93_out, not_94_out,
       not_95_out, not_96_out, not_97_out, not_98_out, not_99_out, not_100_out, not_101_out, not_102_out,
       not_103_out, not_104_out, not_105_out, not_106_out, not_107_out, not_108_out, not_109_out,
       not_110_out, not_111_out, not_112_out, not_113_out, not_114_out, not_115_out, not_116_out,
       not_117_out, not_118_out, not_119_out, not_120_out, not_121_out, not_122_out, not_123_out,
       not_124_out, not_125_out, not_126_out, not_127_out, not_128_out, not_129_out, not_130_out,
       not_131_out, not_132_out, not_133_out, not_134_out, not_135_out, not_136_out, not_137_out,
       not_138_out, not_139_out, not_140_out, not_141_out, not_142_out, not_143_out, not_144_out,
       not_145_out, not_146_out, not_147_out, not_148_out, not_149_out, not_150_out, not_151_out,
       not_152_out, not_153_out, not_154_out, not_155_out, not_156_out, not_157_out, not_158_out,
       not_159_out, not_160_out, not_161_out, not_162_out, not_163_out, not_164_out, not_165_out,
       not_166_out, not_167_out, not_168_out, not_169_out, not_170_out, not_171_out, not_172_out,
       not_173_out, not_174_out, not_175_out, not_176_out, not_177_out, not_178_out, not_179_out,
       not_180_out, not_181_out, not_182_out, not_183_out, not_184_out, not_185_out, not_186_out,
       not_187_out, not_188_out, not_189_out, not_190_out, not_191_out, not_192_out, not_193_out,
       not_194_out, not_195_out, not_196_out, not_197_out, not_198_out, not_199_out, not_200_out,
       not_201_out, not_202_out, not_203_out, not_204_out, not_205_out, not_206_out, not_207_out,
       not_208_out, not_209_out, not_210_out, not_211_out, not_212_out, not_213_out, not_214_out,
       not_215_out, not_216_out, not_217_out, not_218_out, not_219_out, not_220_out, not_221_out,
       not_222_out, not_223_out, not_224_out, not_225_out, not_226_out, not_227_out, not_228_out,
       not_229_out, not_230_out, not_231_out, not_232_out, not_233_out, not_234_out, not_235_out,
       not_236_out, not_237_out, not_238_out, not_239_out, not_240_out, not_241_out, not_242_out,
       not_243_out, not_244_out, not_245_out, not_246_out, not_247_out, not_248_out, not_249_out,
       not_250_out, not_251_out, not_252_out, not_253_out, not_254_out, not_255_out, not_256_out,
       not_257_out, not_258_out, not_259_out, not_260_out, not_261_out, not_262_out, not_263_out,
       not_264_out, not_265_out, not_266_out, not_267_out, not_268_out, not_269_out, not_270_out,
       not_271_out, not_272_out, not_273_out, not_274_out, not_275_out, not_276_out, not_277_out,
       not_278_out, not_279_out, not_280_out, not_281_out, not_282_out, not_283_out, not_284_out,
       not_285_out, not_286_out, not_287_out, not_288_out, not_289_out, not_290_out, not_291_out,
       not_292_out, not_293_out, not_294_out, not_295_out, not_296_out, not_297_out, not_298_out,
       not_299_out, not_300_out, not_301_out, not_302_out, not_303_out, not_304_out, not_305_out,
       not_306_out, not_307_out, not_308_out;

  not not_1 (not_1_out, OP5);
  not not_2 (not_2_out, OP4);
  not not_3 (not_3_out, OP3);
  not not_4 (not_4_out, OP2);
  not not_5 (not_5_out, OP1);
  not not_6 (not_6_out, OP0);
  not not_7 (not_7_out, F5);
  not not_8 (not_8_out, F4);
  not not_9 (not_9_out, F3);
  not not_10 (not_10_out, F2);
  not not_11 (not_11_out, OP5);
  not not_12 (not_12_out, OP4);
  not not_13 (not_13_out, OP3);
  not not_14 (not_14_out, OP2);
  not not_15 (not_15_out, OP1);
  not not_16 (not_16_out, OP0);
  not not_17 (not_17_out, F4);
  not not_18 (not_18_out, F3);
  not not_19 (not_19_out, F2);
  not not_20 (not_20_out, F1);
  not not_21 (not_21_out, F0);
  not not_22 (not_22_out, OP5);
  not not_23 (not_23_out, OP4);
  not not_24 (not_24_out, OP3);
  not not_25 (not_25_out, OP2);
  not not_26 (not_26_out, OP1);
  not not_27 (not_27_out, OP0);
  not not_28 (not_28_out, F4);
  not not_29 (not_29_out, F3);
  not not_30 (not_30_out, F2);
  not not_31 (not_31_out, F1);
  not not_32 (not_32_out, OP5);
  not not_33 (not_33_out, OP4);
  not not_34 (not_34_out, OP3);
  not not_35 (not_35_out, OP2);
  not not_36 (not_36_out, OP1);
  not not_37 (not_37_out, OP0);
  not not_38 (not_38_out, F4);
  not not_39 (not_39_out, F3);
  not not_40 (not_40_out, F1);
  not not_41 (not_41_out, F0);
  not not_42 (not_42_out, OP5);
  not not_43 (not_43_out, OP4);
  not not_44 (not_44_out, OP3);
  not not_45 (not_45_out, OP2);
  not not_46 (not_46_out, OP1);
  not not_47 (not_47_out, OP0);
  not not_48 (not_48_out, F4);
  not not_49 (not_49_out, F2);
  not not_50 (not_50_out, F0);
  not not_51 (not_51_out, OP5);
  not not_52 (not_52_out, OP4);
  not not_53 (not_53_out, OP3);
  not not_54 (not_54_out, OP2);
  not not_55 (not_55_out, OP1);
  not not_56 (not_56_out, OP0);
  not not_57 (not_57_out, F5);
  not not_58 (not_58_out, F4);
  not not_59 (not_59_out, F1);
  not not_60 (not_60_out, F0);
  not not_61 (not_61_out, OP5);
  not not_62 (not_62_out, OP4);
  not not_63 (not_63_out, OP2);
  not not_64 (not_64_out, OP1);
  not not_65 (not_65_out, OP0);
  not not_66 (not_66_out, OP5);
  not not_67 (not_67_out, OP4);
  not not_68 (not_68_out, OP1);
  not not_69 (not_69_out, OP0);
  not not_70 (not_70_out, OP5);
  not not_71 (not_71_out, OP4);
  not not_72 (not_72_out, OP2);
  not not_73 (not_73_out, OP1);
  not not_74 (not_74_out, OP5);
  not not_75 (not_75_out, OP4);
  not not_76 (not_76_out, OP2);
  not not_77 (not_77_out, OP0);
  not not_78 (not_78_out, OP4);
  not not_79 (not_79_out, OP3);
  not not_80 (not_80_out, OP2);
  not not_81 (not_81_out, OP4);
  not not_82 (not_82_out, OP2);
  not not_83 (not_83_out, OP5);
  not not_84 (not_84_out, OP4);
  not not_85 (not_85_out, OP3);
  not not_86 (not_86_out, OP2);
  not not_87 (not_87_out, OP1);
  not not_88 (not_88_out, OP0);
  not not_89 (not_89_out, F5);
  not not_90 (not_90_out, F4);
  not not_91 (not_91_out, F3);
  not not_92 (not_92_out, OP4);
  not not_93 (not_93_out, OP3);
  not not_94 (not_94_out, OP1);
  not not_95 (not_95_out, OP0);
  not not_96 (not_96_out, OP5);
  not not_97 (not_97_out, OP4);
  not not_98 (not_98_out, OP3);
  not not_99 (not_99_out, OP2);
  not not_100 (not_100_out, OP1);
  not not_101 (not_101_out, OP5);
  not not_102 (not_102_out, OP4);
  not not_103 (not_103_out, OP3);
  not not_104 (not_104_out, OP2);
  not not_105 (not_105_out, OP1);
  not not_106 (not_106_out, OP0);
  not not_107 (not_107_out, F5);
  not not_108 (not_108_out, F4);
  not not_109 (not_109_out, F3);
  not not_110 (not_110_out, F2);
  not not_111 (not_111_out, F0);
  not not_112 (not_112_out, OP5);
  not not_113 (not_113_out, OP4);
  not not_114 (not_114_out, OP3);
  not not_115 (not_115_out, OP2);
  not not_116 (not_116_out, OP1);
  not not_117 (not_117_out, OP0);
  not not_118 (not_118_out, F4);
  not not_119 (not_119_out, F3);
  not not_120 (not_120_out, F2);
  not not_121 (not_121_out, F0);
  not not_122 (not_122_out, OP5);
  not not_123 (not_123_out, OP4);
  not not_124 (not_124_out, OP3);
  not not_125 (not_125_out, OP2);
  not not_126 (not_126_out, OP1);
  not not_127 (not_127_out, OP0);
  not not_128 (not_128_out, F4);
  not not_129 (not_129_out, F3);
  not not_130 (not_130_out, F1);
  not not_131 (not_131_out, F0);
  not not_132 (not_132_out, OP5);
  not not_133 (not_133_out, OP4);
  not not_134 (not_134_out, OP3);
  not not_135 (not_135_out, OP2);
  not not_136 (not_136_out, OP1);
  not not_137 (not_137_out, OP0);
  not not_138 (not_138_out, F4);
  not not_139 (not_139_out, F3);
  not not_140 (not_140_out, OP5);
  not not_141 (not_141_out, OP4);
  not not_142 (not_142_out, OP3);
  not not_143 (not_143_out, OP2);
  not not_144 (not_144_out, OP1);
  not not_145 (not_145_out, OP0);
  not not_146 (not_146_out, F4);
  not not_147 (not_147_out, F2);
  not not_148 (not_148_out, F0);
  not not_149 (not_149_out, OP5);
  not not_150 (not_150_out, OP4);
  not not_151 (not_151_out, OP3);
  not not_152 (not_152_out, OP2);
  not not_153 (not_153_out, OP1);
  not not_154 (not_154_out, OP0);
  not not_155 (not_155_out, F5);
  not not_156 (not_156_out, F4);
  not not_157 (not_157_out, F1);
  not not_158 (not_158_out, F0);
  not not_159 (not_159_out, OP5);
  not not_160 (not_160_out, OP4);
  not not_161 (not_161_out, OP1);
  not not_162 (not_162_out, OP0);
  not not_163 (not_163_out, OP5);
  not not_164 (not_164_out, OP4);
  not not_165 (not_165_out, OP2);
  not not_166 (not_166_out, OP0);
  not not_167 (not_167_out, OP5);
  not not_168 (not_168_out, OP4);
  not not_169 (not_169_out, OP3);
  not not_170 (not_170_out, OP2);
  not not_171 (not_171_out, OP1);
  not not_172 (not_172_out, OP0);
  not not_173 (not_173_out, F5);
  not not_174 (not_174_out, F4);
  not not_175 (not_175_out, F3);
  not not_176 (not_176_out, F0);
  not not_177 (not_177_out, OP5);
  not not_178 (not_178_out, OP4);
  not not_179 (not_179_out, OP3);
  not not_180 (not_180_out, OP2);
  not not_181 (not_181_out, OP1);
  not not_182 (not_182_out, OP5);
  not not_183 (not_183_out, OP4);
  not not_184 (not_184_out, OP3);
  not not_185 (not_185_out, OP2);
  not not_186 (not_186_out, OP1);
  not not_187 (not_187_out, OP0);
  not not_188 (not_188_out, F4);
  not not_189 (not_189_out, F3);
  not not_190 (not_190_out, F2);
  not not_191 (not_191_out, F1);
  not not_192 (not_192_out, F0);
  not not_193 (not_193_out, OP5);
  not not_194 (not_194_out, OP4);
  not not_195 (not_195_out, OP3);
  not not_196 (not_196_out, OP2);
  not not_197 (not_197_out, OP1);
  not not_198 (not_198_out, OP0);
  not not_199 (not_199_out, F4);
  not not_200 (not_200_out, F3);
  not not_201 (not_201_out, F2);
  not not_202 (not_202_out, F1);
  not not_203 (not_203_out, OP5);
  not not_204 (not_204_out, OP4);
  not not_205 (not_205_out, OP3);
  not not_206 (not_206_out, OP2);
  not not_207 (not_207_out, OP1);
  not not_208 (not_208_out, OP0);
  not not_209 (not_209_out, F4);
  not not_210 (not_210_out, F3);
  not not_211 (not_211_out, F2);
  not not_212 (not_212_out, F0);
  not not_213 (not_213_out, OP5);
  not not_214 (not_214_out, OP4);
  not not_215 (not_215_out, OP3);
  not not_216 (not_216_out, OP2);
  not not_217 (not_217_out, OP1);
  not not_218 (not_218_out, OP0);
  not not_219 (not_219_out, F4);
  not not_220 (not_220_out, F3);
  not not_221 (not_221_out, F1);
  not not_222 (not_222_out, F0);
  not not_223 (not_223_out, OP5);
  not not_224 (not_224_out, OP4);
  not not_225 (not_225_out, OP3);
  not not_226 (not_226_out, OP2);
  not not_227 (not_227_out, OP1);
  not not_228 (not_228_out, OP0);
  not not_229 (not_229_out, F4);
  not not_230 (not_230_out, F2);
  not not_231 (not_231_out, OP5);
  not not_232 (not_232_out, OP4);
  not not_233 (not_233_out, OP2);
  not not_234 (not_234_out, OP1);
  not not_235 (not_235_out, OP0);
  not not_236 (not_236_out, OP5);
  not not_237 (not_237_out, OP4);
  not not_238 (not_238_out, OP1);
  not not_239 (not_239_out, OP0);
  not not_240 (not_240_out, OP5);
  not not_241 (not_241_out, OP4);
  not not_242 (not_242_out, OP2);
  not not_243 (not_243_out, OP1);
  not not_244 (not_244_out, OP4);
  not not_245 (not_245_out, OP3);
  not not_246 (not_246_out, OP2);
  not not_247 (not_247_out, OP4);
  not not_248 (not_248_out, OP2);
  not not_249 (not_249_out, OP4);
  not not_250 (not_250_out, OP3);
  not not_251 (not_251_out, OP1);
  not not_252 (not_252_out, OP0);
  not not_253 (not_253_out, OP5);
  not not_254 (not_254_out, OP4);
  not not_255 (not_255_out, OP3);
  not not_256 (not_256_out, OP2);
  not not_257 (not_257_out, OP1);
  not not_258 (not_258_out, OP0);
  not not_259 (not_259_out, F4);
  not not_260 (not_260_out, F3);
  not not_261 (not_261_out, F1);
  not not_262 (not_262_out, OP5);
  not not_263 (not_263_out, OP4);
  not not_264 (not_264_out, OP3);
  not not_265 (not_265_out, OP2);
  not not_266 (not_266_out, OP1);
  not not_267 (not_267_out, OP0);
  not not_268 (not_268_out, F4);
  not not_269 (not_269_out, F3);
  not not_270 (not_270_out, OP5);
  not not_271 (not_271_out, OP4);
  not not_272 (not_272_out, OP3);
  not not_273 (not_273_out, OP2);
  not not_274 (not_274_out, OP1);
  not not_275 (not_275_out, OP0);
  not not_276 (not_276_out, F4);
  not not_277 (not_277_out, F2);
  not not_278 (not_278_out, F0);
  not not_279 (not_279_out, OP5);
  not not_280 (not_280_out, OP4);
  not not_281 (not_281_out, OP3);
  not not_282 (not_282_out, OP2);
  not not_283 (not_283_out, OP1);
  not not_284 (not_284_out, OP0);
  not not_285 (not_285_out, F4);
  not not_286 (not_286_out, F2);
  not not_287 (not_287_out, OP5);
  not not_288 (not_288_out, OP4);
  not not_289 (not_289_out, OP3);
  not not_290 (not_290_out, OP2);
  not not_291 (not_291_out, OP1);
  not not_292 (not_292_out, OP0);
  not not_293 (not_293_out, F5);
  not not_294 (not_294_out, F4);
  not not_295 (not_295_out, F1);
  not not_296 (not_296_out, F0);
  not not_297 (not_297_out, OP5);
  not not_298 (not_298_out, OP4);
  not not_299 (not_299_out, OP2);
  not not_300 (not_300_out, OP0);
  not not_301 (not_301_out, OP5);
  not not_302 (not_302_out, OP4);
  not not_303 (not_303_out, OP1);
  not not_304 (not_304_out, OP5);
  not not_305 (not_305_out, OP4);
  not not_306 (not_306_out, OP3);
  not not_307 (not_307_out, OP2);
  not not_308 (not_308_out, OP1);
  and and_1 (and_1_out, not_1_out, not_2_out, not_3_out, not_4_out, not_5_out, not_6_out, not_7_out, not_8_out, not_9_out, not_10_out, F1, F0);
  and and_2 (and_2_out, not_11_out, not_12_out, not_13_out, not_14_out, not_15_out, not_16_out, F5, not_17_out, not_18_out, not_19_out, not_20_out, not_21_out);
  and and_3 (and_3_out, not_22_out, not_23_out, not_24_out, not_25_out, not_26_out, not_27_out, F5, not_28_out, not_29_out, not_30_out, not_31_out, F0);
  and and_4 (and_4_out, not_32_out, not_33_out, not_34_out, not_35_out, not_36_out, not_37_out, F5, not_38_out, not_39_out, F2, not_40_out, not_41_out);
  and and_5 (and_5_out, not_42_out, not_43_out, not_44_out, not_45_out, not_46_out, not_47_out, F5, not_48_out, F3, not_49_out, F1, not_50_out);
  and and_6 (and_6_out, not_51_out, not_52_out, not_53_out, not_54_out, not_55_out, not_56_out, not_57_out, not_58_out, F3, F2, not_59_out, not_60_out);
  and and_7 (and_7_out, not_61_out, not_62_out, OP3, not_63_out, not_64_out, not_65_out);
  and and_8 (and_8_out, not_66_out, not_67_out, OP3, OP2, not_68_out, not_69_out);
  and and_9 (and_9_out, not_70_out, not_71_out, OP3, not_72_out, not_73_out, OP0);
  and and_10 (and_10_out, not_74_out, not_75_out, OP3, not_76_out, OP1, not_77_out);
  and and_11 (and_11_out, OP5, not_78_out, not_79_out, not_80_out, OP1, OP0);
  and and_12 (and_12_out, OP5, not_81_out, OP3, not_82_out, OP1, OP0);
  and and_13 (and_13_out, not_83_out, not_84_out, not_85_out, not_86_out, not_87_out, not_88_out, not_89_out, not_90_out, not_91_out, F2, F1, F0);
  and and_14 (and_14_out, OP5, not_92_out, not_93_out, OP2, not_94_out, not_95_out);
  and and_15 (and_15_out, not_96_out, not_97_out, not_98_out, not_99_out, not_100_out, OP0);
  and and_16 (and_16_out, not_101_out, not_102_out, not_103_out, not_104_out, not_105_out, not_106_out, not_107_out, not_108_out, not_109_out, not_110_out, F1, not_111_out);
  and and_17 (and_17_out, not_112_out, not_113_out, not_114_out, not_115_out, not_116_out, not_117_out, F5, not_118_out, not_119_out, not_120_out, F1, not_121_out);
  and and_18 (and_18_out, not_122_out, not_123_out, not_124_out, not_125_out, not_126_out, not_127_out, F5, not_128_out, not_129_out, F2, not_130_out, not_131_out);
  and and_19 (and_19_out, not_132_out, not_133_out, not_134_out, not_135_out, not_136_out, not_137_out, F5, not_138_out, not_139_out, F2, F1, F0);
  and and_20 (and_20_out, not_140_out, not_141_out, not_142_out, not_143_out, not_144_out, not_145_out, F5, not_146_out, F3, not_147_out, F1, not_148_out);
  and and_21 (and_21_out, not_149_out, not_150_out, not_151_out, not_152_out, not_153_out, not_154_out, not_155_out, not_156_out, F3, F2, not_157_out, not_158_out);
  and and_22 (and_22_out, not_159_out, not_160_out, OP3, OP2, not_161_out, not_162_out);
  and and_23 (and_23_out, not_163_out, not_164_out, OP3, not_165_out, OP1, not_166_out);
  and and_24 (and_24_out, not_167_out, not_168_out, not_169_out, not_170_out, not_171_out, not_172_out, not_173_out, not_174_out, not_175_out, F2, F1, not_176_out);
  and and_25 (and_25_out, not_177_out, not_178_out, not_179_out, not_180_out, not_181_out, OP0);
  and and_26 (and_26_out, not_182_out, not_183_out, not_184_out, not_185_out, not_186_out, not_187_out, F5, not_188_out, not_189_out, not_190_out, not_191_out, not_192_out);
  and and_27 (and_27_out, not_193_out, not_194_out, not_195_out, not_196_out, not_197_out, not_198_out, F5, not_199_out, not_200_out, not_201_out, not_202_out, F0);
  and and_28 (and_28_out, not_203_out, not_204_out, not_205_out, not_206_out, not_207_out, not_208_out, F5, not_209_out, not_210_out, not_211_out, F1, not_212_out);
  and and_29 (and_29_out, not_213_out, not_214_out, not_215_out, not_216_out, not_217_out, not_218_out, F5, not_219_out, not_220_out, F2, not_221_out, not_222_out);
  and and_30 (and_30_out, not_223_out, not_224_out, not_225_out, not_226_out, not_227_out, not_228_out, F5, not_229_out, F3, not_230_out, F1, F0);
  and and_31 (and_31_out, not_231_out, not_232_out, OP3, not_233_out, not_234_out, not_235_out);
  and and_32 (and_32_out, not_236_out, not_237_out, OP3, OP2, not_238_out, not_239_out);
  and and_33 (and_33_out, not_240_out, not_241_out, OP3, not_242_out, not_243_out, OP0);
  and and_34 (and_34_out, OP5, not_244_out, not_245_out, not_246_out, OP1, OP0);
  and and_35 (and_35_out, OP5, not_247_out, OP3, not_248_out, OP1, OP0);
  and and_36 (and_36_out, OP5, not_249_out, not_250_out, OP2, not_251_out, not_252_out);
  and and_37 (and_37_out, not_253_out, not_254_out, not_255_out, not_256_out, not_257_out, not_258_out, F5, not_259_out, not_260_out, F2, not_261_out, F0);
  and and_38 (and_38_out, not_262_out, not_263_out, not_264_out, not_265_out, not_266_out, not_267_out, F5, not_268_out, not_269_out, F2, F1, F0);
  and and_39 (and_39_out, not_270_out, not_271_out, not_272_out, not_273_out, not_274_out, not_275_out, F5, not_276_out, F3, not_277_out, F1, not_278_out);
  and and_40 (and_40_out, not_279_out, not_280_out, not_281_out, not_282_out, not_283_out, not_284_out, F5, not_285_out, F3, not_286_out, F1, F0);
  and and_41 (and_41_out, not_287_out, not_288_out, not_289_out, not_290_out, not_291_out, not_292_out, not_293_out, not_294_out, F3, F2, not_295_out, not_296_out);
  and and_42 (and_42_out, not_297_out, not_298_out, OP3, not_299_out, OP1, not_300_out);
  and and_43 (and_43_out, not_301_out, not_302_out, OP3, OP2, not_303_out, OP0);
  and and_44 (and_44_out, not_304_out, not_305_out, not_306_out, not_307_out, not_308_out, OP0);
  or or_1 (S1, and_16_out, and_17_out, and_18_out, and_19_out, and_20_out, and_21_out, and_22_out, and_23_out, and_24_out, and_25_out);
  or or_2 (S2, and_26_out, and_27_out, and_28_out, and_29_out, and_30_out, and_31_out, and_32_out, and_33_out, and_34_out, and_35_out, and_36_out);
  or or_3 (S3, and_37_out, and_38_out, and_39_out, and_40_out, and_41_out, and_42_out, and_43_out, and_44_out);
  or or_4 (S0, and_1_out, and_2_out, and_3_out, and_4_out, and_5_out, and_6_out, and_7_out, and_8_out, and_9_out, and_10_out, and_11_out, and_12_out, and_13_out, and_14_out, and_15_out);
endmodule

// 控制信号生成
module \控制信号生成  (
  input  OP0,
  input  OP1,
  input  OP2,
  input  OP3,
  input  OP4,
  input  OP5,
  input  F0,
  input  F1,
  input  F2,
  input  F3,
  input  F4,
  input  F5,
  output MemToReg,
  output MemWrite,
  output ALU_SRC,
  output RegWrite,
  output SysCALL,
  output SignedExt,
  output LBU,
  output BGEZ,
  output RegDst,
  output SV,
  output BEQ,
  output BNE,
  output JR,
  output JMP,
  output JAL
);

  wire and_1_out, and_2_out, and_4_out, and_5_out, and_6_out, and_7_out, and_8_out, and_9_out, and_10_out,
       and_11_out, and_12_out, and_13_out, and_14_out, and_15_out, and_16_out, and_17_out, and_18_out,
       and_19_out, and_20_out, and_21_out, and_22_out, and_23_out, and_24_out, and_25_out, and_26_out,
       and_27_out, and_28_out, and_29_out, and_30_out, and_31_out, and_32_out, and_34_out, and_35_out,
       and_36_out, and_37_out, and_38_out, and_39_out, and_40_out, and_41_out, and_44_out, and_45_out,
       and_46_out, and_47_out, and_48_out, and_49_out, and_50_out, and_51_out, and_52_out, and_53_out,
       and_54_out, and_55_out, and_56_out, and_60_out, and_61_out, and_62_out, not_1_out, not_2_out,
       not_3_out, not_4_out, not_5_out, not_6_out, not_7_out, not_8_out, not_9_out, not_10_out, not_11_out,
       not_12_out, not_13_out, not_14_out, not_15_out, not_16_out, not_17_out, not_18_out, not_19_out,
       not_20_out, not_21_out, not_22_out, not_23_out, not_24_out, not_25_out, not_26_out, not_27_out,
       not_28_out, not_29_out, not_30_out, not_31_out, not_32_out, not_33_out, not_34_out, not_35_out,
       not_36_out, not_37_out, not_38_out, not_39_out, not_40_out, not_41_out, not_42_out, not_43_out,
       not_44_out, not_45_out, not_46_out, not_47_out, not_48_out, not_49_out, not_50_out, not_51_out,
       not_52_out, not_53_out, not_54_out, not_55_out, not_56_out, not_57_out, not_58_out, not_59_out,
       not_60_out, not_61_out, not_62_out, not_63_out, not_64_out, not_65_out, not_66_out, not_67_out,
       not_68_out, not_69_out, not_70_out, not_71_out, not_72_out, not_73_out, not_74_out, not_75_out,
       not_76_out, not_77_out, not_78_out, not_79_out, not_80_out, not_81_out, not_82_out, not_83_out,
       not_84_out, not_85_out, not_86_out, not_87_out, not_88_out, not_89_out, not_90_out, not_91_out,
       not_92_out, not_93_out, not_94_out, not_95_out, not_96_out, not_97_out, not_98_out, not_99_out,
       not_100_out, not_101_out, not_102_out, not_103_out, not_104_out, not_105_out, not_106_out,
       not_107_out, not_108_out, not_109_out, not_110_out, not_111_out, not_112_out, not_113_out,
       not_114_out, not_115_out, not_116_out, not_117_out, not_118_out, not_119_out, not_120_out,
       not_121_out, not_122_out, not_123_out, not_124_out, not_125_out, not_126_out, not_127_out,
       not_128_out, not_129_out, not_130_out, not_131_out, not_132_out, not_133_out, not_134_out,
       not_135_out, not_136_out, not_137_out, not_138_out, not_139_out, not_140_out, not_141_out,
       not_142_out, not_143_out, not_144_out, not_145_out, not_146_out, not_147_out, not_148_out,
       not_149_out, not_150_out, not_151_out, not_152_out, not_153_out, not_154_out, not_155_out,
       not_156_out, not_157_out, not_158_out, not_159_out, not_160_out, not_161_out, not_162_out,
       not_163_out, not_164_out, not_165_out, not_166_out, not_167_out, not_168_out, not_169_out,
       not_170_out, not_171_out, not_172_out, not_173_out, not_174_out, not_175_out, not_176_out,
       not_177_out, not_178_out, not_179_out, not_180_out, not_181_out, not_182_out, not_183_out,
       not_184_out, not_185_out, not_186_out, not_187_out, not_188_out, not_189_out, not_190_out,
       not_191_out, not_192_out, not_193_out, not_194_out, not_195_out, not_196_out, not_197_out,
       not_198_out, not_199_out, not_200_out, not_201_out, not_202_out, not_203_out, not_204_out,
       not_205_out, not_206_out, not_207_out, not_208_out, not_209_out, not_210_out, not_211_out,
       not_212_out, not_213_out, not_214_out, not_215_out, not_216_out, not_217_out, not_218_out,
       not_219_out, not_220_out, not_221_out, not_222_out, not_223_out, not_224_out, not_225_out,
       not_226_out, not_227_out, not_228_out, not_229_out, not_230_out, not_231_out, not_232_out,
       not_233_out, not_234_out, not_235_out, not_236_out, not_237_out, not_238_out, not_239_out,
       not_240_out, not_241_out, not_242_out, not_243_out, not_244_out, not_245_out, not_246_out,
       not_247_out, not_248_out, not_249_out, not_250_out, not_251_out, not_252_out, not_253_out,
       not_254_out, not_255_out, not_256_out, not_257_out, not_258_out, not_259_out, not_260_out,
       not_261_out, not_262_out, not_263_out, not_264_out, not_265_out, not_266_out, not_267_out,
       not_268_out, not_269_out, not_270_out, not_271_out, not_272_out, not_273_out, not_274_out,
       not_275_out, not_276_out, not_277_out, not_278_out, not_279_out, not_280_out, not_281_out,
       not_282_out, not_283_out, not_284_out, not_285_out, not_286_out, not_287_out, not_288_out,
       not_289_out, not_290_out, not_291_out, not_292_out, not_293_out, not_294_out, not_295_out,
       not_296_out, not_297_out, not_298_out, not_299_out, not_300_out, not_301_out, not_302_out,
       not_303_out, not_304_out, not_305_out, not_306_out, not_307_out, not_308_out, not_309_out,
       not_310_out, not_311_out, not_312_out, not_313_out, not_314_out, not_315_out, not_316_out,
       not_317_out, not_318_out, not_319_out, not_320_out, not_321_out, not_322_out, not_323_out,
       not_324_out, not_325_out, not_326_out, not_327_out, not_328_out, not_329_out, not_330_out,
       not_331_out, not_332_out, not_333_out, not_334_out, not_335_out, not_336_out, not_337_out,
       not_338_out, not_339_out, not_340_out, not_341_out, not_342_out, not_343_out, not_344_out,
       not_345_out, not_346_out, not_347_out, not_348_out, not_349_out, not_350_out, not_351_out,
       not_352_out, not_353_out, not_354_out, not_355_out, not_356_out, not_357_out, not_358_out,
       not_359_out, not_360_out, not_361_out, not_362_out, not_363_out, not_364_out, not_365_out,
       not_366_out, not_367_out, not_368_out, not_369_out, not_370_out, not_371_out, not_372_out,
       not_373_out, not_374_out, not_375_out, not_376_out, not_377_out, not_378_out, not_379_out,
       not_380_out, not_381_out, not_382_out, not_383_out, not_384_out, not_385_out, not_386_out,
       not_387_out, not_388_out, not_389_out, not_390_out, not_391_out, not_392_out, not_393_out,
       not_394_out, not_395_out, not_396_out, not_397_out, not_398_out, not_399_out, not_400_out,
       not_401_out, not_402_out, not_403_out, not_404_out, not_405_out, not_406_out, not_407_out,
       not_408_out, not_409_out, not_410_out, not_411_out, not_412_out, not_413_out, not_414_out,
       not_415_out, not_416_out, not_417_out, not_418_out, not_419_out, not_420_out, not_421_out,
       not_422_out, not_423_out, not_424_out;

  not not_1 (not_1_out, OP4);
  not not_2 (not_2_out, OP3);
  not not_3 (not_3_out, OP2);
  not not_4 (not_4_out, OP4);
  not not_5 (not_5_out, OP3);
  not not_6 (not_6_out, OP1);
  not not_7 (not_7_out, OP0);
  not not_8 (not_8_out, OP4);
  not not_9 (not_9_out, OP2);
  not not_10 (not_10_out, OP5);
  not not_11 (not_11_out, OP4);
  not not_12 (not_12_out, OP2);
  not not_13 (not_13_out, OP1);
  not not_14 (not_14_out, OP0);
  not not_15 (not_15_out, OP5);
  not not_16 (not_16_out, OP4);
  not not_17 (not_17_out, OP1);
  not not_18 (not_18_out, OP0);
  not not_19 (not_19_out, OP5);
  not not_20 (not_20_out, OP4);
  not not_21 (not_21_out, OP2);
  not not_22 (not_22_out, OP1);
  not not_23 (not_23_out, OP5);
  not not_24 (not_24_out, OP4);
  not not_25 (not_25_out, OP2);
  not not_26 (not_26_out, OP0);
  not not_27 (not_27_out, OP5);
  not not_28 (not_28_out, OP4);
  not not_29 (not_29_out, OP1);
  not not_30 (not_30_out, OP4);
  not not_31 (not_31_out, OP3);
  not not_32 (not_32_out, OP2);
  not not_33 (not_33_out, OP4);
  not not_34 (not_34_out, OP2);
  not not_35 (not_35_out, OP4);
  not not_36 (not_36_out, OP3);
  not not_37 (not_37_out, OP1);
  not not_38 (not_38_out, OP0);
  not not_39 (not_39_out, OP5);
  not not_40 (not_40_out, OP4);
  not not_41 (not_41_out, OP3);
  not not_42 (not_42_out, OP2);
  not not_43 (not_43_out, OP1);
  not not_44 (not_44_out, OP0);
  not not_45 (not_45_out, F5);
  not not_46 (not_46_out, F4);
  not not_47 (not_47_out, F3);
  not not_48 (not_48_out, F2);
  not not_49 (not_49_out, F1);
  not not_50 (not_50_out, F0);
  not not_51 (not_51_out, OP5);
  not not_52 (not_52_out, OP4);
  not not_53 (not_53_out, OP3);
  not not_54 (not_54_out, OP2);
  not not_55 (not_55_out, OP1);
  not not_56 (not_56_out, OP0);
  not not_57 (not_57_out, F5);
  not not_58 (not_58_out, F4);
  not not_59 (not_59_out, F3);
  not not_60 (not_60_out, F2);
  not not_61 (not_61_out, OP5);
  not not_62 (not_62_out, OP4);
  not not_63 (not_63_out, OP3);
  not not_64 (not_64_out, OP2);
  not not_65 (not_65_out, OP1);
  not not_66 (not_66_out, OP0);
  not not_67 (not_67_out, F5);
  not not_68 (not_68_out, F4);
  not not_69 (not_69_out, F3);
  not not_70 (not_70_out, F2);
  not not_71 (not_71_out, F0);
  not not_72 (not_72_out, OP5);
  not not_73 (not_73_out, OP4);
  not not_74 (not_74_out, OP3);
  not not_75 (not_75_out, OP2);
  not not_76 (not_76_out, OP1);
  not not_77 (not_77_out, OP0);
  not not_78 (not_78_out, F4);
  not not_79 (not_79_out, F3);
  not not_80 (not_80_out, F2);
  not not_81 (not_81_out, F1);
  not not_82 (not_82_out, F0);
  not not_83 (not_83_out, OP5);
  not not_84 (not_84_out, OP4);
  not not_85 (not_85_out, OP3);
  not not_86 (not_86_out, OP2);
  not not_87 (not_87_out, OP1);
  not not_88 (not_88_out, OP0);
  not not_89 (not_89_out, F4);
  not not_90 (not_90_out, F3);
  not not_91 (not_91_out, F2);
  not not_92 (not_92_out, F1);
  not not_93 (not_93_out, OP5);
  not not_94 (not_94_out, OP4);
  not not_95 (not_95_out, OP3);
  not not_96 (not_96_out, OP2);
  not not_97 (not_97_out, OP1);
  not not_98 (not_98_out, OP0);
  not not_99 (not_99_out, F4);
  not not_100 (not_100_out, F3);
  not not_101 (not_101_out, F2);
  not not_102 (not_102_out, F0);
  not not_103 (not_103_out, OP5);
  not not_104 (not_104_out, OP4);
  not not_105 (not_105_out, OP3);
  not not_106 (not_106_out, OP2);
  not not_107 (not_107_out, OP1);
  not not_108 (not_108_out, OP0);
  not not_109 (not_109_out, F4);
  not not_110 (not_110_out, F3);
  not not_111 (not_111_out, F1);
  not not_112 (not_112_out, F0);
  not not_113 (not_113_out, OP5);
  not not_114 (not_114_out, OP4);
  not not_115 (not_115_out, OP3);
  not not_116 (not_116_out, OP2);
  not not_117 (not_117_out, OP1);
  not not_118 (not_118_out, OP0);
  not not_119 (not_119_out, F4);
  not not_120 (not_120_out, F3);
  not not_121 (not_121_out, F1);
  not not_122 (not_122_out, OP5);
  not not_123 (not_123_out, OP4);
  not not_124 (not_124_out, OP3);
  not not_125 (not_125_out, OP2);
  not not_126 (not_126_out, OP1);
  not not_127 (not_127_out, OP0);
  not not_128 (not_128_out, F4);
  not not_129 (not_129_out, F3);
  not not_130 (not_130_out, OP5);
  not not_131 (not_131_out, OP4);
  not not_132 (not_132_out, OP3);
  not not_133 (not_133_out, OP2);
  not not_134 (not_134_out, OP1);
  not not_135 (not_135_out, OP0);
  not not_136 (not_136_out, F4);
  not not_137 (not_137_out, F2);
  not not_138 (not_138_out, F0);
  not not_139 (not_139_out, OP5);
  not not_140 (not_140_out, OP4);
  not not_141 (not_141_out, OP3);
  not not_142 (not_142_out, OP2);
  not not_143 (not_143_out, OP1);
  not not_144 (not_144_out, OP0);
  not not_145 (not_145_out, F4);
  not not_146 (not_146_out, F2);
  not not_147 (not_147_out, OP5);
  not not_148 (not_148_out, OP4);
  not not_149 (not_149_out, OP3);
  not not_150 (not_150_out, OP2);
  not not_151 (not_151_out, OP5);
  not not_152 (not_152_out, OP4);
  not not_153 (not_153_out, OP2);
  not not_154 (not_154_out, OP1);
  not not_155 (not_155_out, OP0);
  not not_156 (not_156_out, OP5);
  not not_157 (not_157_out, OP4);
  not not_158 (not_158_out, OP1);
  not not_159 (not_159_out, OP0);
  not not_160 (not_160_out, OP5);
  not not_161 (not_161_out, OP4);
  not not_162 (not_162_out, OP2);
  not not_163 (not_163_out, OP1);
  not not_164 (not_164_out, OP5);
  not not_165 (not_165_out, OP4);
  not not_166 (not_166_out, OP2);
  not not_167 (not_167_out, OP0);
  not not_168 (not_168_out, OP5);
  not not_169 (not_169_out, OP4);
  not not_170 (not_170_out, OP1);
  not not_171 (not_171_out, OP4);
  not not_172 (not_172_out, OP3);
  not not_173 (not_173_out, OP2);
  not not_174 (not_174_out, OP5);
  not not_175 (not_175_out, OP4);
  not not_176 (not_176_out, OP3);
  not not_177 (not_177_out, OP2);
  not not_178 (not_178_out, OP1);
  not not_179 (not_179_out, OP0);
  not not_180 (not_180_out, F5);
  not not_181 (not_181_out, F4);
  not not_182 (not_182_out, F3);
  not not_183 (not_183_out, F0);
  not not_184 (not_184_out, OP5);
  not not_185 (not_185_out, OP4);
  not not_186 (not_186_out, OP3);
  not not_187 (not_187_out, OP2);
  not not_188 (not_188_out, OP1);
  not not_189 (not_189_out, OP0);
  not not_190 (not_190_out, F5);
  not not_191 (not_191_out, F4);
  not not_192 (not_192_out, F3);
  not not_193 (not_193_out, OP4);
  not not_194 (not_194_out, OP3);
  not not_195 (not_195_out, OP1);
  not not_196 (not_196_out, OP0);
  not not_197 (not_197_out, OP5);
  not not_198 (not_198_out, OP4);
  not not_199 (not_199_out, OP3);
  not not_200 (not_200_out, OP2);
  not not_201 (not_201_out, OP1);
  not not_202 (not_202_out, OP0);
  not not_203 (not_203_out, F5);
  not not_204 (not_204_out, F4);
  not not_205 (not_205_out, F1);
  not not_206 (not_206_out, F0);
  not not_207 (not_207_out, OP5);
  not not_208 (not_208_out, OP4);
  not not_209 (not_209_out, OP3);
  not not_210 (not_210_out, OP2);
  not not_211 (not_211_out, OP1);
  not not_212 (not_212_out, OP0);
  not not_213 (not_213_out, F5);
  not not_214 (not_214_out, F4);
  not not_215 (not_215_out, F2);
  not not_216 (not_216_out, F1);
  not not_217 (not_217_out, F0);
  not not_218 (not_218_out, OP5);
  not not_219 (not_219_out, OP4);
  not not_220 (not_220_out, OP3);
  not not_221 (not_221_out, OP1);
  not not_222 (not_222_out, OP0);
  not not_223 (not_223_out, OP5);
  not not_224 (not_224_out, OP4);
  not not_225 (not_225_out, OP3);
  not not_226 (not_226_out, OP1);
  not not_227 (not_227_out, OP5);
  not not_228 (not_228_out, OP4);
  not not_229 (not_229_out, OP2);
  not not_230 (not_230_out, OP1);
  not not_231 (not_231_out, OP0);
  not not_232 (not_232_out, OP5);
  not not_233 (not_233_out, OP4);
  not not_234 (not_234_out, OP2);
  not not_235 (not_235_out, OP1);
  not not_236 (not_236_out, OP5);
  not not_237 (not_237_out, OP4);
  not not_238 (not_238_out, OP2);
  not not_239 (not_239_out, OP0);
  not not_240 (not_240_out, OP4);
  not not_241 (not_241_out, OP3);
  not not_242 (not_242_out, OP2);
  not not_243 (not_243_out, OP4);
  not not_244 (not_244_out, OP2);
  not not_245 (not_245_out, OP4);
  not not_246 (not_246_out, OP3);
  not not_247 (not_247_out, OP1);
  not not_248 (not_248_out, OP0);
  not not_249 (not_249_out, OP5);
  not not_250 (not_250_out, OP4);
  not not_251 (not_251_out, OP3);
  not not_252 (not_252_out, OP2);
  not not_253 (not_253_out, OP1);
  not not_254 (not_254_out, OP5);
  not not_255 (not_255_out, OP4);
  not not_256 (not_256_out, OP3);
  not not_257 (not_257_out, OP2);
  not not_258 (not_258_out, OP1);
  not not_259 (not_259_out, OP0);
  not not_260 (not_260_out, F5);
  not not_261 (not_261_out, F4);
  not not_262 (not_262_out, F3);
  not not_263 (not_263_out, F2);
  not not_264 (not_264_out, F1);
  not not_265 (not_265_out, F0);
  not not_266 (not_266_out, OP5);
  not not_267 (not_267_out, OP4);
  not not_268 (not_268_out, OP3);
  not not_269 (not_269_out, OP2);
  not not_270 (not_270_out, OP1);
  not not_271 (not_271_out, OP0);
  not not_272 (not_272_out, F5);
  not not_273 (not_273_out, F4);
  not not_274 (not_274_out, F3);
  not not_275 (not_275_out, F2);
  not not_276 (not_276_out, OP5);
  not not_277 (not_277_out, OP4);
  not not_278 (not_278_out, OP3);
  not not_279 (not_279_out, OP2);
  not not_280 (not_280_out, OP1);
  not not_281 (not_281_out, OP0);
  not not_282 (not_282_out, F5);
  not not_283 (not_283_out, F4);
  not not_284 (not_284_out, F3);
  not not_285 (not_285_out, F2);
  not not_286 (not_286_out, F0);
  not not_287 (not_287_out, OP5);
  not not_288 (not_288_out, OP4);
  not not_289 (not_289_out, OP3);
  not not_290 (not_290_out, OP2);
  not not_291 (not_291_out, OP1);
  not not_292 (not_292_out, OP0);
  not not_293 (not_293_out, F4);
  not not_294 (not_294_out, F3);
  not not_295 (not_295_out, F2);
  not not_296 (not_296_out, F1);
  not not_297 (not_297_out, F0);
  not not_298 (not_298_out, OP5);
  not not_299 (not_299_out, OP4);
  not not_300 (not_300_out, OP3);
  not not_301 (not_301_out, OP2);
  not not_302 (not_302_out, OP1);
  not not_303 (not_303_out, OP0);
  not not_304 (not_304_out, F4);
  not not_305 (not_305_out, F3);
  not not_306 (not_306_out, F2);
  not not_307 (not_307_out, F1);
  not not_308 (not_308_out, OP5);
  not not_309 (not_309_out, OP4);
  not not_310 (not_310_out, OP3);
  not not_311 (not_311_out, OP2);
  not not_312 (not_312_out, OP1);
  not not_313 (not_313_out, OP0);
  not not_314 (not_314_out, F4);
  not not_315 (not_315_out, F3);
  not not_316 (not_316_out, F2);
  not not_317 (not_317_out, F0);
  not not_318 (not_318_out, OP5);
  not not_319 (not_319_out, OP4);
  not not_320 (not_320_out, OP3);
  not not_321 (not_321_out, OP2);
  not not_322 (not_322_out, OP1);
  not not_323 (not_323_out, OP0);
  not not_324 (not_324_out, F4);
  not not_325 (not_325_out, F3);
  not not_326 (not_326_out, F1);
  not not_327 (not_327_out, F0);
  not not_328 (not_328_out, OP5);
  not not_329 (not_329_out, OP4);
  not not_330 (not_330_out, OP3);
  not not_331 (not_331_out, OP2);
  not not_332 (not_332_out, OP1);
  not not_333 (not_333_out, OP0);
  not not_334 (not_334_out, F4);
  not not_335 (not_335_out, F3);
  not not_336 (not_336_out, F1);
  not not_337 (not_337_out, OP5);
  not not_338 (not_338_out, OP4);
  not not_339 (not_339_out, OP3);
  not not_340 (not_340_out, OP2);
  not not_341 (not_341_out, OP1);
  not not_342 (not_342_out, OP0);
  not not_343 (not_343_out, F4);
  not not_344 (not_344_out, F3);
  not not_345 (not_345_out, OP5);
  not not_346 (not_346_out, OP4);
  not not_347 (not_347_out, OP3);
  not not_348 (not_348_out, OP2);
  not not_349 (not_349_out, OP1);
  not not_350 (not_350_out, OP0);
  not not_351 (not_351_out, F4);
  not not_352 (not_352_out, F2);
  not not_353 (not_353_out, F0);
  not not_354 (not_354_out, OP5);
  not not_355 (not_355_out, OP4);
  not not_356 (not_356_out, OP3);
  not not_357 (not_357_out, OP2);
  not not_358 (not_358_out, OP1);
  not not_359 (not_359_out, OP0);
  not not_360 (not_360_out, F4);
  not not_361 (not_361_out, F2);
  not not_362 (not_362_out, OP5);
  not not_363 (not_363_out, OP4);
  not not_364 (not_364_out, OP3);
  not not_365 (not_365_out, OP2);
  not not_366 (not_366_out, OP1);
  not not_367 (not_367_out, OP0);
  not not_368 (not_368_out, F5);
  not not_369 (not_369_out, F4);
  not not_370 (not_370_out, F3);
  not not_371 (not_371_out, F0);
  not not_372 (not_372_out, OP5);
  not not_373 (not_373_out, OP4);
  not not_374 (not_374_out, OP3);
  not not_375 (not_375_out, OP2);
  not not_376 (not_376_out, OP1);
  not not_377 (not_377_out, OP0);
  not not_378 (not_378_out, F5);
  not not_379 (not_379_out, F4);
  not not_380 (not_380_out, F3);
  not not_381 (not_381_out, OP5);
  not not_382 (not_382_out, OP4);
  not not_383 (not_383_out, OP3);
  not not_384 (not_384_out, OP1);
  not not_385 (not_385_out, OP0);
  not not_386 (not_386_out, OP5);
  not not_387 (not_387_out, OP4);
  not not_388 (not_388_out, OP3);
  not not_389 (not_389_out, OP1);
  not not_390 (not_390_out, OP5);
  not not_391 (not_391_out, OP4);
  not not_392 (not_392_out, OP3);
  not not_393 (not_393_out, OP2);
  not not_394 (not_394_out, OP1);
  not not_395 (not_395_out, OP0);
  not not_396 (not_396_out, F5);
  not not_397 (not_397_out, F4);
  not not_398 (not_398_out, F2);
  not not_399 (not_399_out, F1);
  not not_400 (not_400_out, F0);
  not not_401 (not_401_out, OP5);
  not not_402 (not_402_out, OP4);
  not not_403 (not_403_out, OP3);
  not not_404 (not_404_out, OP2);
  not not_405 (not_405_out, OP1);
  not not_406 (not_406_out, OP0);
  not not_407 (not_407_out, F5);
  not not_408 (not_408_out, F4);
  not not_409 (not_409_out, F2);
  not not_410 (not_410_out, F1);
  not not_411 (not_411_out, F0);
  not not_412 (not_412_out, OP5);
  not not_413 (not_413_out, OP4);
  not not_414 (not_414_out, OP3);
  not not_415 (not_415_out, OP2);
  not not_416 (not_416_out, OP0);
  not not_417 (not_417_out, OP5);
  not not_418 (not_418_out, OP4);
  not not_419 (not_419_out, OP3);
  not not_420 (not_420_out, OP2);
  not not_421 (not_421_out, OP5);
  not not_422 (not_422_out, OP4);
  not not_423 (not_423_out, OP3);
  not not_424 (not_424_out, OP2);
  and and_1 (and_1_out, OP5, not_1_out, not_2_out, not_3_out, OP1, OP0);
  and and_2 (and_2_out, OP5, not_4_out, not_5_out, OP2, not_6_out, not_7_out);
  and and_3 (MemWrite, OP5, not_8_out, OP3, not_9_out, OP1, OP0);
  and and_4 (and_4_out, not_10_out, not_11_out, OP3, not_12_out, not_13_out, not_14_out);
  and and_5 (and_5_out, not_15_out, not_16_out, OP3, OP2, not_17_out, not_18_out);
  and and_6 (and_6_out, not_19_out, not_20_out, OP3, not_21_out, not_22_out, OP0);
  and and_7 (and_7_out, not_23_out, not_24_out, OP3, not_25_out, OP1, not_26_out);
  and and_8 (and_8_out, not_27_out, not_28_out, OP3, OP2, not_29_out, OP0);
  and and_9 (and_9_out, OP5, not_30_out, not_31_out, not_32_out, OP1, OP0);
  and and_10 (and_10_out, OP5, not_33_out, OP3, not_34_out, OP1, OP0);
  and and_11 (and_11_out, OP5, not_35_out, not_36_out, OP2, not_37_out, not_38_out);
  and and_12 (and_12_out, not_39_out, not_40_out, not_41_out, not_42_out, not_43_out, not_44_out, not_45_out, not_46_out, not_47_out, not_48_out, not_49_out, not_50_out);
  and and_13 (and_13_out, not_51_out, not_52_out, not_53_out, not_54_out, not_55_out, not_56_out, not_57_out, not_58_out, not_59_out, not_60_out, F1, F0);
  and and_14 (and_14_out, not_61_out, not_62_out, not_63_out, not_64_out, not_65_out, not_66_out, not_67_out, not_68_out, not_69_out, not_70_out, F1, not_71_out);
  and and_15 (and_15_out, not_72_out, not_73_out, not_74_out, not_75_out, not_76_out, not_77_out, F5, not_78_out, not_79_out, not_80_out, not_81_out, not_82_out);
  and and_16 (and_16_out, not_83_out, not_84_out, not_85_out, not_86_out, not_87_out, not_88_out, F5, not_89_out, not_90_out, not_91_out, not_92_out, F0);
  and and_17 (and_17_out, not_93_out, not_94_out, not_95_out, not_96_out, not_97_out, not_98_out, F5, not_99_out, not_100_out, not_101_out, F1, not_102_out);
  and and_18 (and_18_out, not_103_out, not_104_out, not_105_out, not_106_out, not_107_out, not_108_out, F5, not_109_out, not_110_out, F2, not_111_out, not_112_out);
  and and_19 (and_19_out, not_113_out, not_114_out, not_115_out, not_116_out, not_117_out, not_118_out, F5, not_119_out, not_120_out, F2, not_121_out, F0);
  and and_20 (and_20_out, not_122_out, not_123_out, not_124_out, not_125_out, not_126_out, not_127_out, F5, not_128_out, not_129_out, F2, F1, F0);
  and and_21 (and_21_out, not_130_out, not_131_out, not_132_out, not_133_out, not_134_out, not_135_out, F5, not_136_out, F3, not_137_out, F1, not_138_out);
  and and_22 (and_22_out, not_139_out, not_140_out, not_141_out, not_142_out, not_143_out, not_144_out, F5, not_145_out, F3, not_146_out, F1, F0);
  and and_23 (and_23_out, not_147_out, not_148_out, not_149_out, not_150_out, OP1, OP0);
  and and_24 (and_24_out, not_151_out, not_152_out, OP3, not_153_out, not_154_out, not_155_out);
  and and_25 (and_25_out, not_156_out, not_157_out, OP3, OP2, not_158_out, not_159_out);
  and and_26 (and_26_out, not_160_out, not_161_out, OP3, not_162_out, not_163_out, OP0);
  and and_27 (and_27_out, not_164_out, not_165_out, OP3, not_166_out, OP1, not_167_out);
  and and_28 (and_28_out, not_168_out, not_169_out, OP3, OP2, not_170_out, OP0);
  and and_29 (and_29_out, OP5, not_171_out, not_172_out, not_173_out, OP1, OP0);
  and and_30 (and_30_out, not_174_out, not_175_out, not_176_out, not_177_out, not_178_out, not_179_out, not_180_out, not_181_out, not_182_out, F2, F1, not_183_out);
  and and_31 (and_31_out, not_184_out, not_185_out, not_186_out, not_187_out, not_188_out, not_189_out, not_190_out, not_191_out, not_192_out, F2, F1, F0);
  and and_32 (and_32_out, OP5, not_193_out, not_194_out, OP2, not_195_out, not_196_out);
  and and_33 (SysCALL, not_197_out, not_198_out, not_199_out, not_200_out, not_201_out, not_202_out, not_203_out, not_204_out, F3, F2, not_205_out, not_206_out);
  and and_34 (and_34_out, not_207_out, not_208_out, not_209_out, not_210_out, not_211_out, not_212_out, not_213_out, not_214_out, F3, not_215_out, not_216_out, not_217_out);
  and and_35 (and_35_out, not_218_out, not_219_out, not_220_out, OP2, not_221_out, not_222_out);
  and and_36 (and_36_out, not_223_out, not_224_out, not_225_out, OP2, not_226_out, OP0);
  and and_37 (and_37_out, not_227_out, not_228_out, OP3, not_229_out, not_230_out, not_231_out);
  and and_38 (and_38_out, not_232_out, not_233_out, OP3, not_234_out, not_235_out, OP0);
  and and_39 (and_39_out, not_236_out, not_237_out, OP3, not_238_out, OP1, not_239_out);
  and and_40 (and_40_out, OP5, not_240_out, not_241_out, not_242_out, OP1, OP0);
  and and_41 (and_41_out, OP5, not_243_out, OP3, not_244_out, OP1, OP0);
  and and_42 (LBU, OP5, not_245_out, not_246_out, OP2, not_247_out, not_248_out);
  and and_43 (BGEZ, not_249_out, not_250_out, not_251_out, not_252_out, not_253_out, OP0);
  and and_44 (and_44_out, not_254_out, not_255_out, not_256_out, not_257_out, not_258_out, not_259_out, not_260_out, not_261_out, not_262_out, not_263_out, not_264_out, not_265_out);
  and and_45 (and_45_out, not_266_out, not_267_out, not_268_out, not_269_out, not_270_out, not_271_out, not_272_out, not_273_out, not_274_out, not_275_out, F1, F0);
  and and_46 (and_46_out, not_276_out, not_277_out, not_278_out, not_279_out, not_280_out, not_281_out, not_282_out, not_283_out, not_284_out, not_285_out, F1, not_286_out);
  and and_47 (and_47_out, not_287_out, not_288_out, not_289_out, not_290_out, not_291_out, not_292_out, F5, not_293_out, not_294_out, not_295_out, not_296_out, not_297_out);
  and and_48 (and_48_out, not_298_out, not_299_out, not_300_out, not_301_out, not_302_out, not_303_out, F5, not_304_out, not_305_out, not_306_out, not_307_out, F0);
  and and_49 (and_49_out, not_308_out, not_309_out, not_310_out, not_311_out, not_312_out, not_313_out, F5, not_314_out, not_315_out, not_316_out, F1, not_317_out);
  and and_50 (and_50_out, not_318_out, not_319_out, not_320_out, not_321_out, not_322_out, not_323_out, F5, not_324_out, not_325_out, F2, not_326_out, not_327_out);
  and and_51 (and_51_out, not_328_out, not_329_out, not_330_out, not_331_out, not_332_out, not_333_out, F5, not_334_out, not_335_out, F2, not_336_out, F0);
  and and_52 (and_52_out, not_337_out, not_338_out, not_339_out, not_340_out, not_341_out, not_342_out, F5, not_343_out, not_344_out, F2, F1, F0);
  and and_53 (and_53_out, not_345_out, not_346_out, not_347_out, not_348_out, not_349_out, not_350_out, F5, not_351_out, F3, not_352_out, F1, not_353_out);
  and and_54 (and_54_out, not_354_out, not_355_out, not_356_out, not_357_out, not_358_out, not_359_out, F5, not_360_out, F3, not_361_out, F1, F0);
  and and_55 (and_55_out, not_362_out, not_363_out, not_364_out, not_365_out, not_366_out, not_367_out, not_368_out, not_369_out, not_370_out, F2, F1, not_371_out);
  and and_56 (and_56_out, not_372_out, not_373_out, not_374_out, not_375_out, not_376_out, not_377_out, not_378_out, not_379_out, not_380_out, F2, F1, F0);
  and and_57 (BEQ, not_381_out, not_382_out, not_383_out, OP2, not_384_out, not_385_out);
  and and_58 (BNE, not_386_out, not_387_out, not_388_out, OP2, not_389_out, OP0);
  and and_59 (JR, not_390_out, not_391_out, not_392_out, not_393_out, not_394_out, not_395_out, not_396_out, not_397_out, F3, not_398_out, not_399_out, not_400_out);
  and and_60 (and_60_out, not_401_out, not_402_out, not_403_out, not_404_out, not_405_out, not_406_out, not_407_out, not_408_out, F3, not_409_out, not_410_out, not_411_out);
  and and_61 (and_61_out, not_412_out, not_413_out, not_414_out, not_415_out, OP1, not_416_out);
  and and_62 (and_62_out, not_417_out, not_418_out, not_419_out, not_420_out, OP1, OP0);
  and and_63 (JAL, not_421_out, not_422_out, not_423_out, not_424_out, OP1, OP0);
  or or_1 (MemToReg, and_1_out, and_2_out);
  or or_2 (ALU_SRC, and_4_out, and_5_out, and_6_out, and_7_out, and_8_out, and_9_out, and_10_out, and_11_out);
  or or_3 (SignedExt, and_34_out, and_35_out, and_36_out, and_37_out, and_38_out, and_39_out, and_40_out, and_41_out, LBU, BGEZ);
  or or_4 (JMP, and_60_out, and_61_out, and_62_out);
  or or_5 (RegWrite, and_12_out, and_13_out, and_14_out, and_15_out, and_16_out, and_17_out, and_18_out, and_19_out, and_20_out, and_21_out, and_22_out, and_23_out, and_24_out, and_25_out, and_26_out, and_27_out, and_28_out, and_29_out, and_30_out, and_31_out, and_32_out);
  or or_6 (RegDst, and_44_out, and_45_out, and_46_out, and_47_out, and_48_out, and_49_out, and_50_out, and_51_out, and_52_out, and_53_out, and_54_out, and_55_out, and_56_out);
  or or_7 (SV, and_55_out, and_56_out);
endmodule

// ALU
module MIPS_ALU (
  input  [4:0] shamt,
  input  [31:0] X,
  input  [31:0] Y,
  input  [3:0] AluOP,
  output Equal,
  output [31:0] Result,
  output [31:0] Result_2
);

  wire [0:0] comparator_1_lt, comparator_2_lt;
  wire [31:0] adder_1_out, AND_out, divider_1_out, divider_1_rem, multiplier_1_cout, multiplier_1_out,
       NOR_out, OR_out, shifter_1_out, shifter_2_out, shifter_3_out, subtractor_1_out, XOR_out;

  assign AND_out = X & Y;  // AND_Gate AND, 32 bits wide
  assign OR_out = X | Y;  // OR_Gate OR, 32 bits wide
  Shifter #(.width(32)) shifter_1 (.in(Y), .\dist (shamt), .out(shifter_1_out));
  Shifter #(.width(32), .shift("ar")) shifter_2 (.in(Y), .\dist (shamt), .out(shifter_2_out));
  Shifter #(.width(32), .shift("lr")) shifter_3 (.in(Y), .\dist (shamt), .out(shifter_3_out));
  Multiplier #(.width(32)) multiplier_1 (.a(X), .b(Y), .out(multiplier_1_out), .cout(multiplier_1_cout));  // open: cin
  Divider #(.width(32)) divider_1 (.a(X), .b(Y), .out(divider_1_out), .rem(divider_1_rem));  // open: upper
  Adder #(.width(32)) adder_1 (.a(X), .b(Y), .out(adder_1_out));  // open: cin, cout
  Subtractor #(.width(32)) subtractor_1 (.a(X), .b(Y), .out(subtractor_1_out));  // open: bin, bout
  assign XOR_out = X ^ Y;  // XOR_Gate XOR, 32 bits wide
  assign NOR_out = ~(X | Y);  // NOR_Gate NOR, 32 bits wide
  Comparator #(.width(32)) comparator_1 (.a(X), .b(Y), .eq(Equal), .lt(comparator_1_lt[0]));  // open: gt
  Comparator #(.width(32), .mode("unsigned")) comparator_2 (.a(X), .b(Y), .lt(comparator_2_lt[0]));  // open: gt, eq
  Multiplexer #(.select(4), .width(32), .enable("false")) multiplexer_1 (
    .in0(shifter_1_out), .in1(shifter_2_out), .in2(shifter_3_out), .in3(multiplier_1_out),
    .in4(divider_1_out), .in5(adder_1_out), .in6(subtractor_1_out), .in7(AND_out), .in8(OR_out),
    .in9(XOR_out), .in10(NOR_out), .in11({{31{1'b0}}, comparator_1_lt[0]}),
    .in12({{31{1'b0}}, comparator_2_lt[0]}), .in13({32{1'b0}}), .in14({32{1'b0}}), .in15({32{1'b0}}),
    .out(Result), .sel(AluOP));
  Multiplexer #(.select(4), .width(32), .enable("false")) multiplexer_2 (
    .in0({32{1'b0}}), .in1({32{1'b0}}), .in2({32{1'b0}}), .in3(multiplier_1_cout), .in4(divider_1_rem),
    .in5({32{1'b0}}), .in6({32{1'b0}}), .in7({32{1'b0}}), .in8({32{1'b0}}), .in9({32{1'b0}}),
    .in10({32{1'b0}}), .in11({32{1'b0}}), .in12({32{1'b0}}), .in13({32{1'b0}}), .in14({32{1'b0}}),
    .in15({32{1'b0}}), .out(Result_2), .sel(AluOP));

  // Other names for the same wires on the sheet: Result2[31:0] = Result_2; S[3:0] = AluOP

  // Notes on the sheet:
  //   不要改变此引脚区域内容，也不要改变ALU封装形式
  //   输入引脚
  //   输出引脚
endmodule

module MIPS_Regifile (
  input  [31:0] Din,
  input  Clk,
  input  WE,
  input  [4:0] R1_num,
  input  [4:0] W_num,
  input  [4:0] R2_num,
  output [31:0] R1,
  output [31:0] R2
);

  // RegisterFile registerfile_1: pin names not known; wires that end beside it: Din, Clk, WE, W_num, R1_num, R2_num, R1, R2
endmodule

module \理想流水线  (
);

  wire and_1_out, CLK, comparator_1_eq, comparator_2_eq, ex_mem_1_jmp_2, ex_mem_1_lbu_2, ex_mem_1_memtoreg_2,
       ex_mem_1_regwrite_2, ex_mem_1_syscall_2, \ex_mem_1_传输状态out_表明当前传输数据有效 , Go, halt, id_ex_1_alusrc_2,
       id_ex_1_bgez_2, id_ex_1_jmp_2, id_ex_1_lbu_2, id_ex_1_memtoreg_2, id_ex_1_memwrite_2,
       id_ex_1_regwrite_2, id_ex_1_syscall_2, \id_ex_1_传输状态out_表明当前传输数据有效 , \if_id_1_传输状态out_表明当前传输数据有效 ,
       IR1, IR2, IR3, JMP, LBU, mem_wb_1_memtoreg_2, MemWrite, not_1_out, not_2_out, PC_en, RegWrite, RST,
       show, SignedExt, Syscall, W1, W2, W3, WB_Valid, \硬布线控制器_1_alu_src , \硬布线控制器_1_bgez , \硬布线控制器_1_jal ,
       \硬布线控制器_1_jmp , \硬布线控制器_1_lbu , \硬布线控制器_1_memtoreg , \硬布线控制器_1_memwrite , \硬布线控制器_1_regdst ,
       \硬布线控制器_1_regwrite , \硬布线控制器_1_signedext , \硬布线控制器_1_syscall ;
  wire [3:0] id_ex_1_aluop_2, \硬布线控制器_1_alu_op ;
  wire [4:0] ex_mem_1_w_num_2, id_ex_1_shamt_2, id_ex_1_w_num_2, multiplexer_2_out, W_num;
  wire [15:0] id_ex_1_imm16_2, \LoadUse次数 , \总周期数 , \插入气泡数 , \无条件分支数 , \条件分支成功数 ;
  wire [25:0] if_id_1_ir_3;
  wire [31:0] adder_1_out, adder_2_out, adder_3_out, bit_extender_1_out, bit_extender_2_out, Din,
       ex_mem_1_ir_2, ex_mem_1_r1_2, ex_mem_1_r2_2, ex_mem_1_result1_2, EX_PC, id_ex_1_ir_2, id_ex_1_r1_2,
       id_ex_1_r2_2, ID_PC, if_id_1_ir_2, IF_PC, LedData, MEM_PC, mem_wb_1_dout_2, mem_wb_1_result1_2,
       mips_alu_1_result, mips_alu_1_result_2, mips_regifile_1_r1, mips_regifile_1_r2, multiplexer_1_out,
       multiplexer_3_out, multiplexer_4_out, R1, R2, ram_1_data, rom_1_data, shifter_1_out, WB_IR, WB_PC;
  wire [31:26] if_id_1_ir_3_2;

  Button \u_总复位  (.out(RST));
  Button _1 (.out(IR1));
  Button _2 (.out(IR2));
  Button _3 (.out(IR3));
  Button \u_继续运行  (.out(Go));
  LED led_1 (.in(W1));
  LED led_2 (.in(W2));
  LED led_3 (.in(W3));
  Comparator #(.width(32)) comparator_1 (.a(WB_IR), .b({32{1'b0}}), .eq(comparator_1_eq));  // open: gt, lt
  not not_1 (not_1_out, halt);
  Multiplexer #(.width(32), .enable("false")) multiplexer_1 (
    .in0(adder_1_out), .in1(adder_3_out), .out(multiplexer_1_out), .sel(JMP));
  Hex_Digit_Display hex_digit_display_1 (.value(LedData[31:28]));  // open: dp
  and and_1 (and_1_out, comparator_1_eq, WB_Valid, not_1_out);
  Counter #(.width(16), .max('hffff)) counter_1 (
    .count(not_1_out), .Q(\总周期数 ), .clk(CLK), .clr(RST));  // open: load, D, carry
  or or_1 (PC_en, not_1_out, Go);
  Register #(.width(32)) PC (.D(multiplexer_1_out), .en(PC_en), .Q(IF_PC), .clk(CLK), .clr(RST));
  Hex_Digit_Display hex_digit_display_2 (.value(LedData[23:20]));  // open: dp
  Hex_Digit_Display hex_digit_display_3 (.value(LedData[27:24]));  // open: dp
  Counter #(.width(16), .max('hffff)) counter_2 (
    .count(and_1_out), .Q(\插入气泡数 ), .clk(CLK), .clr(RST));  // open: load, D, carry
  Hex_Digit_Display hex_digit_display_4 (.value(LedData[15:12]));  // open: dp
  Hex_Digit_Display hex_digit_display_5 (.value(LedData[19:16]));  // open: dp
  Adder #(.width(32)) adder_1 (.a(IF_PC), .b(32'h4), .out(adder_1_out));  // open: cin, cout
  Hex_Digit_Display hex_digit_display_6 (.value(LedData[7:4]));  // open: dp
  Hex_Digit_Display hex_digit_display_7 (.value(LedData[11:8]));  // open: dp
  Clock clock_1 (.out(CLK));
  ROM #(.addrWidth(10), .dataWidth(32)) rom_1 (.addr(IF_PC[11:2]), .data(rom_1_data));  // open: sel
  Hex_Digit_Display hex_digit_display_8 (.value(LedData[3:0]));  // open: dp
  IF_ID if_id_1 (
    .CLK(CLK), .reset(RST), .en(halt), .PC(IF_PC), .IR(rom_1_data), .PC_2(ID_PC), .IR_2(if_id_1_ir_2),
    .IR_3({if_id_1_ir_3_2, if_id_1_ir_3}), .\传输状态In_表明当前传输数据有效 (1'b1),
    .\传输状态Out_表明当前传输数据有效 (\if_id_1_传输状态out_表明当前传输数据有效 ));
  // Probe on \总周期数 
  // Probe on \无条件分支数 
  // Probe on \条件分支成功数 
  // Probe on \插入气泡数 
  // Probe on \LoadUse次数 
  // Probe on if_id_1_ir_2
  // Probe on IF_PC[11:0]
  \硬布线控制器  \u_硬布线控制器_1  (
    .Func(if_id_1_ir_3[5:0]), .OP(if_id_1_ir_3_2), .ALU_OP(\硬布线控制器_1_alu_op ),
    .MemToReg(\硬布线控制器_1_memtoreg ), .MemWrite(\硬布线控制器_1_memwrite ), .ALU_SRC(\硬布线控制器_1_alu_src ),
    .RegWrite(\硬布线控制器_1_regwrite ), .SysCALL(\硬布线控制器_1_syscall ), .SignedExt(\硬布线控制器_1_signedext ),
    .RegDst(\硬布线控制器_1_regdst ), .JMP(\硬布线控制器_1_jmp ), .JAL(\硬布线控制器_1_jal ), .BGEZ(\硬布线控制器_1_bgez ),
    .LBU(\硬布线控制器_1_lbu ));  // open: JR, Beq, Bne, SV
  // Probe on ID_PC[11:0]
  Multiplexer #(.width(5), .enable("false")) multiplexer_2 (
    .in0(if_id_1_ir_3[20:16]), .in1(if_id_1_ir_3[15:11]), .out(multiplexer_2_out), .sel(\硬布线控制器_1_regdst ));
  // Probe on MEM_PC[11:0]
  // Probe on EX_PC[11:0]
  // Probe on WB_PC[11:0]
  MIPS_Regifile mips_regifile_1 (
    .Din(Din), .Clk(CLK), .R1(mips_regifile_1_r1), .R2(mips_regifile_1_r2), .WE(RegWrite), .W_num(W_num),
    .R1_num(if_id_1_ir_3[25:21]), .R2_num(if_id_1_ir_3[20:16]));
  Comparator #(.width(32)) comparator_2 (.a(R1), .b(32'h22), .eq(comparator_2_eq));  // open: gt, lt
  ID_EX id_ex_1 (
    .CLK(CLK), .reset(RST), .en(halt), .PC(ID_PC), .R1(mips_regifile_1_r1), .IR(if_id_1_ir_2),
    .R2(mips_regifile_1_r2), .SignedExt(\硬布线控制器_1_signedext ), .shamt(if_id_1_ir_3[10:6]),
    .imm16(if_id_1_ir_3[15:0]), .JMP(\硬布线控制器_1_jmp ), .LBU(\硬布线控制器_1_lbu ), .BGEZ(\硬布线控制器_1_bgez ),
    .MemToReg(\硬布线控制器_1_memtoreg ), .MemWrite(\硬布线控制器_1_memwrite ), .AluOP(\硬布线控制器_1_alu_op ),
    .AluSrc(\硬布线控制器_1_alu_src ), .RegWrite(\硬布线控制器_1_regwrite ), .JAL(\硬布线控制器_1_jal ),
    .RegDst(\硬布线控制器_1_regdst ), .Syscall(\硬布线控制器_1_syscall ), .PC_2(EX_PC), .R1_2(id_ex_1_r1_2),
    .IR_2(id_ex_1_ir_2), .R2_2(id_ex_1_r2_2), .SignedExt_2(SignedExt), .shamt_2(id_ex_1_shamt_2),
    .imm16_2(id_ex_1_imm16_2), .JMP_2(id_ex_1_jmp_2), .LBU_2(id_ex_1_lbu_2), .BGEZ_2(id_ex_1_bgez_2),
    .MemToReg_2(id_ex_1_memtoreg_2), .MemWrite_2(id_ex_1_memwrite_2), .AluOP_2(id_ex_1_aluop_2),
    .AluSrc_2(id_ex_1_alusrc_2), .RegWrite_2(id_ex_1_regwrite_2), .Syscall_2(id_ex_1_syscall_2),
    .imm26(if_id_1_ir_3), .W_num(multiplexer_2_out), .W_num_2(id_ex_1_w_num_2),
    .\传输状态In_表明当前传输数据有效 (\if_id_1_传输状态out_表明当前传输数据有效 ), .\传输状态Out_表明当前传输数据有效 (\id_ex_1_传输状态out_表明当前传输数据有效 ));  // open: JR, SV, BEQ, BNE, JR_2, SV_2, BEQ_2, BNE_2, JAL_2, RegDst_2, imm26_2, ID_R1_num, ID_R1_num_2, ID_R2_num, ID_R2_num_2
  and and_2 (show, comparator_2_eq, Syscall);
  and and_3 (halt, Syscall, not_2_out);
  not not_2 (not_2_out, comparator_2_eq);
  assign bit_extender_1_out = {{16{id_ex_1_imm16_2[15]}}, id_ex_1_imm16_2};  // Bit_Extender bit_extender_1
  assign bit_extender_2_out = {{16{1'b0}}, id_ex_1_imm16_2};  // Bit_Extender bit_extender_2
  // Probe on id_ex_1_ir_2
  Multiplexer #(.width(32), .enable("false")) multiplexer_3 (
    .in0(bit_extender_2_out), .in1(bit_extender_1_out), .out(multiplexer_3_out), .sel(SignedExt));
  Multiplexer #(.width(32), .enable("false")) multiplexer_4 (
    .in0(id_ex_1_r2_2), .in1(multiplexer_3_out), .out(multiplexer_4_out), .sel(id_ex_1_alusrc_2));
  Shifter #(.width(32)) shifter_1 (.in(multiplexer_3_out), .\dist (5'b00010), .out(shifter_1_out));
  Adder #(.width(32)) adder_2 (.a(EX_PC), .b(32'h4), .out(adder_2_out));  // open: cin, cout
  MIPS_ALU mips_alu_1 (
    .X(id_ex_1_r1_2), .Y(multiplexer_4_out), .AluOP(id_ex_1_aluop_2), .Result(mips_alu_1_result),
    .Result_2(mips_alu_1_result_2), .shamt(id_ex_1_shamt_2));  // open: Equal
  Adder #(.width(32)) adder_3 (.a(shifter_1_out), .b(adder_2_out), .out(adder_3_out));  // open: cin, cout
  EX_MEM ex_mem_1 (
    .CLK(CLK), .reset(RST), .en(halt), .PC(EX_PC), .Result1(mips_alu_1_result), .IR(id_ex_1_ir_2),
    .R2(id_ex_1_r2_2), .JMP(id_ex_1_jmp_2), .LBU(id_ex_1_lbu_2), .BGEZ(id_ex_1_bgez_2),
    .MemToReg(id_ex_1_memtoreg_2), .MemWrite(id_ex_1_memwrite_2), .AluOP(id_ex_1_aluop_2),
    .AluSrc(id_ex_1_alusrc_2), .RegWrite(id_ex_1_regwrite_2), .Syscall(id_ex_1_syscall_2), .PC_2(MEM_PC),
    .Result1_2(ex_mem_1_result1_2), .IR_2(ex_mem_1_ir_2), .R2_2(ex_mem_1_r2_2), .JMP_2(ex_mem_1_jmp_2),
    .LBU_2(ex_mem_1_lbu_2), .MemToReg_2(ex_mem_1_memtoreg_2), .MemWrite_2(MemWrite),
    .RegWrite_2(ex_mem_1_regwrite_2), .Syscall_2(ex_mem_1_syscall_2), .Result2(mips_alu_1_result_2),
    .R1(id_ex_1_r1_2), .R1_2(ex_mem_1_r1_2), .W_num(id_ex_1_w_num_2), .W_num_2(ex_mem_1_w_num_2),
    .\传输状态In_表明当前传输数据有效 (\id_ex_1_传输状态out_表明当前传输数据有效 ), .\传输状态Out_表明当前传输数据有效 (\ex_mem_1_传输状态out_表明当前传输数据有效 ));  // open: SignedExt, JR, SV, BEQ, BNE, JAL, RegDst, SignedExt_2, JR_2, SV_2, BGEZ_2, BEQ_2, BNE_2, AluOP_2, AluSrc_2, JAL_2, RegDst_2, Result2_2, EPC, EPC_2
  // Probe on ex_mem_1_ir_2
  RAM #(.addrWidth(10), .dataWidth(32), .bus("separate")) ram_1 (
    .addr(ex_mem_1_result1_2[11:2]), .din(ex_mem_1_r2_2), .data(ram_1_data), .str(MemWrite), .clk(CLK),
    .clr(RST));  // open: sel, ld
  MEM_WB mem_wb_1 (
    .CLK(CLK), .reset(RST), .en(halt), .PC(MEM_PC), .Result1(ex_mem_1_result1_2), .IR(ex_mem_1_ir_2),
    .Dout(ram_1_data), .JMP(ex_mem_1_jmp_2), .LBU(ex_mem_1_lbu_2), .MemToReg(ex_mem_1_memtoreg_2),
    .RegWrite(ex_mem_1_regwrite_2), .Syscall(ex_mem_1_syscall_2), .PC_2(WB_PC),
    .Result1_2(mem_wb_1_result1_2), .IR_2(WB_IR), .Dout_2(mem_wb_1_dout_2), .JMP_2(JMP), .LBU_2(LBU),
    .MemToReg_2(mem_wb_1_memtoreg_2), .RegWrite_2(RegWrite), .Syscall_2(Syscall), .R1(ex_mem_1_r1_2),
    .R1_2(R1), .R2(ex_mem_1_r2_2), .R2_2(R2), .W_num(ex_mem_1_w_num_2), .W_num_2(W_num),
    .\传输状态In_表明当前传输数据有效 (\ex_mem_1_传输状态out_表明当前传输数据有效 ), .\传输状态Out_表明当前传输数据有效 (WB_Valid));  // open: SignedExt, JR, SV, BGEZ, BEQ, BNE, MemWrite, AluOP, AluSrc, JAL, RegDst, SignedExt_2, JR_2, SV_2, BGEZ_2, BEQ_2, BNE_2, MemWrite_2, AluOP_2, AluSrc_2, JAL_2, RegDst_2, EPC, EPC_2
  // Probe on WB_IR
  Multiplexer #(.width(32), .enable("false")) multiplexer_5 (
    .in0(mem_wb_1_result1_2), .in1(mem_wb_1_dout_2), .out(Din), .sel(mem_wb_1_memtoreg_2));
  // Probe on Din

  // Notes on the sheet:
  //   中断源
  //   中断等待指示
  //   数码管输出
  //   指令存储器
  //   contents of rom_1 (hex, n*v repeats v):
  //   20100000 20110001 20120002 20130003 36100000 36310001 36520002 36730003 ae100000 ae110004 ae120008
  //   ae13000c 2002000a 0 0 0 c
  //   OP
  //   rs
  //   指令字
  //   rt
  //   rd
  //   shamt
  //   imm16
  //   JMP
  //   JR
  //   Func
  //   imm26
  //   Beq
  //   Bne
  //   OP
  //   JAL
  //   Func
  //   Syscall
  //   MemToReg
  //   MemWrite
  //   AluOP
  //   AluSrcB
  //   RegWrite
  //   RegDst
  //   流水调试日志用
endmodule

// 源寄存器使用情况
module \源寄存器使用情况  (
  input  OP0,
  input  OP1,
  input  OP2,
  input  OP3,
  input  OP4,
  input  OP5,
  input  F0,
  input  F1,
  input  F2,
  input  F3,
  input  F4,
  input  F5,
  output R1_Used,
  output R2_Used
);

  wire and_1_out, and_2_out, and_3_out, and_4_out, and_5_out, and_6_out, and_7_out, and_8_out, and_9_out,
       and_10_out, and_11_out, and_12_out, and_13_out, and_14_out, and_15_out, and_16_out, and_17_out,
       and_18_out, and_19_out, and_20_out, and_21_out, and_22_out, and_23_out, and_24_out, and_25_out,
       and_26_out, and_27_out, and_28_out, and_29_out, and_30_out, and_31_out, and_32_out, and_33_out,
       and_34_out, and_35_out, and_36_out, and_37_out, and_38_out, and_39_out, and_40_out, and_41_out,
       not_1_out, not_2_out, not_3_out, not_4_out, not_5_out, not_6_out, not_7_out, not_8_out, not_9_out,
       not_10_out, not_11_out, not_12_out, not_13_out, not_14_out, not_15_out, not_16_out, not_17_out,
       not_18_out, not_19_out, not_20_out, not_21_out, not_22_out, not_23_out, not_24_out, not_25_out,
       not_26_out, not_27_out, not_28_out, not_29_out, not_30_out, not_31_out, not_32_out, not_33_out,
       not_34_out, not_35_out, not_36_out, not_37_out, not_38_out, not_39_out, not_40_out, not_41_out,
       not_42_out, not_43_out, not_44_out, not_45_out, not_46_out, not_47_out, not_48_out, not_49_out,
       not_50_out, not_51_out, not_52_out, not_53_out, not_54_out, not_55_out, not_56_out, not_57_out,
       not_58_out, not_59_out, not_60_out, not_61_out, not_62_out, not_63_out, not_64_out, not_65_out,
       not_66_out, not_67_out, not_68_out, not_69_out, not_70_out, not_71_out, not_72_out, not_73_out,
       not_74_out, not_75_out, not_76_out, not_77_out, not_78_out, not_79_out, not_80_out, not_81_out,
       not_82_out, not_83_out, not_84_out, not_85_out, not_86_out, not_87_out, not_88_out, not_89_out,
       not_90_out, not_91_out, not_92_out, not_93_out, not_94_out, not_95_out, not_96_out, not_97_out,
       not_98_out, not_99_out, not_100_out, not_101_out, not_102_out, not_103_out, not_104_out, not_105_out,
       not_106_out, not_107_out, not_108_out, not_109_out, not_110_out, not_111_out, not_112_out,
       not_113_out, not_114_out, not_115_out, not_116_out, not_117_out, not_118_out, not_119_out,
       not_120_out, not_121_out, not_122_out, not_123_out, not_124_out, not_125_out, not_126_out,
       not_127_out, not_128_out, not_129_out, not_130_out, not_131_out, not_132_out, not_133_out,
       not_134_out, not_135_out, not_136_out, not_137_out, not_138_out, not_139_out, not_140_out,
       not_141_out, not_142_out, not_143_out, not_144_out, not_145_out, not_146_out, not_147_out,
       not_148_out, not_149_out, not_150_out, not_151_out, not_152_out, not_153_out, not_154_out,
       not_155_out, not_156_out, not_157_out, not_158_out, not_159_out, not_160_out, not_161_out,
       not_162_out, not_163_out, not_164_out, not_165_out, not_166_out, not_167_out, not_168_out,
       not_169_out, not_170_out, not_171_out, not_172_out, not_173_out, not_174_out, not_175_out,
       not_176_out, not_177_out, not_178_out, not_179_out, not_180_out, not_181_out, not_182_out,
       not_183_out, not_184_out, not_185_out, not_186_out, not_187_out, not_188_out, not_189_out,
       not_190_out, not_191_out, not_192_out, not_193_out, not_194_out, not_195_out, not_196_out,
       not_197_out, not_198_out, not_199_out, not_200_out, not_201_out, not_202_out, not_203_out,
       not_204_out, not_205_out, not_206_out, not_207_out, not_208_out, not_209_out, not_210_out,
       not_211_out, not_212_out, not_213_out, not_214_out, not_215_out, not_216_out, not_217_out,
       not_218_out, not_219_out, not_220_out, not_221_out, not_222_out, not_223_out, not_224_out,
       not_225_out, not_226_out, not_227_out, not_228_out, not_229_out, not_230_out, not_231_out,
       not_232_out, not_233_out, not_234_out, not_235_out, not_236_out, not_237_out, not_238_out,
       not_239_out, not_240_out, not_241_out, not_242_out, not_243_out, not_244_out, not_245_out,
       not_246_out, not_247_out, not_248_out, not_249_out, not_250_out, not_251_out, not_252_out,
       not_253_out, not_254_out, not_255_out, not_256_out, not_257_out, not_258_out, not_259_out,
       not_260_out, not_261_out, not_262_out, not_263_out, not_264_out, not_265_out, not_266_out,
       not_267_out, not_268_out, not_269_out, not_270_out, not_271_out, not_272_out, not_273_out,
       not_274_out, not_275_out, not_276_out, not_277_out, not_278_out, not_279_out, not_280_out,
       not_281_out, not_282_out, not_283_out, not_284_out, not_285_out, not_286_out, not_287_out,
       not_288_out, not_289_out, not_290_out, not_291_out, not_292_out, not_293_out, not_294_out,
       not_295_out, not_296_out, not_297_out, not_298_out, not_299_out, not_300_out, not_301_out,
       not_302_out, not_303_out, not_304_out, not_305_out, not_306_out, not_307_out, not_308_out,
       not_309_out, not_310_out, not_311_out, not_312_out, not_313_out, not_314_out, not_315_out,
       not_316_out, not_317_out;

  not not_1 (not_1_out, OP5);
  not not_2 (not_2_out, OP4);
  not not_3 (not_3_out, OP3);
  not not_4 (not_4_out, OP2);
  not not_5 (not_5_out, OP1);
  not not_6 (not_6_out, OP0);
  not not_7 (not_7_out, F4);
  not not_8 (not_8_out, F3);
  not not_9 (not_9_out, F2);
  not not_10 (not_10_out, F1);
  not not_11 (not_11_out, F0);
  not not_12 (not_12_out, OP5);
  not not_13 (not_13_out, OP4);
  not not_14 (not_14_out, OP3);
  not not_15 (not_15_out, OP2);
  not not_16 (not_16_out, OP1);
  not not_17 (not_17_out, OP0);
  not not_18 (not_18_out, F4);
  not not_19 (not_19_out, F3);
  not not_20 (not_20_out, F2);
  not not_21 (not_21_out, F1);
  not not_22 (not_22_out, OP5);
  not not_23 (not_23_out, OP4);
  not not_24 (not_24_out, OP3);
  not not_25 (not_25_out, OP2);
  not not_26 (not_26_out, OP1);
  not not_27 (not_27_out, OP0);
  not not_28 (not_28_out, F4);
  not not_29 (not_29_out, F3);
  not not_30 (not_30_out, F2);
  not not_31 (not_31_out, F0);
  not not_32 (not_32_out, OP5);
  not not_33 (not_33_out, OP4);
  not not_34 (not_34_out, OP3);
  not not_35 (not_35_out, OP2);
  not not_36 (not_36_out, OP1);
  not not_37 (not_37_out, OP0);
  not not_38 (not_38_out, F4);
  not not_39 (not_39_out, F3);
  not not_40 (not_40_out, F1);
  not not_41 (not_41_out, F0);
  not not_42 (not_42_out, OP5);
  not not_43 (not_43_out, OP4);
  not not_44 (not_44_out, OP3);
  not not_45 (not_45_out, OP2);
  not not_46 (not_46_out, OP1);
  not not_47 (not_47_out, OP0);
  not not_48 (not_48_out, F4);
  not not_49 (not_49_out, F3);
  not not_50 (not_50_out, F1);
  not not_51 (not_51_out, OP5);
  not not_52 (not_52_out, OP4);
  not not_53 (not_53_out, OP3);
  not not_54 (not_54_out, OP2);
  not not_55 (not_55_out, OP1);
  not not_56 (not_56_out, OP0);
  not not_57 (not_57_out, F4);
  not not_58 (not_58_out, F3);
  not not_59 (not_59_out, OP5);
  not not_60 (not_60_out, OP4);
  not not_61 (not_61_out, OP3);
  not not_62 (not_62_out, OP2);
  not not_63 (not_63_out, OP1);
  not not_64 (not_64_out, OP0);
  not not_65 (not_65_out, F4);
  not not_66 (not_66_out, F2);
  not not_67 (not_67_out, F0);
  not not_68 (not_68_out, OP5);
  not not_69 (not_69_out, OP4);
  not not_70 (not_70_out, OP3);
  not not_71 (not_71_out, OP2);
  not not_72 (not_72_out, OP1);
  not not_73 (not_73_out, OP0);
  not not_74 (not_74_out, F4);
  not not_75 (not_75_out, F2);
  not not_76 (not_76_out, OP5);
  not not_77 (not_77_out, OP4);
  not not_78 (not_78_out, OP3);
  not not_79 (not_79_out, OP2);
  not not_80 (not_80_out, OP1);
  not not_81 (not_81_out, OP0);
  not not_82 (not_82_out, F5);
  not not_83 (not_83_out, F4);
  not not_84 (not_84_out, F2);
  not not_85 (not_85_out, F1);
  not not_86 (not_86_out, F0);
  not not_87 (not_87_out, OP5);
  not not_88 (not_88_out, OP4);
  not not_89 (not_89_out, OP3);
  not not_90 (not_90_out, OP2);
  not not_91 (not_91_out, OP1);
  not not_92 (not_92_out, OP0);
  not not_93 (not_93_out, F5);
  not not_94 (not_94_out, F4);
  not not_95 (not_95_out, F1);
  not not_96 (not_96_out, F0);
  not not_97 (not_97_out, OP5);
  not not_98 (not_98_out, OP4);
  not not_99 (not_99_out, OP3);
  not not_100 (not_100_out, OP1);
  not not_101 (not_101_out, OP0);
  not not_102 (not_102_out, OP5);
  not not_103 (not_103_out, OP4);
  not not_104 (not_104_out, OP3);
  not not_105 (not_105_out, OP1);
  not not_106 (not_106_out, OP5);
  not not_107 (not_107_out, OP4);
  not not_108 (not_108_out, OP2);
  not not_109 (not_109_out, OP1);
  not not_110 (not_110_out, OP0);
  not not_111 (not_111_out, OP5);
  not not_112 (not_112_out, OP4);
  not not_113 (not_113_out, OP1);
  not not_114 (not_114_out, OP0);
  not not_115 (not_115_out, OP5);
  not not_116 (not_116_out, OP4);
  not not_117 (not_117_out, OP2);
  not not_118 (not_118_out, OP1);
  not not_119 (not_119_out, OP5);
  not not_120 (not_120_out, OP4);
  not not_121 (not_121_out, OP2);
  not not_122 (not_122_out, OP0);
  not not_123 (not_123_out, OP5);
  not not_124 (not_124_out, OP4);
  not not_125 (not_125_out, OP1);
  not not_126 (not_126_out, OP4);
  not not_127 (not_127_out, OP3);
  not not_128 (not_128_out, OP2);
  not not_129 (not_129_out, OP4);
  not not_130 (not_130_out, OP2);
  not not_131 (not_131_out, OP5);
  not not_132 (not_132_out, OP4);
  not not_133 (not_133_out, OP3);
  not not_134 (not_134_out, OP2);
  not not_135 (not_135_out, OP1);
  not not_136 (not_136_out, OP0);
  not not_137 (not_137_out, F5);
  not not_138 (not_138_out, F4);
  not not_139 (not_139_out, F3);
  not not_140 (not_140_out, F0);
  not not_141 (not_141_out, OP5);
  not not_142 (not_142_out, OP4);
  not not_143 (not_143_out, OP3);
  not not_144 (not_144_out, OP2);
  not not_145 (not_145_out, OP1);
  not not_146 (not_146_out, OP0);
  not not_147 (not_147_out, F5);
  not not_148 (not_148_out, F4);
  not not_149 (not_149_out, F3);
  not not_150 (not_150_out, OP4);
  not not_151 (not_151_out, OP3);
  not not_152 (not_152_out, OP1);
  not not_153 (not_153_out, OP0);
  not not_154 (not_154_out, OP5);
  not not_155 (not_155_out, OP4);
  not not_156 (not_156_out, OP3);
  not not_157 (not_157_out, OP2);
  not not_158 (not_158_out, OP1);
  not not_159 (not_159_out, OP5);
  not not_160 (not_160_out, OP4);
  not not_161 (not_161_out, OP3);
  not not_162 (not_162_out, OP2);
  not not_163 (not_163_out, OP1);
  not not_164 (not_164_out, OP0);
  not not_165 (not_165_out, F5);
  not not_166 (not_166_out, F4);
  not not_167 (not_167_out, F3);
  not not_168 (not_168_out, F2);
  not not_169 (not_169_out, F1);
  not not_170 (not_170_out, F0);
  not not_171 (not_171_out, OP5);
  not not_172 (not_172_out, OP4);
  not not_173 (not_173_out, OP3);
  not not_174 (not_174_out, OP2);
  not not_175 (not_175_out, OP1);
  not not_176 (not_176_out, OP0);
  not not_177 (not_177_out, F5);
  not not_178 (not_178_out, F4);
  not not_179 (not_179_out, F3);
  not not_180 (not_180_out, F2);
  not not_181 (not_181_out, OP5);
  not not_182 (not_182_out, OP4);
  not not_183 (not_183_out, OP3);
  not not_184 (not_184_out, OP2);
  not not_185 (not_185_out, OP1);
  not not_186 (not_186_out, OP0);
  not not_187 (not_187_out, F5);
  not not_188 (not_188_out, F4);
  not not_189 (not_189_out, F3);
  not not_190 (not_190_out, F2);
  not not_191 (not_191_out, F0);
  not not_192 (not_192_out, OP5);
  not not_193 (not_193_out, OP4);
  not not_194 (not_194_out, OP3);
  not not_195 (not_195_out, OP2);
  not not_196 (not_196_out, OP1);
  not not_197 (not_197_out, OP0);
  not not_198 (not_198_out, F4);
  not not_199 (not_199_out, F3);
  not not_200 (not_200_out, F2);
  not not_201 (not_201_out, F1);
  not not_202 (not_202_out, F0);
  not not_203 (not_203_out, OP5);
  not not_204 (not_204_out, OP4);
  not not_205 (not_205_out, OP3);
  not not_206 (not_206_out, OP2);
  not not_207 (not_207_out, OP1);
  not not_208 (not_208_out, OP0);
  not not_209 (not_209_out, F4);
  not not_210 (not_210_out, F3);
  not not_211 (not_211_out, F2);
  not not_212 (not_212_out, F1);
  not not_213 (not_213_out, OP5);
  not not_214 (not_214_out, OP4);
  not not_215 (not_215_out, OP3);
  not not_216 (not_216_out, OP2);
  not not_217 (not_217_out, OP1);
  not not_218 (not_218_out, OP0);
  not not_219 (not_219_out, F4);
  not not_220 (not_220_out, F3);
  not not_221 (not_221_out, F2);
  not not_222 (not_222_out, F0);
  not not_223 (not_223_out, OP5);
  not not_224 (not_224_out, OP4);
  not not_225 (not_225_out, OP3);
  not not_226 (not_226_out, OP2);
  not not_227 (not_227_out, OP1);
  not not_228 (not_228_out, OP0);
  not not_229 (not_229_out, F4);
  not not_230 (not_230_out, F3);
  not not_231 (not_231_out, F1);
  not not_232 (not_232_out, F0);
  not not_233 (not_233_out, OP5);
  not not_234 (not_234_out, OP4);
  not not_235 (not_235_out, OP3);
  not not_236 (not_236_out, OP2);
  not not_237 (not_237_out, OP1);
  not not_238 (not_238_out, OP0);
  not not_239 (not_239_out, F4);
  not not_240 (not_240_out, F3);
  not not_241 (not_241_out, F1);
  not not_242 (not_242_out, OP5);
  not not_243 (not_243_out, OP4);
  not not_244 (not_244_out, OP3);
  not not_245 (not_245_out, OP2);
  not not_246 (not_246_out, OP1);
  not not_247 (not_247_out, OP0);
  not not_248 (not_248_out, F4);
  not not_249 (not_249_out, F3);
  not not_250 (not_250_out, OP5);
  not not_251 (not_251_out, OP4);
  not not_252 (not_252_out, OP3);
  not not_253 (not_253_out, OP2);
  not not_254 (not_254_out, OP1);
  not not_255 (not_255_out, OP0);
  not not_256 (not_256_out, F4);
  not not_257 (not_257_out, F2);
  not not_258 (not_258_out, F0);
  not not_259 (not_259_out, OP5);
  not not_260 (not_260_out, OP4);
  not not_261 (not_261_out, OP3);
  not not_262 (not_262_out, OP2);
  not not_263 (not_263_out, OP1);
  not not_264 (not_264_out, OP0);
  not not_265 (not_265_out, F4);
  not not_266 (not_266_out, F2);
  not not_267 (not_267_out, OP5);
  not not_268 (not_268_out, OP4);
  not not_269 (not_269_out, OP3);
  not not_270 (not_270_out, OP2);
  not not_271 (not_271_out, OP1);
  not not_272 (not_272_out, OP0);
  not not_273 (not_273_out, F5);
  not not_274 (not_274_out, F4);
  not not_275 (not_275_out, F1);
  not not_276 (not_276_out, F0);
  not not_277 (not_277_out, OP5);
  not not_278 (not_278_out, OP4);
  not not_279 (not_279_out, OP3);
  not not_280 (not_280_out, OP1);
  not not_281 (not_281_out, OP0);
  not not_282 (not_282_out, OP5);
  not not_283 (not_283_out, OP4);
  not not_284 (not_284_out, OP3);
  not not_285 (not_285_out, OP1);
  not not_286 (not_286_out, OP4);
  not not_287 (not_287_out, OP2);
  not not_288 (not_288_out, OP5);
  not not_289 (not_289_out, OP4);
  not not_290 (not_290_out, OP3);
  not not_291 (not_291_out, OP2);
  not not_292 (not_292_out, OP1);
  not not_293 (not_293_out, OP0);
  not not_294 (not_294_out, F5);
  not not_295 (not_295_out, F4);
  not not_296 (not_296_out, F3);
  not not_297 (not_297_out, F0);
  not not_298 (not_298_out, OP5);
  not not_299 (not_299_out, OP4);
  not not_300 (not_300_out, OP3);
  not not_301 (not_301_out, OP2);
  not not_302 (not_302_out, OP1);
  not not_303 (not_303_out, OP0);
  not not_304 (not_304_out, F5);
  not not_305 (not_305_out, F4);
  not not_306 (not_306_out, F3);
  not not_307 (not_307_out, OP5);
  not not_308 (not_308_out, OP3);
  not not_309 (not_309_out, OP2);
  not not_310 (not_310_out, OP1);
  not not_311 (not_311_out, OP0);
  not not_312 (not_312_out, F5);
  not not_313 (not_313_out, F4);
  not not_314 (not_314_out, F3);
  not not_315 (not_315_out, F2);
  not not_316 (not_316_out, F1);
  not not_317 (not_317_out, F0);
  and and_1 (and_1_out, not_1_out, not_2_out, not_3_out, not_4_out, not_5_out, not_6_out, F5, not_7_out, not_8_out, not_9_out, not_10_out, not_11_out);
  and and_2 (and_2_out, not_12_out, not_13_out, not_14_out, not_15_out, not_16_out, not_17_out, F5, not_18_out, not_19_out, not_20_out, not_21_out, F0);
  and and_3 (and_3_out, not_22_out, not_23_out, not_24_out, not_25_out, not_26_out, not_27_out, F5, not_28_out, not_29_out, not_30_out, F1, not_31_out);
  and and_4 (and_4_out, not_32_out, not_33_out, not_34_out, not_35_out, not_36_out, not_37_out, F5, not_38_out, not_39_out, F2, not_40_out, not_41_out);
  and and_5 (and_5_out, not_42_out, not_43_out, not_44_out, not_45_out, not_46_out, not_47_out, F5, not_48_out, not_49_out, F2, not_50_out, F0);
  and and_6 (and_6_out, not_51_out, not_52_out, not_53_out, not_54_out, not_55_out, not_56_out, F5, not_57_out, not_58_out, F2, F1, F0);
  and and_7 (and_7_out, not_59_out, not_60_out, not_61_out, not_62_out, not_63_out, not_64_out, F5, not_65_out, F3, not_66_out, F1, not_67_out);
  and and_8 (and_8_out, not_68_out, not_69_out, not_70_out, not_71_out, not_72_out, not_73_out, F5, not_74_out, F3, not_75_out, F1, F0);
  and and_9 (and_9_out, not_76_out, not_77_out, not_78_out, not_79_out, not_80_out, not_81_out, not_82_out, not_83_out, F3, not_84_out, not_85_out, not_86_out);
  and and_10 (and_10_out, not_87_out, not_88_out, not_89_out, not_90_out, not_91_out, not_92_out, not_93_out, not_94_out, F3, F2, not_95_out, not_96_out);
  and and_11 (and_11_out, not_97_out, not_98_out, not_99_out, OP2, not_100_out, not_101_out);
  and and_12 (and_12_out, not_102_out, not_103_out, not_104_out, OP2, not_105_out, OP0);
  and and_13 (and_13_out, not_106_out, not_107_out, OP3, not_108_out, not_109_out, not_110_out);
  and and_14 (and_14_out, not_111_out, not_112_out, OP3, OP2, not_113_out, not_114_out);
  and and_15 (and_15_out, not_115_out, not_116_out, OP3, not_117_out, not_118_out, OP0);
  and and_16 (and_16_out, not_119_out, not_120_out, OP3, not_121_out, OP1, not_122_out);
  and and_17 (and_17_out, not_123_out, not_124_out, OP3, OP2, not_125_out, OP0);
  and and_18 (and_18_out, OP5, not_126_out, not_127_out, not_128_out, OP1, OP0);
  and and_19 (and_19_out, OP5, not_129_out, OP3, not_130_out, OP1, OP0);
  and and_20 (and_20_out, not_131_out, not_132_out, not_133_out, not_134_out, not_135_out, not_136_out, not_137_out, not_138_out, not_139_out, F2, F1, not_140_out);
  and and_21 (and_21_out, not_141_out, not_142_out, not_143_out, not_144_out, not_145_out, not_146_out, not_147_out, not_148_out, not_149_out, F2, F1, F0);
  and and_22 (and_22_out, OP5, not_150_out, not_151_out, OP2, not_152_out, not_153_out);
  and and_23 (and_23_out, not_154_out, not_155_out, not_156_out, not_157_out, not_158_out, OP0);
  and and_24 (and_24_out, not_159_out, not_160_out, not_161_out, not_162_out, not_163_out, not_164_out, not_165_out, not_166_out, not_167_out, not_168_out, not_169_out, not_170_out);
  and and_25 (and_25_out, not_171_out, not_172_out, not_173_out, not_174_out, not_175_out, not_176_out, not_177_out, not_178_out, not_179_out, not_180_out, F1, F0);
  and and_26 (and_26_out, not_181_out, not_182_out, not_183_out, not_184_out, not_185_out, not_186_out, not_187_out, not_188_out, not_189_out, not_190_out, F1, not_191_out);
  and and_27 (and_27_out, not_192_out, not_193_out, not_194_out, not_195_out, not_196_out, not_197_out, F5, not_198_out, not_199_out, not_200_out, not_201_out, not_202_out);
  and and_28 (and_28_out, not_203_out, not_204_out, not_205_out, not_206_out, not_207_out, not_208_out, F5, not_209_out, not_210_out, not_211_out, not_212_out, F0);
  and and_29 (and_29_out, not_213_out, not_214_out, not_215_out, not_216_out, not_217_out, not_218_out, F5, not_219_out, not_220_out, not_221_out, F1, not_222_out);
  and and_30 (and_30_out, not_223_out, not_224_out, not_225_out, not_226_out, not_227_out, not_228_out, F5, not_229_out, not_230_out, F2, not_231_out, not_232_out);
  and and_31 (and_31_out, not_233_out, not_234_out, not_235_out, not_236_out, not_237_out, not_238_out, F5, not_239_out, not_240_out, F2, not_241_out, F0);
  and and_32 (and_32_out, not_242_out, not_243_out, not_244_out, not_245_out, not_246_out, not_247_out, F5, not_248_out, not_249_out, F2, F1, F0);
  and and_33 (and_33_out, not_250_out, not_251_out, not_252_out, not_253_out, not_254_out, not_255_out, F5, not_256_out, F3, not_257_out, F1, not_258_out);
  and and_34 (and_34_out, not_259_out, not_260_out, not_261_out, not_262_out, not_263_out, not_264_out, F5, not_265_out, F3, not_266_out, F1, F0);
  and and_35 (and_35_out, not_267_out, not_268_out, not_269_out, not_270_out, not_271_out, not_272_out, not_273_out, not_274_out, F3, F2, not_275_out, not_276_out);
  and and_36 (and_36_out, not_277_out, not_278_out, not_279_out, OP2, not_280_out, not_281_out);
  and and_37 (and_37_out, not_282_out, not_283_out, not_284_out, OP2, not_285_out, OP0);
  and and_38 (and_38_out, OP5, not_286_out, OP3, not_287_out, OP1, OP0);
  and and_39 (and_39_out, not_288_out, not_289_out, not_290_out, not_291_out, not_292_out, not_293_out, not_294_out, not_295_out, not_296_out, F2, F1, not_297_out);
  and and_40 (and_40_out, not_298_out, not_299_out, not_300_out, not_301_out, not_302_out, not_303_out, not_304_out, not_305_out, not_306_out, F2, F1, F0);
  and and_41 (and_41_out, not_307_out, OP4, not_308_out, not_309_out, not_310_out, not_311_out, not_312_out, not_313_out, not_314_out, not_315_out, not_316_out, not_317_out);
  or or_1 (R1_Used, and_1_out, and_2_out, and_3_out, and_4_out, and_5_out, and_6_out, and_7_out, and_8_out, and_9_out, and_10_out, and_11_out, and_12_out, and_13_out, and_14_out, and_15_out, and_16_out, and_17_out, and_18_out, and_19_out, and_20_out, and_21_out, and_22_out, and_23_out);
  or or_2 (R2_Used, and_24_out, and_25_out, and_26_out, and_27_out, and_28_out, and_29_out, and_30_out, and_31_out, and_32_out, and_33_out, and_34_out, and_35_out, and_36_out, and_37_out, and_38_out, and_39_out, and_40_out, and_41_out);
endmodule

// 数据相关检测
module \数据相关检测  (
  input  [5:0] OP,
  input  [4:0] EX_WriteReg_num,
  input  EX_RegWrite,
  input  [4:0] MEM_WriteReg_num,
  input  MEM_RegWrite,
  input  [5:0] Func,
  input  [4:0] ID_R1_num,
  input  [4:0] ID_R2_num,
  output \数据相关 
);

  wire and_1_out, and_2_out, and_3_out, and_4_out, and_5_out, and_6_out, comparator_1_eq, comparator_2_eq,
       comparator_3_eq, comparator_4_eq, comparator_5_eq, comparator_6_eq, comparator_7_eq, comparator_8_eq,
       not_1_out, not_2_out, not_3_out, not_4_out, or_1_out, or_2_out, \源寄存器使用情况_1_r1_used ,
       \源寄存器使用情况_1_r2_used ;

  \源寄存器使用情况  \u_源寄存器使用情况_1  (
    .OP0(OP[0]), .OP1(OP[1]), .OP2(OP[2]), .OP3(OP[3]), .OP4(OP[4]), .OP5(OP[5]), .F0(Func[0]), .F1(Func[1]),
    .F2(Func[2]), .F3(Func[3]), .F4(Func[4]), .F5(Func[5]), .R1_Used(\源寄存器使用情况_1_r1_used ),
    .R2_Used(\源寄存器使用情况_1_r2_used ));
  Comparator #(.width(5)) comparator_1 (.a(ID_R1_num), .b(EX_WriteReg_num), .eq(comparator_1_eq));  // open: gt, lt
  Comparator #(.width(5)) comparator_2 (.a(ID_R2_num), .b(EX_WriteReg_num), .eq(comparator_2_eq));  // open: gt, lt
  Comparator #(.width(5)) comparator_3 (.a(ID_R1_num), .b(MEM_WriteReg_num), .eq(comparator_3_eq));  // open: gt, lt
  Comparator #(.width(5)) comparator_4 (.a(ID_R2_num), .b(MEM_WriteReg_num), .eq(comparator_4_eq));  // open: gt, lt
  Comparator #(.width(5)) comparator_5 (.a(ID_R1_num), .b({5{1'b0}}), .eq(comparator_5_eq));  // open: gt, lt
  Comparator #(.width(5)) comparator_6 (.a(ID_R2_num), .b({5{1'b0}}), .eq(comparator_6_eq));  // open: gt, lt
  Comparator #(.width(5)) comparator_7 (.a(ID_R1_num), .b({5{1'b0}}), .eq(comparator_7_eq));  // open: gt, lt
  Comparator #(.width(5)) comparator_8 (.a(ID_R2_num), .b({5{1'b0}}), .eq(comparator_8_eq));  // open: gt, lt
  not not_1 (not_1_out, comparator_5_eq);
  not not_2 (not_2_out, comparator_6_eq);
  not not_3 (not_3_out, comparator_7_eq);
  not not_4 (not_4_out, comparator_8_eq);
  and and_1 (and_1_out, \源寄存器使用情况_1_r1_used , comparator_1_eq, not_1_out);
  and and_2 (and_2_out, \源寄存器使用情况_1_r2_used , comparator_2_eq, not_2_out);
  and and_3 (and_3_out, \源寄存器使用情况_1_r1_used , comparator_3_eq, not_3_out);
  and and_4 (and_4_out, \源寄存器使用情况_1_r2_used , comparator_4_eq, not_4_out);
  or or_1 (or_1_out, and_1_out, and_2_out);
  or or_2 (or_2_out, and_3_out, and_4_out);
  and and_5 (and_5_out, EX_RegWrite, or_1_out);
  and and_6 (and_6_out, MEM_RegWrite, or_2_out);
  or or_3 (\数据相关 , and_5_out, and_6_out);

  // Other names for the same wires on the sheet: OP_CODE[5:0] = OP
endmodule
// IF/ID
module IF_ID (
  input  CLK,
  input  reset,
  input  en,
  input  [31:0] PC,
  input  [31:0] IR,
  input  \传输状态In_表明当前传输数据有效 ,
  output [31:0] PC_2,
  output [31:0] IR_2,
  output [31:0] IR_3,
  output \传输状态Out_表明当前传输数据有效 
);

  wire multiplexer_3_out, not_1_out;
  wire [31:0] multiplexer_1_out, multiplexer_2_out;

  not not_1 (not_1_out, en);
  Multiplexer #(.width(32), .enable("false")) multiplexer_1 (
    .in0(PC), .in1({32{1'b0}}), .out(multiplexer_1_out), .sel(reset));
  Multiplexer #(.width(32), .enable("false")) multiplexer_2 (
    .in0(IR), .in1({32{1'b0}}), .out(multiplexer_2_out), .sel(reset));
  Multiplexer #(.enable("false")) multiplexer_3 (
    .in0(\传输状态In_表明当前传输数据有效 ), .in1(1'b0), .out(multiplexer_3_out), .sel(reset));
  Register #(.width(32)) register_1 (.D(multiplexer_1_out), .en(not_1_out), .Q(PC_2), .clk(CLK));  // open: clr
  Register #(.width(32)) register_2 (.D(multiplexer_2_out), .en(not_1_out), .Q(IR_2), .clk(CLK));  // open: clr
  Register #(.width(1)) register_3 (
    .D(multiplexer_3_out), .en(not_1_out), .Q(\传输状态Out_表明当前传输数据有效 ), .clk(CLK));  // open: clr

  assign IR_3 = IR_2;
endmodule

// ID/EX
module ID_EX (
  input  CLK,
  input  reset,
  input  en,
  input  [31:0] PC,
  input  [31:0] R1,
  input  [31:0] IR,
  input  [31:0] R2,
  input  SignedExt,
  input  [4:0] shamt,
  input  JR,
  input  [15:0] imm16,
  input  JMP,
  input  SV,
  input  [25:0] imm26,
  input  LBU,
  input  [4:0] W_num,
  input  BGEZ,
  input  \传输状态In_表明当前传输数据有效 ,
  input  BEQ,
  input  BNE,
  input  MemToReg,
  input  [4:0] ID_R1_num,
  input  MemWrite,
  input  [4:0] ID_R2_num,
  input  [3:0] AluOP,
  input  AluSrc,
  input  RegWrite,
  input  JAL,
  input  RegDst,
  input  Syscall,
  output [31:0] PC_2,
  output [31:0] R1_2,
  output [31:0] IR_2,
  output [31:0] R2_2,
  output SignedExt_2,
  output [4:0] shamt_2,
  output JR_2,
  output [15:0] imm16_2,
  output JMP_2,
  output SV_2,
  output [25:0] imm26_2,
  output LBU_2,
  output [4:0] W_num_2,
  output BGEZ_2,
  output \传输状态Out_表明当前传输数据有效 ,
  output BEQ_2,
  output BNE_2,
  output MemToReg_2,
  output [4:0] ID_R1_num_2,
  output MemWrite_2,
  output [4:0] ID_R2_num_2,
  output [3:0] AluOP_2,
  output AluSrc_2,
  output RegWrite_2,
  output JAL_2,
  output RegDst_2,
  output Syscall_2
);

  wire multiplexer_3_out, multiplexer_4_out, multiplexer_5_out, multiplexer_6_out, multiplexer_7_out,
       multiplexer_8_out, multiplexer_9_out, multiplexer_10_out, multiplexer_11_out, multiplexer_12_out,
       multiplexer_14_out, multiplexer_15_out, multiplexer_16_out, multiplexer_17_out, multiplexer_18_out,
       multiplexer_25_out, not_1_out;
  wire [3:0] multiplexer_13_out;
  wire [4:0] multiplexer_21_out, multiplexer_24_out, multiplexer_26_out, multiplexer_27_out;
  wire [15:0] multiplexer_22_out;
  wire [25:0] multiplexer_23_out;
  wire [31:0] multiplexer_1_out, multiplexer_2_out, multiplexer_19_out, multiplexer_20_out;

  not not_1 (not_1_out, en);
  Multiplexer #(.width(32), .enable("false")) multiplexer_1 (
    .in0(PC), .in1({32{1'b0}}), .out(multiplexer_1_out), .sel(reset));
  Multiplexer #(.width(32), .enable("false")) multiplexer_2 (
    .in0(IR), .in1({32{1'b0}}), .out(multiplexer_2_out), .sel(reset));
  Multiplexer #(.enable("false")) multiplexer_3 (.in0(SignedExt), .in1(1'b0), .out(multiplexer_3_out), .sel(reset));
  Multiplexer #(.enable("false")) multiplexer_4 (.in0(JR), .in1(1'b0), .out(multiplexer_4_out), .sel(reset));
  Multiplexer #(.enable("false")) multiplexer_5 (.in0(JMP), .in1(1'b0), .out(multiplexer_5_out), .sel(reset));
  Multiplexer #(.enable("false")) multiplexer_6 (.in0(SV), .in1(1'b0), .out(multiplexer_6_out), .sel(reset));
  Multiplexer #(.enable("false")) multiplexer_7 (.in0(LBU), .in1(1'b0), .out(multiplexer_7_out), .sel(reset));
  Multiplexer #(.enable("false")) multiplexer_8 (.in0(BGEZ), .in1(1'b0), .out(multiplexer_8_out), .sel(reset));
  Multiplexer #(.enable("false")) multiplexer_9 (.in0(BEQ), .in1(1'b0), .out(multiplexer_9_out), .sel(reset));
  Multiplexer #(.enable("false")) multiplexer_10 (.in0(BNE), .in1(1'b0), .out(multiplexer_10_out), .sel(reset));
  Multiplexer #(.enable("false")) multiplexer_11 (.in0(MemToReg), .in1(1'b0), .out(multiplexer_11_out), .sel(reset));
  Multiplexer #(.enable("false")) multiplexer_12 (.in0(MemWrite), .in1(1'b0), .out(multiplexer_12_out), .sel(reset));
  Multiplexer #(.width(4), .enable("false")) multiplexer_13 (
    .in0(AluOP), .in1(4'b0000), .out(multiplexer_13_out), .sel(reset));
  Multiplexer #(.enable("false")) multiplexer_14 (.in0(AluSrc), .in1(1'b0), .out(multiplexer_14_out), .sel(reset));
  Multiplexer #(.enable("false")) multiplexer_15 (.in0(RegWrite), .in1(1'b0), .out(multiplexer_15_out), .sel(reset));
  Multiplexer #(.enable("false")) multiplexer_16 (.in0(JAL), .in1(1'b0), .out(multiplexer_16_out), .sel(reset));
  Multiplexer #(.enable("false")) multiplexer_17 (.in0(RegDst), .in1(1'b0), .out(multiplexer_17_out), .sel(reset));
  Multiplexer #(.enable("false")) multiplexer_18 (.in0(Syscall), .in1(1'b0), .out(multiplexer_18_out), .sel(reset));
  Register #(.width(32)) register_1 (.D(multiplexer_1_out), .en(not_1_out), .Q(PC_2), .clk(CLK));  // open: clr
  Register #(.width(32)) register_2 (.D(multiplexer_2_out), .en(not_1_out), .Q(IR_2), .clk(CLK));  // open: clr
  Register #(.width(1)) register_3 (.D(multiplexer_3_out), .en(not_1_out), .Q(SignedExt_2), .clk(CLK));  // open: clr
  Register #(.width(1)) register_4 (.D(multiplexer_4_out), .en(not_1_out), .Q(JR_2), .clk(CLK));  // open: clr
  Register #(.width(1)) register_5 (.D(multiplexer_5_out), .en(not_1_out), .Q(JMP_2), .clk(CLK));  // open: clr
  Register #(.width(1)) register_6 (.D(multiplexer_6_out), .en(not_1_out), .Q(SV_2), .clk(CLK));  // open: clr
  Register #(.width(1)) register_7 (.D(multiplexer_7_out), .en(not_1_out), .Q(LBU_2), .clk(CLK));  // open: clr
  Register #(.width(1)) register_8 (.D(multiplexer_8_out), .en(not_1_out), .Q(BGEZ_2), .clk(CLK));  // open: clr
  Register #(.width(1)) register_9 (.D(multiplexer_9_out), .en(not_1_out), .Q(BEQ_2), .clk(CLK));  // open: clr
  Register #(.width(1)) register_10 (.D(multiplexer_10_out), .en(not_1_out), .Q(BNE_2), .clk(CLK));  // open: clr
  Register #(.width(1)) register_11 (.D(multiplexer_11_out), .en(not_1_out), .Q(MemToReg_2), .clk(CLK));  // open: clr
  Register #(.width(1)) register_12 (.D(multiplexer_12_out), .en(not_1_out), .Q(MemWrite_2), .clk(CLK));  // open: clr
  Register #(.width(4)) register_13 (.D(multiplexer_13_out), .en(not_1_out), .Q(AluOP_2), .clk(CLK));  // open: clr
  Register #(.width(1)) register_14 (.D(multiplexer_14_out), .en(not_1_out), .Q(AluSrc_2), .clk(CLK));  // open: clr
  Register #(.width(1)) register_15 (.D(multiplexer_15_out), .en(not_1_out), .Q(RegWrite_2), .clk(CLK));  // open: clr
  Register #(.width(1)) register_16 (.D(multiplexer_16_out), .en(not_1_out), .Q(JAL_2), .clk(CLK));  // open: clr
  Register #(.width(1)) register_17 (.D(multiplexer_17_out), .en(not_1_out), .Q(RegDst_2), .clk(CLK));  // open: clr
  Register #(.width(1)) register_18 (.D(multiplexer_18_out), .en(not_1_out), .Q(Syscall_2), .clk(CLK));  // open: clr
  Multiplexer #(.width(32), .enable("false")) multiplexer_19 (
    .in0(R1), .in1({32{1'b0}}), .out(multiplexer_19_out), .sel(reset));
  Multiplexer #(.width(32), .enable("false")) multiplexer_20 (
    .in0(R2), .in1({32{1'b0}}), .out(multiplexer_20_out), .sel(reset));
  Multiplexer #(.width(5), .enable("false")) multiplexer_21 (
    .in0(shamt), .in1({5{1'b0}}), .out(multiplexer_21_out), .sel(reset));
  Multiplexer #(.width(16), .enable("false")) multiplexer_22 (
    .in0(imm16), .in1({16{1'b0}}), .out(multiplexer_22_out), .sel(reset));
  Multiplexer #(.width(26), .enable("false")) multiplexer_23 (
    .in0(imm26), .in1({26{1'b0}}), .out(multiplexer_23_out), .sel(reset));
  Multiplexer #(.width(5), .enable("false")) multiplexer_24 (
    .in0(W_num), .in1({5{1'b0}}), .out(multiplexer_24_out), .sel(reset));
  Multiplexer #(.enable("false")) multiplexer_25 (
    .in0(\传输状态In_表明当前传输数据有效 ), .in1(1'b0), .out(multiplexer_25_out), .sel(reset));
  Multiplexer #(.width(5), .enable("false")) multiplexer_26 (
    .in0(ID_R1_num), .in1({5{1'b0}}), .out(multiplexer_26_out), .sel(reset));
  Multiplexer #(.width(5), .enable("false")) multiplexer_27 (
    .in0(ID_R2_num), .in1({5{1'b0}}), .out(multiplexer_27_out), .sel(reset));
  Register #(.width(32)) register_19 (.D(multiplexer_19_out), .en(not_1_out), .Q(R1_2), .clk(CLK));  // open: clr
  Register #(.width(32)) register_20 (.D(multiplexer_20_out), .en(not_1_out), .Q(R2_2), .clk(CLK));  // open: clr
  Register #(.width(5)) register_21 (.D(multiplexer_21_out), .en(not_1_out), .Q(shamt_2), .clk(CLK));  // open: clr
  Register #(.width(16)) register_22 (.D(multiplexer_22_out), .en(not_1_out), .Q(imm16_2), .clk(CLK));  // open: clr
  Register #(.width(26)) register_23 (.D(multiplexer_23_out), .en(not_1_out), .Q(imm26_2), .clk(CLK));  // open: clr
  Register #(.width(5)) register_24 (.D(multiplexer_24_out), .en(not_1_out), .Q(W_num_2), .clk(CLK));  // open: clr
  Register #(.width(1)) register_25 (
    .D(multiplexer_25_out), .en(not_1_out), .Q(\传输状态Out_表明当前传输数据有效 ), .clk(CLK));  // open: clr
  Register #(.width(5)) register_26 (.D(multiplexer_26_out), .en(not_1_out), .Q(ID_R1_num_2), .clk(CLK));  // open: clr
  Register #(.width(5)) register_27 (.D(multiplexer_27_out), .en(not_1_out), .Q(ID_R2_num_2), .clk(CLK));  // open: clr
endmodule

module EX_MEM (
  input  CLK,
  input  reset,
  input  en,
  input  [31:0] PC,
  input  [31:0] Result1,
  input  [31:0] IR,
  input  [31:0] R2,
  input  SignedExt,
  input  [31:0] Result2,
  input  JR,
  input  JMP,
  input  [31:0] R1,
  input  SV,
  input  LBU,
  input  [4:0] W_num,
  input  BGEZ,
  input  \传输状态In_表明当前传输数据有效 ,
  input  BEQ,
  input  BNE,
  input  [31:0] EPC,
  input  MemToReg,
  input  MemWrite,
  input  [3:0] AluOP,
  input  AluSrc,
  input  RegWrite,
  input  JAL,
  input  RegDst,
  input  Syscall,
  output [31:0] PC_2,
  output [31:0] Result1_2,
  output [31:0] IR_2,
  output [31:0] R2_2,
  output SignedExt_2,
  output [31:0] Result2_2,
  output JR_2,
  output JMP_2,
  output [31:0] R1_2,
  output SV_2,
  output LBU_2,
  output [4:0] W_num_2,
  output BGEZ_2,
  output \传输状态Out_表明当前传输数据有效 ,
  output BEQ_2,
  output BNE_2,
  output [31:0] EPC_2,
  output MemToReg_2,
  output MemWrite_2,
  output [3:0] AluOP_2,
  output AluSrc_2,
  output RegWrite_2,
  output JAL_2,
  output RegDst_2,
  output Syscall_2
);

  wire multiplexer_3_out, multiplexer_4_out, multiplexer_5_out, multiplexer_6_out, multiplexer_7_out,
       multiplexer_8_out, multiplexer_9_out, multiplexer_10_out, multiplexer_11_out, multiplexer_12_out,
       multiplexer_14_out, multiplexer_15_out, multiplexer_16_out, multiplexer_17_out, multiplexer_18_out,
       multiplexer_22_out, multiplexer_25_out, not_1_out, register_22_q, undriven;
  wire [3:0] multiplexer_13_out;
  wire [4:0] multiplexer_24_out;
  wire [31:0] multiplexer_1_out, multiplexer_2_out, multiplexer_19_out, multiplexer_20_out,
       multiplexer_21_out, multiplexer_23_out, multiplexer_26_out;

  not not_1 (not_1_out, en);
  Multiplexer #(.width(32), .enable("false")) multiplexer_1 (
    .in0(PC), .in1({32{1'b0}}), .out(multiplexer_1_out), .sel(reset));
  Multiplexer #(.width(32), .enable("false")) multiplexer_2 (
    .in0(IR), .in1({32{1'b0}}), .out(multiplexer_2_out), .sel(reset));
  Multiplexer #(.enable("false")) multiplexer_3 (.in0(SignedExt), .in1(1'b0), .out(multiplexer_3_out), .sel(reset));
  Multiplexer #(.enable("false")) multiplexer_4 (.in0(JR), .in1(1'b0), .out(multiplexer_4_out), .sel(reset));
  Multiplexer #(.enable("false")) multiplexer_5 (.in0(JMP), .in1(1'b0), .out(multiplexer_5_out), .sel(reset));
  Multiplexer #(.enable("false")) multiplexer_6 (.in0(SV), .in1(1'b0), .out(multiplexer_6_out), .sel(reset));
  Multiplexer #(.enable("false")) multiplexer_7 (.in0(LBU), .in1(1'b0), .out(multiplexer_7_out), .sel(reset));
  Multiplexer #(.enable("false")) multiplexer_8 (.in0(BGEZ), .in1(1'b0), .out(multiplexer_8_out), .sel(reset));
  Multiplexer #(.enable("false")) multiplexer_9 (.in0(BEQ), .in1(1'b0), .out(multiplexer_9_out), .sel(reset));
  Multiplexer #(.enable("false")) multiplexer_10 (.in0(BNE), .in1(1'b0), .out(multiplexer_10_out), .sel(reset));
  Multiplexer #(.enable("false")) multiplexer_11 (.in0(MemToReg), .in1(1'b0), .out(multiplexer_11_out), .sel(reset));
  Multiplexer #(.enable("false")) multiplexer_12 (.in0(MemWrite), .in1(1'b0), .out(multiplexer_12_out), .sel(reset));
  Multiplexer #(.width(4), .enable("false")) multiplexer_13 (
    .in0(AluOP), .in1(4'b0000), .out(multiplexer_13_out), .sel(reset));
  Multiplexer #(.enable("false")) multiplexer_14 (.in0(AluSrc), .in1(1'b0), .out(multiplexer_14_out), .sel(reset));
  Multiplexer #(.enable("false")) multiplexer_15 (.in0(RegWrite), .in1(1'b0), .out(multiplexer_15_out), .sel(reset));
  Multiplexer #(.enable("false")) multiplexer_16 (.in0(JAL), .in1(1'b0), .out(multiplexer_16_out), .sel(reset));
  Multiplexer #(.enable("false")) multiplexer_17 (.in0(RegDst), .in1(1'b0), .out(multiplexer_17_out), .sel(reset));
  Multiplexer #(.enable("false")) multiplexer_18 (.in0(Syscall), .in1(1'b0), .out(multiplexer_18_out), .sel(reset));
  Register #(.width(32)) register_1 (.D(multiplexer_1_out), .en(not_1_out), .Q(PC_2), .clk(CLK));  // open: clr
  Register #(.width(32)) register_2 (.D(multiplexer_2_out), .en(not_1_out), .Q(IR_2), .clk(CLK));  // open: clr
  Register #(.width(1)) register_3 (.D(multiplexer_3_out), .en(not_1_out), .Q(SignedExt_2), .clk(CLK));  // open: clr
  Register #(.width(1)) register_4 (.D(multiplexer_4_out), .en(not_1_out), .Q(JR_2), .clk(CLK));  // open: clr
  Register #(.width(1)) register_5 (.D(multiplexer_5_out), .en(not_1_out), .Q(JMP_2), .clk(CLK));  // open: clr
  Register #(.width(1)) register_6 (.D(multiplexer_6_out), .en(not_1_out), .Q(SV_2), .clk(CLK));  // open: clr
  Register #(.width(1)) register_7 (.D(multiplexer_7_out), .en(not_1_out), .Q(LBU_2), .clk(CLK));  // open: clr
  Register #(.width(1)) register_8 (.D(multiplexer_8_out), .en(not_1_out), .Q(BGEZ_2), .clk(CLK));  // open: clr
  Register #(.width(1)) register_9 (.D(multiplexer_9_out), .en(not_1_out), .Q(BEQ_2), .clk(CLK));  // open: clr
  Register #(.width(1)) register_10 (.D(multiplexer_10_out), .en(not_1_out), .Q(BNE_2), .clk(CLK));  // open: clr
  Register #(.width(1)) register_11 (.D(multiplexer_11_out), .en(not_1_out), .Q(MemToReg_2), .clk(CLK));  // open: clr
  Register #(.width(1)) register_12 (.D(multiplexer_12_out), .en(not_1_out), .Q(MemWrite_2), .clk(CLK));  // open: clr
  Register #(.width(4)) register_13 (.D(multiplexer_13_out), .en(not_1_out), .Q(AluOP_2), .clk(CLK));  // open: clr
  Register #(.width(1)) register_14 (.D(multiplexer_14_out), .en(not_1_out), .Q(AluSrc_2), .clk(CLK));  // open: clr
  Register #(.width(1)) register_15 (.D(multiplexer_15_out), .en(not_1_out), .Q(RegWrite_2), .clk(CLK));  // open: clr
  Register #(.width(1)) register_16 (.D(multiplexer_16_out), .en(not_1_out), .Q(JAL_2), .clk(CLK));  // open: clr
  Register #(.width(1)) register_17 (.D(multiplexer_17_out), .en(not_1_out), .Q(RegDst_2), .clk(CLK));  // open: clr
  Register #(.width(1)) register_18 (.D(multiplexer_18_out), .en(not_1_out), .Q(Syscall_2), .clk(CLK));  // open: clr
  Multiplexer #(.width(32), .enable("false")) multiplexer_19 (
    .in0(Result1), .in1({32{1'b0}}), .out(multiplexer_19_out), .sel(reset));
  Multiplexer #(.width(32), .enable("false")) multiplexer_20 (
    .in0(R2), .in1({32{1'b0}}), .out(multiplexer_20_out), .sel(reset));
  Multiplexer #(.width(32), .enable("false")) multiplexer_21 (
    .in0(Result2), .in1({32{1'b0}}), .out(multiplexer_21_out), .sel(reset));
  Multiplexer #(.enable("false")) multiplexer_22 (.in0(undriven), .in1(1'b0), .out(multiplexer_22_out), .sel(reset));
  Multiplexer #(.width(32), .enable("false")) multiplexer_23 (
    .in0(R1), .in1({32{1'b0}}), .out(multiplexer_23_out), .sel(reset));
  Multiplexer #(.width(5), .enable("false")) multiplexer_24 (
    .in0(W_num), .in1({5{1'b0}}), .out(multiplexer_24_out), .sel(reset));
  Multiplexer #(.enable("false")) multiplexer_25 (
    .in0(\传输状态In_表明当前传输数据有效 ), .in1(1'b0), .out(multiplexer_25_out), .sel(reset));
  Multiplexer #(.width(32), .enable("false")) multiplexer_26 (
    .in0(EPC), .in1({32{1'b0}}), .out(multiplexer_26_out), .sel(reset));
  Register #(.width(32)) register_19 (.D(multiplexer_19_out), .en(not_1_out), .Q(Result1_2), .clk(CLK));  // open: clr
  Register #(.width(32)) register_20 (.D(multiplexer_20_out), .en(not_1_out), .Q(R2_2), .clk(CLK));  // open: clr
  Register #(.width(32)) register_21 (.D(multiplexer_21_out), .en(not_1_out), .Q(Result2_2), .clk(CLK));  // open: clr
  Register #(.width(1)) register_22 (
    .D(multiplexer_22_out), .en(not_1_out), .Q(register_22_q), .clk(CLK));  // open: clr
  Register #(.width(32)) register_23 (.D(multiplexer_23_out), .en(not_1_out), .Q(R1_2), .clk(CLK));  // open: clr
  Register #(.width(5)) register_24 (.D(multiplexer_24_out), .en(not_1_out), .Q(W_num_2), .clk(CLK));  // open: clr
  Register #(.width(1)) register_25 (
    .D(multiplexer_25_out), .en(not_1_out), .Q(\传输状态Out_表明当前传输数据有效 ), .clk(CLK));  // open: clr
  Register #(.width(32)) register_26 (.D(multiplexer_26_out), .en(not_1_out), .Q(EPC_2), .clk(CLK));  // open: clr
endmodule

module MEM_WB (
  input  CLK,
  input  reset,
  input  en,
  input  [31:0] PC,
  input  [31:0] Result1,
  input  [31:0] IR,
  input  [31:0] Dout,
  input  SignedExt,
  input  [31:0] R1,
  input  JR,
  input  [31:0] R2,
  input  JMP,
  input  [4:0] W_num,
  input  SV,
  input  LBU,
  input  BGEZ,
  input  \传输状态In_表明当前传输数据有效 ,
  input  BEQ,
  input  BNE,
  input  [31:0] EPC,
  input  MemToReg,
  input  MemWrite,
  input  [3:0] AluOP,
  input  AluSrc,
  input  RegWrite,
  input  JAL,
  input  RegDst,
  input  Syscall,
  output [31:0] PC_2,
  output [31:0] Result1_2,
  output [31:0] IR_2,
  output [31:0] Dout_2,
  output SignedExt_2,
  output [31:0] R1_2,
  output JR_2,
  output [31:0] R2_2,
  output JMP_2,
  output [4:0] W_num_2,
  output SV_2,
  output LBU_2,
  output BGEZ_2,
  output \传输状态Out_表明当前传输数据有效 ,
  output BEQ_2,
  output BNE_2,
  output [31:0] EPC_2,
  output MemToReg_2,
  output MemWrite_2,
  output [3:0] AluOP_2,
  output AluSrc_2,
  output RegWrite_2,
  output JAL_2,
  output RegDst_2,
  output Syscall_2
);

  wire multiplexer_3_out, multiplexer_4_out, multiplexer_5_out, multiplexer_6_out, multiplexer_7_out,
       multiplexer_8_out, multiplexer_9_out, multiplexer_10_out, multiplexer_11_out, multiplexer_12_out,
       multiplexer_14_out, multiplexer_15_out, multiplexer_16_out, multiplexer_17_out, multiplexer_18_out,
       multiplexer_24_out, multiplexer_25_out, not_1_out, register_24_q, undriven;
  wire [3:0] multiplexer_13_out;
  wire [4:0] multiplexer_23_out;
  wire [31:0] multiplexer_1_out, multiplexer_2_out, multiplexer_19_out, multiplexer_20_out,
       multiplexer_21_out, multiplexer_22_out, multiplexer_26_out;

  not not_1 (not_1_out, en);
  Multiplexer #(.width(32), .enable("false")) multiplexer_1 (
    .in0(PC), .in1({32{1'b0}}), .out(multiplexer_1_out), .sel(reset));
  Multiplexer #(.width(32), .enable("false")) multiplexer_2 (
    .in0(IR), .in1({32{1'b0}}), .out(multiplexer_2_out), .sel(reset));
  Multiplexer #(.enable("false")) multiplexer_3 (.in0(SignedExt), .in1(1'b0), .out(multiplexer_3_out), .sel(reset));
  Multiplexer #(.enable("false")) multiplexer_4 (.in0(JR), .in1(1'b0), .out(multiplexer_4_out), .sel(reset));
  Multiplexer #(.enable("false")) multiplexer_5 (.in0(JMP), .in1(1'b0), .out(multiplexer_5_out), .sel(reset));
  Multiplexer #(.enable("false")) multiplexer_6 (.in0(SV), .in1(1'b0), .out(multiplexer_6_out), .sel(reset));
  Multiplexer #(.enable("false")) multiplexer_7 (.in0(LBU), .in1(1'b0), .out(multiplexer_7_out), .sel(reset));
  Multiplexer #(.enable("false")) multiplexer_8 (.in0(BGEZ), .in1(1'b0), .out(multiplexer_8_out), .sel(reset));
  Multiplexer #(.enable("false")) multiplexer_9 (.in0(BEQ), .in1(1'b0), .out(multiplexer_9_out), .sel(reset));
  Multiplexer #(.enable("false")) multiplexer_10 (.in0(BNE), .in1(1'b0), .out(multiplexer_10_out), .sel(reset));
  Multiplexer #(.enable("false")) multiplexer_11 (.in0(MemToReg), .in1(1'b0), .out(multiplexer_11_out), .sel(reset));
  Multiplexer #(.enable("false")) multiplexer_12 (.in0(MemWrite), .in1(1'b0), .out(multiplexer_12_out), .sel(reset));
  Multiplexer #(.width(4), .enable("false")) multiplexer_13 (
    .in0(AluOP), .in1(4'b0000), .out(multiplexer_13_out), .sel(reset));
  Multiplexer #(.enable("false")) multiplexer_14 (.in0(AluSrc), .in1(1'b0), .out(multiplexer_14_out), .sel(reset));
  Multiplexer #(.enable("false")) multiplexer_15 (.in0(RegWrite), .in1(1'b0), .out(multiplexer_15_out), .sel(reset));
  Multiplexer #(.enable("false")) multiplexer_16 (.in0(JAL), .in1(1'b0), .out(multiplexer_16_out), .sel(reset));
  Multiplexer #(.enable("false")) multiplexer_17 (.in0(RegDst), .in1(1'b0), .out(multiplexer_17_out), .sel(reset));
  Multiplexer #(.enable("false")) multiplexer_18 (.in0(Syscall), .in1(1'b0), .out(multiplexer_18_out), .sel(reset));
  Register #(.width(32)) register_1 (.D(multiplexer_1_out), .en(not_1_out), .Q(PC_2), .clk(CLK));  // open: clr
  Register #(.width(32)) register_2 (.D(multiplexer_2_out), .en(not_1_out), .Q(IR_2), .clk(CLK));  // open: clr
  Register #(.width(1)) register_3 (.D(multiplexer_3_out), .en(not_1_out), .Q(SignedExt_2), .clk(CLK));  // open: clr
  Register #(.width(1)) register_4 (.D(multiplexer_4_out), .en(not_1_out), .Q(JR_2), .clk(CLK));  // open: clr
  Register #(.width(1)) register_5 (.D(multiplexer_5_out), .en(not_1_out), .Q(JMP_2), .clk(CLK));  // open: clr
  Register #(.width(1)) register_6 (.D(multiplexer_6_out), .en(not_1_out), .Q(SV_2), .clk(CLK));  // open: clr
  Register #(.width(1)) register_7 (.D(multiplexer_7_out), .en(not_1_out), .Q(LBU_2), .clk(CLK));  // open: clr
  Register #(.width(1)) register_8 (.D(multiplexer_8_out), .en(not_1_out), .Q(BGEZ_2), .clk(CLK));  // open: clr
  Register #(.width(1)) register_9 (.D(multiplexer_9_out), .en(not_1_out), .Q(BEQ_2), .clk(CLK));  // open: clr
  Register #(.width(1)) register_10 (.D(multiplexer_10_out), .en(not_1_out), .Q(BNE_2), .clk(CLK));  // open: clr
  Register #(.width(1)) register_11 (.D(multiplexer_11_out), .en(not_1_out), .Q(MemToReg_2), .clk(CLK));  // open: clr
  Register #(.width(1)) register_12 (.D(multiplexer_12_out), .en(not_1_out), .Q(MemWrite_2), .clk(CLK));  // open: clr
  Register #(.width(4)) register_13 (.D(multiplexer_13_out), .en(not_1_out), .Q(AluOP_2), .clk(CLK));  // open: clr
  Register #(.width(1)) register_14 (.D(multiplexer_14_out), .en(not_1_out), .Q(AluSrc_2), .clk(CLK));  // open: clr
  Register #(.width(1)) register_15 (.D(multiplexer_15_out), .en(not_1_out), .Q(RegWrite_2), .clk(CLK));  // open: clr
  Register #(.width(1)) register_16 (.D(multiplexer_16_out), .en(not_1_out), .Q(JAL_2), .clk(CLK));  // open: clr
  Register #(.width(1)) register_17 (.D(multiplexer_17_out), .en(not_1_out), .Q(RegDst_2), .clk(CLK));  // open: clr
  Register #(.width(1)) register_18 (.D(multiplexer_18_out), .en(not_1_out), .Q(Syscall_2), .clk(CLK));  // open: clr
  Multiplexer #(.width(32), .enable("false")) multiplexer_19 (
    .in0(Result1), .in1({32{1'b0}}), .out(multiplexer_19_out), .sel(reset));
  Multiplexer #(.width(32), .enable("false")) multiplexer_20 (
    .in0(Dout), .in1({32{1'b0}}), .out(multiplexer_20_out), .sel(reset));
  Multiplexer #(.width(32), .enable("false")) multiplexer_21 (
    .in0(R1), .in1({32{1'b0}}), .out(multiplexer_21_out), .sel(reset));
  Multiplexer #(.width(32), .enable("false")) multiplexer_22 (
    .in0(R2), .in1({32{1'b0}}), .out(multiplexer_22_out), .sel(reset));
  Multiplexer #(.width(5), .enable("false")) multiplexer_23 (
    .in0(W_num), .in1({5{1'b0}}), .out(multiplexer_23_out), .sel(reset));
  Multiplexer #(.enable("false")) multiplexer_24 (.in0(undriven), .in1(1'b0), .out(multiplexer_24_out), .sel(reset));
  Multiplexer #(.enable("false")) multiplexer_25 (
    .in0(\传输状态In_表明当前传输数据有效 ), .in1(1'b0), .out(multiplexer_25_out), .sel(reset));
  Multiplexer #(.width(32), .enable("false")) multiplexer_26 (
    .in0(EPC), .in1({32{1'b0}}), .out(multiplexer_26_out), .sel(reset));
  Register #(.width(32)) register_19 (.D(multiplexer_19_out), .en(not_1_out), .Q(Result1_2), .clk(CLK));  // open: clr
  Register #(.width(32)) register_20 (.D(multiplexer_20_out), .en(not_1_out), .Q(Dout_2), .clk(CLK));  // open: clr
  Register #(.width(32)) register_21 (.D(multiplexer_21_out), .en(not_1_out), .Q(R1_2), .clk(CLK));  // open: clr
  Register #(.width(32)) register_22 (.D(multiplexer_22_out), .en(not_1_out), .Q(R2_2), .clk(CLK));  // open: clr
  Register #(.width(5)) register_23 (.D(multiplexer_23_out), .en(not_1_out), .Q(W_num_2), .clk(CLK));  // open: clr
  Register #(.width(1)) register_24 (
    .D(multiplexer_24_out), .en(not_1_out), .Q(register_24_q), .clk(CLK));  // open: clr
  Register #(.width(1)) register_25 (
    .D(multiplexer_25_out), .en(not_1_out), .Q(\传输状态Out_表明当前传输数据有效 ), .clk(CLK));  // open: clr
  Register #(.width(32)) register_26 (.D(multiplexer_26_out), .en(not_1_out), .Q(EPC_2), .clk(CLK));  // open: clr
endmodule

module \分支相关流水线  (
);

  wire CLK, Go, IR1, IR2, IR3, RST, W1, W2, W3;
  wire [11:0] EX_PC, ID_PC, IF_PC, MEM_PC, WB_PC;
  wire [15:0] \LoadUse次数 , \总周期数 , \插入气泡数 , \无条件分支数 , \条件分支成功数 ;
  wire [31:0] LedData;

  Button \u_总复位  (.out(RST));
  Button _1 (.out(IR1));
  Button _2 (.out(IR2));
  Button _3 (.out(IR3));
  Button \u_继续运行  (.out(Go));
  LED led_1 (.in(W1));
  LED led_2 (.in(W2));
  LED led_3 (.in(W3));
  Hex_Digit_Display hex_digit_display_1 (.value(LedData[31:28]));  // open: dp
  Hex_Digit_Display hex_digit_display_2 (.value(LedData[27:24]));  // open: dp
  Hex_Digit_Display hex_digit_display_3 (.value(LedData[23:20]));  // open: dp
  Hex_Digit_Display hex_digit_display_4 (.value(LedData[19:16]));  // open: dp
  Hex_Digit_Display hex_digit_display_5 (.value(LedData[15:12]));  // open: dp
  Hex_Digit_Display hex_digit_display_6 (.value(LedData[11:8]));  // open: dp
  Hex_Digit_Display hex_digit_display_7 (.value(LedData[7:4]));  // open: dp
  Clock clock_1 (.out(CLK));
  Hex_Digit_Display hex_digit_display_8 (.value(LedData[3:0]));  // open: dp
  // Probe on \总周期数 
  // Probe on \无条件分支数 
  // Probe on \条件分支成功数 
  // Probe on \插入气泡数 
  // Probe on \LoadUse次数 
  // Probe on IF_PC
  // Probe on ID_PC
  // Probe on MEM_PC
  // Probe on EX_PC
  // Probe on WB_PC

  // Notes on the sheet:
  //   中断源
  //   中断等待指示
  //   数码管输出
  //   流水调试日志用
endmodule

module \气泡流水线  (
);

  wire and_1_out, and_3_out, and_4_out, and_5_out, and_7_out, BEQ, BGEZ, BNE, CLK, comparator_1_eq, EX_B,
       EX_B_en, EX_Branch, EX_Equal, EX_JMP, EX_JR, ex_mem_1_jal_2, ex_mem_1_lbu_2, ex_mem_1_memtoreg_2,
       \ex_mem_1_传输状态out_表明当前传输数据有效 , EX_RegWrite, EX_SYSCALL, EX_Valid, Go, halt, id_ex_1_alusrc_2,
       id_ex_1_jal_2, id_ex_1_lbu_2, id_ex_1_memtoreg_2, id_ex_1_memwrite_2, \if_id_1_传输状态out_表明当前传输数据有效 ,
       IR1, IR2, IR3, MEM_RegWrite, MEM_SYSCALL, mem_wb_1_jal_2, mem_wb_1_lbu_2, mem_wb_1_memtoreg_2,
       MemWrite, mips_alu_1_equal, not_1_out, not_2_out, not_3_out, not_4_out, not_5_out, not_6_out,
       not_7_out, not_8_out, or_1_out, or_2_out, or_3_out, PC_en, RegWrite, RST, show, SignedExt, SV, W1, W2,
       W3, WB_Syscall, WB_Valid, \数据相关 , \硬布线控制器_1_alu_src , \硬布线控制器_1_beq , \硬布线控制器_1_bgez , \硬布线控制器_1_bne ,
       \硬布线控制器_1_jal , \硬布线控制器_1_jmp , \硬布线控制器_1_jr , \硬布线控制器_1_lbu , \硬布线控制器_1_memtoreg ,
       \硬布线控制器_1_memwrite , \硬布线控制器_1_regdst , \硬布线控制器_1_regwrite , \硬布线控制器_1_signedext , \硬布线控制器_1_syscall ;
  wire [1:1] or_6_out;
  wire [3:0] id_ex_1_aluop_2, \硬布线控制器_1_alu_op ;
  wire [4:0] EX_WriteReg_num, id_ex_1_shamt_2, ID_R1_num, ID_R2_num, MEM_WriteReg_num, multiplexer_4_out,
       multiplexer_5_out, multiplexer_6_out, W_num;
  wire [5:0] FUNC, OP_CODE;
  wire [7:0] multiplexer_11_out;
  wire [15:0] id_ex_1_imm16_2, \LoadUse次数 , \总周期数 , \插入气泡数 , \无条件分支数 , \条件分支成功数 ;
  wire [25:0] id_ex_1_imm26_2;
  wire [25:6] if_id_1_ir_3;
  wire [31:0] adder_1_out, adder_2_out, adder_3_out, adder_4_out, bit_extender_1_out, bit_extender_2_out,
       Din, EX_IR, ex_mem_1_r2_2, ex_mem_1_result1_2, EX_PC, EX_R1, id_ex_1_r2_2, ID_IR, ID_PC, ID_R1, IF_IR,
       IF_PC, LedData, MEM_IR, MEM_PC, MEM_R1, mem_wb_1_dout_2, mem_wb_1_result1_2, mips_alu_1_result,
       mips_alu_1_result_2, mips_regifile_1_r2, multiplexer_1_out, multiplexer_7_out, multiplexer_8_out,
       multiplexer_10_out, multiplexer_12_out, multiplexer_13_out, R1, R2, ram_1_data, shifter_1_out, WB_IR,
       WB_PC;

  Button \u_总复位  (.out(RST));
  Button _1 (.out(IR1));
  Button _2 (.out(IR2));
  Button _3 (.out(IR3));
  Button \u_继续运行  (.out(Go));
  LED led_1 (.in(W1));
  LED led_2 (.in(W2));
  LED led_3 (.in(W3));
  not not_1 (not_1_out, halt);
  not not_2 (not_2_out, halt);
  Multiplexer #(.width(32), .enable("false")) multiplexer_1 (
    .in0(adder_1_out), .in1(multiplexer_10_out), .out(multiplexer_1_out), .sel(EX_Branch));
  Hex_Digit_Display hex_digit_display_1 (.value(LedData[31:28]));  // open: dp
  and and_1 (and_1_out, not_1_out, \数据相关 );
  or or_1 (or_1_out, not_2_out, Go);
  Register #(.width(32)) PC (.D(multiplexer_1_out), .en(PC_en), .Q(IF_PC), .clk(CLK), .clr(RST));
  Hex_Digit_Display hex_digit_display_2 (.value(LedData[27:24]));  // open: dp
  Hex_Digit_Display hex_digit_display_3 (.value(LedData[23:20]));  // open: dp
  Counter #(.width(16), .max('hffff)) counter_1 (
    .count(and_1_out), .Q(\插入气泡数 ), .clk(CLK), .clr(RST));  // open: load, D, carry
  and and_2 (PC_en, or_1_out, not_3_out);
  not not_3 (not_3_out, \数据相关 );
  Hex_Digit_Display hex_digit_display_4 (.value(LedData[15:12]));  // open: dp
  Hex_Digit_Display hex_digit_display_5 (.value(LedData[19:16]));  // open: dp
  Adder #(.width(32)) adder_1 (.a(IF_PC), .b(32'h4), .out(adder_1_out));  // open: cin, cout
  Hex_Digit_Display hex_digit_display_6 (.value(LedData[7:4]));  // open: dp
  Hex_Digit_Display hex_digit_display_7 (.value(LedData[11:8]));  // open: dp
  Clock clock_1 (.out(CLK));
  ROM #(.addrWidth(10), .dataWidth(32)) rom_1 (.addr(IF_PC[11:2]), .data(IF_IR));  // open: sel
  Hex_Digit_Display hex_digit_display_8 (.value(LedData[3:0]));  // open: dp
  not not_4 (not_4_out, PC_en);
  or or_2 (or_2_out, EX_Branch, RST);
  IF_ID if_id_1 (
    .CLK(CLK), .reset(or_2_out), .en(not_4_out), .PC(IF_PC), .IR(IF_IR), .PC_2(ID_PC), .IR_2(ID_IR),
    .IR_3({OP_CODE, if_id_1_ir_3, FUNC}), .\传输状态In_表明当前传输数据有效 (1'b1),
    .\传输状态Out_表明当前传输数据有效 (\if_id_1_传输状态out_表明当前传输数据有效 ));
  // Probe on \总周期数 
  // Probe on \无条件分支数 
  // Probe on \条件分支成功数 
  // Probe on \插入气泡数 
  // Probe on \LoadUse次数 
  // Probe on IF_PC[11:0]
  \硬布线控制器  \u_硬布线控制器_1  (
    .Func(FUNC), .OP(OP_CODE), .ALU_OP(\硬布线控制器_1_alu_op ), .MemToReg(\硬布线控制器_1_memtoreg ),
    .MemWrite(\硬布线控制器_1_memwrite ), .ALU_SRC(\硬布线控制器_1_alu_src ), .RegWrite(\硬布线控制器_1_regwrite ),
    .SysCALL(\硬布线控制器_1_syscall ), .SignedExt(\硬布线控制器_1_signedext ), .RegDst(\硬布线控制器_1_regdst ),
    .JR(\硬布线控制器_1_jr ), .JMP(\硬布线控制器_1_jmp ), .Beq(\硬布线控制器_1_beq ), .JAL(\硬布线控制器_1_jal ),
    .Bne(\硬布线控制器_1_bne ), .SV(SV), .BGEZ(\硬布线控制器_1_bgez ), .LBU(\硬布线控制器_1_lbu ));
  Multiplexer #(.width(5), .enable("false")) multiplexer_2 (
    .in0(if_id_1_ir_3[25:21]), .in1(5'b00010), .out(ID_R1_num), .sel(\硬布线控制器_1_syscall ));
  // Probe on ID_PC[11:0]
  Multiplexer #(.width(5), .enable("false")) multiplexer_3 (
    .in0(if_id_1_ir_3[20:16]), .in1(5'b00100), .out(ID_R2_num), .sel(\硬布线控制器_1_syscall ));
  Multiplexer #(.width(5), .enable("false")) multiplexer_4 (
    .in0(if_id_1_ir_3[20:16]), .in1(if_id_1_ir_3[15:11]), .out(multiplexer_4_out), .sel(\硬布线控制器_1_regdst ));
  // Probe on EX_PC[11:0]
  // Probe on MEM_PC[11:0]
  \数据相关检测  \u_数据相关检测_1  (
    .OP(OP_CODE), .EX_WriteReg_num(EX_WriteReg_num), .EX_RegWrite(EX_RegWrite),
    .MEM_WriteReg_num(MEM_WriteReg_num), .MEM_RegWrite(MEM_RegWrite), .\数据相关 (\数据相关 ), .Func(FUNC),
    .ID_R1_num(ID_R1_num), .ID_R2_num(ID_R2_num));
  Multiplexer #(.width(5), .enable("false")) multiplexer_5 (
    .in0(multiplexer_4_out), .in1({5{1'b1}}), .out(multiplexer_5_out), .sel(\硬布线控制器_1_jal ));
  // Probe on WB_PC[11:0]
  Multiplexer #(.width(5), .enable("false")) multiplexer_6 (
    .in0(if_id_1_ir_3[10:6]), .in1(ID_R1[4:0]), .out(multiplexer_6_out), .sel(SV));
  // Probe on IF_IR
  // Probe on ID_R1
  MIPS_Regifile mips_regifile_1 (
    .Din(Din), .Clk(CLK), .R1(ID_R1), .R2(mips_regifile_1_r2), .WE(RegWrite), .W_num(W_num),
    .R1_num(ID_R1_num), .R2_num(ID_R2_num));
  // Probe on mips_regifile_1_r2
  // Probe on ID_IR
  not not_5 (not_5_out, PC_en);
  or or_3 (or_3_out, not_5_out, EX_Branch, RST);
  // Probe on EX_IR
  ID_EX id_ex_1 (
    .CLK(CLK), .reset(or_3_out), .en(halt), .PC(ID_PC), .R1(ID_R1), .IR(ID_IR), .R2(mips_regifile_1_r2),
    .SignedExt(\硬布线控制器_1_signedext ), .shamt(multiplexer_6_out), .JR(\硬布线控制器_1_jr ),
    .imm16({if_id_1_ir_3[15:6], FUNC}), .JMP(\硬布线控制器_1_jmp ), .LBU(\硬布线控制器_1_lbu ), .BGEZ(\硬布线控制器_1_bgez ),
    .BEQ(\硬布线控制器_1_beq ), .BNE(\硬布线控制器_1_bne ), .MemToReg(\硬布线控制器_1_memtoreg ),
    .MemWrite(\硬布线控制器_1_memwrite ), .AluOP(\硬布线控制器_1_alu_op ), .AluSrc(\硬布线控制器_1_alu_src ),
    .RegWrite(\硬布线控制器_1_regwrite ), .JAL(\硬布线控制器_1_jal ), .Syscall(\硬布线控制器_1_syscall ), .PC_2(EX_PC),
    .R1_2(EX_R1), .IR_2(EX_IR), .R2_2(id_ex_1_r2_2), .SignedExt_2(SignedExt), .shamt_2(id_ex_1_shamt_2),
    .JR_2(EX_JR), .imm16_2(id_ex_1_imm16_2), .JMP_2(EX_JMP), .LBU_2(id_ex_1_lbu_2), .BGEZ_2(BGEZ),
    .BEQ_2(BEQ), .BNE_2(BNE), .MemToReg_2(id_ex_1_memtoreg_2), .MemWrite_2(id_ex_1_memwrite_2),
    .AluOP_2(id_ex_1_aluop_2), .AluSrc_2(id_ex_1_alusrc_2), .RegWrite_2(EX_RegWrite), .JAL_2(id_ex_1_jal_2),
    .Syscall_2(EX_SYSCALL), .imm26({if_id_1_ir_3, FUNC}), .imm26_2(id_ex_1_imm26_2),
    .W_num(multiplexer_5_out), .W_num_2(EX_WriteReg_num), .\传输状态In_表明当前传输数据有效 (\if_id_1_传输状态out_表明当前传输数据有效 ),
    .\传输状态Out_表明当前传输数据有效 (EX_Valid));  // open: SV, RegDst, SV_2, RegDst_2, ID_R1_num, ID_R1_num_2, ID_R2_num, ID_R2_num_2
  or or_4 (EX_B, BNE, BEQ, BGEZ);
  assign bit_extender_1_out = {{16{id_ex_1_imm16_2[15]}}, id_ex_1_imm16_2};  // Bit_Extender bit_extender_1
  assign bit_extender_2_out = {{16{1'b0}}, id_ex_1_imm16_2};  // Bit_Extender bit_extender_2
  // Probe on MEM_IR
  or or_5 (EX_Branch, EX_JR, EX_JMP, EX_B_en);
  Multiplexer #(.width(32), .enable("false")) multiplexer_7 (
    .in0(bit_extender_2_out), .in1(bit_extender_1_out), .out(multiplexer_7_out), .sel(SignedExt));
  Adder #(.width(32)) adder_2 (.a(EX_PC), .b(32'h4), .out(adder_2_out));  // open: cin, cout
  // Probe on WB_IR
  // Probe on EX_R1
  // Probe on id_ex_1_r2_2
  Shifter #(.width(32)) shifter_1 (.in(multiplexer_7_out), .\dist (5'b00010), .out(shifter_1_out));
  Multiplexer #(.width(32), .enable("false")) multiplexer_8 (
    .in0(id_ex_1_r2_2), .in1(multiplexer_7_out), .out(multiplexer_8_out), .sel(id_ex_1_alusrc_2));
  Adder #(.width(32)) adder_3 (.a(shifter_1_out), .b(adder_2_out), .out(adder_3_out));  // open: cin, cout
  MIPS_ALU mips_alu_1 (
    .X(EX_R1), .Y(multiplexer_8_out), .AluOP(id_ex_1_aluop_2), .Equal(mips_alu_1_equal),
    .Result(mips_alu_1_result), .Result_2(mips_alu_1_result_2), .shamt(id_ex_1_shamt_2));
  or or_6 (or_6_out[1], EX_B, EX_JR);
  Multiplexer #(.enable("false")) multiplexer_9 (
    .in0(mips_alu_1_equal), .in1(mips_alu_1_result[0]), .out(EX_Equal), .sel(BGEZ));
  Multiplexer #(.select(2), .width(32), .enable("false")) multiplexer_10 (
    .in0({32{1'b0}}), .in1({adder_2_out[31:28], id_ex_1_imm26_2, 2'b00}), .in2(adder_3_out), .in3(EX_R1),
    .out(multiplexer_10_out), .sel({or_6_out[1], EX_JMP}));
  Counter #(.width(16), .max('hffff)) counter_2 (
    .count(EX_JMP), .Q(\无条件分支数 ), .clk(CLK), .clr(RST));  // open: load, D, carry
  EX_MEM ex_mem_1 (
    .CLK(CLK), .reset(1'b0), .en(halt), .PC(EX_PC), .Result1(mips_alu_1_result), .IR(EX_IR),
    .R2(id_ex_1_r2_2), .LBU(id_ex_1_lbu_2), .MemToReg(id_ex_1_memtoreg_2), .MemWrite(id_ex_1_memwrite_2),
    .AluOP(id_ex_1_aluop_2), .RegWrite(EX_RegWrite), .JAL(id_ex_1_jal_2), .Syscall(EX_SYSCALL),
    .PC_2(MEM_PC), .Result1_2(ex_mem_1_result1_2), .IR_2(MEM_IR), .R2_2(ex_mem_1_r2_2),
    .LBU_2(ex_mem_1_lbu_2), .MemToReg_2(ex_mem_1_memtoreg_2), .MemWrite_2(MemWrite),
    .RegWrite_2(MEM_RegWrite), .JAL_2(ex_mem_1_jal_2), .Syscall_2(MEM_SYSCALL),
    .Result2(mips_alu_1_result_2), .R1(EX_R1), .R1_2(MEM_R1), .W_num(EX_WriteReg_num),
    .W_num_2(MEM_WriteReg_num), .\传输状态In_表明当前传输数据有效 (EX_Valid),
    .\传输状态Out_表明当前传输数据有效 (\ex_mem_1_传输状态out_表明当前传输数据有效 ));  // open: SignedExt, JR, JMP, SV, BGEZ, BEQ, BNE, AluSrc, RegDst, SignedExt_2, JR_2, JMP_2, SV_2, BGEZ_2, BEQ_2, BNE_2, AluOP_2, AluSrc_2, RegDst_2, Result2_2, EPC, EPC_2
  // Probe on MEM_R1
  // Probe on ex_mem_1_r2_2
  and and_3 (and_3_out, BEQ, EX_Equal);
  and and_4 (and_4_out, BNE, not_6_out);
  not not_6 (not_6_out, EX_Equal);
  RAM #(.addrWidth(10), .dataWidth(32), .bus("separate")) ram_1 (
    .addr(ex_mem_1_result1_2[11:2]), .din(ex_mem_1_r2_2), .data(ram_1_data), .str(MemWrite), .clk(CLK),
    .clr(RST));  // open: sel, ld
  or or_7 (EX_B_en, and_4_out, and_3_out, and_5_out);
  and and_5 (and_5_out, not_6_out, BGEZ);
  MEM_WB mem_wb_1 (
    .CLK(CLK), .reset(1'b0), .en(halt), .PC(MEM_PC), .Result1(ex_mem_1_result1_2), .IR(MEM_IR),
    .Dout(ram_1_data), .LBU(ex_mem_1_lbu_2), .MemToReg(ex_mem_1_memtoreg_2), .RegWrite(MEM_RegWrite),
    .JAL(ex_mem_1_jal_2), .Syscall(MEM_SYSCALL), .PC_2(WB_PC), .Result1_2(mem_wb_1_result1_2), .IR_2(WB_IR),
    .Dout_2(mem_wb_1_dout_2), .LBU_2(mem_wb_1_lbu_2), .MemToReg_2(mem_wb_1_memtoreg_2),
    .RegWrite_2(RegWrite), .JAL_2(mem_wb_1_jal_2), .Syscall_2(WB_Syscall), .R1(MEM_R1), .R1_2(R1),
    .R2(ex_mem_1_r2_2), .R2_2(R2), .W_num(MEM_WriteReg_num), .W_num_2(W_num),
    .\传输状态In_表明当前传输数据有效 (\ex_mem_1_传输状态out_表明当前传输数据有效 ), .\传输状态Out_表明当前传输数据有效 (WB_Valid));  // open: SignedExt, JR, JMP, SV, BGEZ, BEQ, BNE, MemWrite, AluOP, AluSrc, RegDst, SignedExt_2, JR_2, JMP_2, SV_2, BGEZ_2, BEQ_2, BNE_2, MemWrite_2, AluOP_2, AluSrc_2, RegDst_2, EPC, EPC_2
  Counter #(.width(16), .max('hffff)) counter_3 (
    .count(EX_B_en), .Q(\条件分支成功数 ), .clk(CLK), .clr(RST));  // open: load, D, carry
  Multiplexer #(.select(2), .width(8), .enable("false")) multiplexer_11 (
    .in0(mem_wb_1_dout_2[7:0]), .in1(mem_wb_1_dout_2[15:8]), .in2(mem_wb_1_dout_2[23:16]),
    .in3(mem_wb_1_dout_2[31:24]), .out(multiplexer_11_out), .sel(mem_wb_1_result1_2[1:0]));
  // Probe on R1
  // Probe on R2
  Multiplexer #(.width(32), .enable("false")) multiplexer_12 (
    .in0(mem_wb_1_result1_2), .in1(multiplexer_13_out), .out(multiplexer_12_out), .sel(mem_wb_1_memtoreg_2));
  Multiplexer #(.width(32), .enable("false")) multiplexer_13 (
    .in0(mem_wb_1_dout_2), .in1({{24{1'b0}}, multiplexer_11_out}), .out(multiplexer_13_out),
    .sel(mem_wb_1_lbu_2));
  // Probe on multiplexer_13_out
  Comparator #(.width(32)) comparator_1 (.a(R1), .b(32'h22), .eq(comparator_1_eq));  // open: gt, lt
  not not_7 (not_7_out, halt);
  Adder #(.width(32)) adder_4 (.a(WB_PC), .b(32'h4), .out(adder_4_out));  // open: cin, cout
  and and_6 (show, comparator_1_eq, WB_Syscall);
  and and_7 (and_7_out, WB_Syscall, not_8_out);
  not not_8 (not_8_out, comparator_1_eq);
  Register #(.width(32)) register_1 (.D(R2), .en(show), .Q(LedData), .clk(CLK), .clr(RST));
  Counter #(.width(16), .max('hffff)) counter_4 (
    .count(not_7_out), .Q(\总周期数 ), .clk(CLK), .clr(RST));  // open: load, D, carry
  Multiplexer #(.width(32), .enable("false")) multiplexer_14 (
    .in0(multiplexer_12_out), .in1(adder_4_out), .out(Din), .sel(mem_wb_1_jal_2));
  // Probe on Din
  Multiplexer #(.enable("false")) multiplexer_15 (.in0(and_7_out), .in1(1'b0), .out(halt), .sel(Go));

  // Notes on the sheet:
  //   中断源
  //   中断等待指示
  //   数码管输出
  //   指令存储器
  //   contents of rom_1 (hex, n*v repeats v):
  //   20110001 8000c05 20110001 20120002 20130003 8000c09 20110001 20120002 20130003 8000c0d 20110001
  //   20120002 20130003 8000c11 20110001 20120002 20130003 c000cfc 20100001 20110001 118fc0 112020
  //   20020022 c 118882 12200001 8000c15 112020 20020022 c 20110001 118880 112020 20020022 c 12200001
  //   8000c1f 20110001 118fc0 112020 20020022 c 1188c3 112020 20020022 c 118903 112020 20020022 c 118903
  //   112020 20020022 c 118903 112020 20020022 c 118903 112020 20020022 c 118903 112020 20020022 c 118903
  //   112020 20020022 c 118903 112020 20020022 c 20100001 109fc0 139fc3 8021 2012000c 24160003 26100001
  //   3210000f 20080008 20090001 139900 2709825 132020 20020022 c 1094022 1500fff9 22100001 2018000f
  //   2188024 108700 20080008 20090001 139902 2709825 132021 20020022 c 1094022 1500fff9 108702 2c9b022
  //   12c00001 8000c50 4020 1084027 84400 3508ffff 82021 20020022 c 2010ffff 20110000 ae300000 22100001
  //   22310004 ae300000 22100001 22310004 ae300000 22100001 22310004 ae300000 22100001 22310004 ae300000
  //   22100001 22310004 ae300000 22100001 22310004 ae300000 22100001 22310004 ae300000 22100001 22310004
  //   ae300000 22100001 22310004 ae300000 22100001 22310004 ae300000 22100001 22310004 ae300000 22100001
  //   22310004 ae300000 22100001 22310004 ae300000 22100001 22310004 ae300000 22100001 22310004 ae300000
  //   22100001 22310004 22100001 8020 2011003c 8e130000 8e340000 274402a 11000002 ae330000 ae140000
  //   2231fffc 1611fff8 102020 20020022 c 22100004 2011003c 1611fff2 20020032 c 20080001 20090003 20110876
  //   118d00 112020 20020022 c 200b0008 1118806 1318806 112020 20020022 c 216bffff 1560fff9 2002000a c
  //   20080001 20090003 20110876 118d00 112020 20020022 c 200b0008 1118807 1318807 112020 20020022 c
  //   216bffff 1560fff9 2002000a c 20090000 200b0010 34118483 20120404 118c00 129400 36318281 22520404
  //   ad310000 2328820 21290004 216bffff 1560fffb 200b0020 20090000 91310000 112020 20020022 c 21290001
  //   216bffff 1560fff9 2002000a c 2011000f 112020 20020022 c 2231ffff 621fffb 2002000a c 2002000a c
  //   20100000 22100001 102020 20020022 c 22100002 102020 20020022 c 22100003 102020 20020022 c 22100004
  //   102020 20020022 c 22100005 102020 20020022 c 22100006 102020 20020022 c 22100007 102020 20020022 c
  //   22100008 102020 20020022 20020022 c 3e00008
  //   OP
  //   rs
  //   指令字
  //   rt
  //   rd
  //   shamt
  //   imm16
  //   JMP
  //   JR
  //   Func
  //   imm26
  //   Beq
  //   Bne
  //   OP
  //   JAL
  //   Func
  //   Syscall
  //   MemToReg
  //   MemWrite
  //   AluOP
  //   AluSrcB
  //   RegWrite
  //   RegDst
  //   流水调试日志用
endmodule

module \重定向流水线  (
);

  wire and_3_out, and_4_out, and_5_out, and_7_out, and_8_out, BEQ, BGEZ, BNE, CLK, comparator_1_eq, EX_B,
       EX_B_en, EX_Branch, EX_Equal, EX_JMP, EX_JR, ex_mem_1_jal_2, ex_mem_1_lbu_2, ex_mem_1_memtoreg_2,
       \ex_mem_1_传输状态out_表明当前传输数据有效 , EX_MemToReg, EX_RegWrite, EX_SYSCALL, EX_Valid, \EX_跳转指令 , Go, halt,
       hit, id_ex_1_alusrc_2, id_ex_1_jal_2, id_ex_1_lbu_2, id_ex_1_memwrite_2, \ID_跳转指令 ,
       \if_id_1_传输状态out_表明当前传输数据有效 , IR1, IR2, IR3, \LoadUse数据相关 , MEM_RegWrite, MEM_SYSCALL, mem_wb_1_jal_2,
       mem_wb_1_lbu_2, mem_wb_1_memtoreg_2, MemWrite, mips_alu_1_equal, not_1_out, not_2_out, not_3_out,
       not_4_out, not_5_out, not_6_out, not_7_out, not_8_out, or_1_out, or_2_out, or_4_out, PC_en,
       predict_clk, predict_fail, predict_suc, RST, show, SignedExt, SV, W1, W2, W3, WB_RegWrite, WB_Syscall,
       WB_Valid, \数据相关检测_1_数据相关 , \硬布线控制器_1_alu_src , \硬布线控制器_1_beq , \硬布线控制器_1_bgez , \硬布线控制器_1_bne ,
       \硬布线控制器_1_jal , \硬布线控制器_1_jmp , \硬布线控制器_1_jr , \硬布线控制器_1_lbu , \硬布线控制器_1_memtoreg ,
       \硬布线控制器_1_memwrite , \硬布线控制器_1_regdst , \硬布线控制器_1_regwrite , \硬布线控制器_1_signedext , \硬布线控制器_1_syscall ;
  wire [1:1] or_7_out;
  wire [3:0] id_ex_1_aluop_2, \硬布线控制器_1_alu_op ;
  wire [4:0] EX_R1_num, EX_R2_num, EX_WriteReg_num, id_ex_1_shamt_2, ID_R1_num, ID_R2_num, MEM_WriteReg_num,
       multiplexer_6_out, multiplexer_7_out, multiplexer_8_out, WB_WriteReg_num;
  wire [5:0] FUNC, OP_CODE;
  wire [7:0] multiplexer_14_out;
  wire [15:0] id_ex_1_imm16_2, \LoadUse次数 , \总周期数 , \插入气泡数 , \无条件分支数 , \条件分支成功数 , \预测跳转失败 , \预测跳转成功 ;
  wire [25:0] id_ex_1_imm26_2;
  wire [25:6] if_id_1_ir_3;
  wire [31:0] adder_3_out, adder_4_out, bit_extender_1_out, bit_extender_2_out, Din, EX_IR, ex_mem_1_r2_2,
       EX_NewPC, EX_PC, EX_PC_4, EX_R1, EX_R2, ID_IR, ID_PC, ID_R1, IF_IR, IF_PC, IF_PC_4, LedData, MEM_Addr,
       MEM_IR, MEM_PC, MEM_R1, mem_wb_1_dout_2, mem_wb_1_result1_2, mips_alu_1_result, mips_alu_1_result_2,
       mips_regifile_1_r2, multiplexer_1_out, multiplexer_3_out, multiplexer_9_out, multiplexer_10_out,
       multiplexer_15_out, multiplexer_16_out, NewPC, Ori_EX_R1, Ori_EX_R2, R1, R2, ram_1_data,
       shifter_1_out, WB_IR, WB_PC, \目标PC ;

  Button \u_总复位  (.out(RST));
  Button _1 (.out(IR1));
  Button _2 (.out(IR2));
  Button _3 (.out(IR3));
  Button \u_继续运行  (.out(Go));
  LED led_1 (.in(W1));
  LED led_2 (.in(W2));
  LED led_3 (.in(W3));
  Multiplexer #(.width(32), .enable("false")) multiplexer_1 (
    .in0(IF_PC_4), .in1(\目标PC ), .out(multiplexer_1_out), .sel(hit));
  Hex_Digit_Display hex_digit_display_1 (.value(LedData[31:28]));  // open: dp
  not not_1 (not_1_out, halt);
  or or_1 (or_1_out, not_1_out, Go);
  Multiplexer #(.width(32), .enable("false")) multiplexer_2 (.in0(IF_PC_4), .in1(NewPC), .sel(EX_Branch));  // open: out
  Hex_Digit_Display hex_digit_display_2 (.value(LedData[23:20]));  // open: dp
  Hex_Digit_Display hex_digit_display_3 (.value(LedData[27:24]));  // open: dp
  Multiplexer #(.width(32), .enable("false")) multiplexer_3 (
    .in0(multiplexer_1_out), .in1(NewPC), .out(multiplexer_3_out), .sel(predict_clk));
  Hex_Digit_Display hex_digit_display_4 (.value(LedData[15:12]));  // open: dp
  Hex_Digit_Display hex_digit_display_5 (.value(LedData[19:16]));  // open: dp
  and and_1 (PC_en, or_1_out, not_2_out);
  not not_2 (not_2_out, \LoadUse数据相关 );
  Adder #(.width(32)) adder_1 (.a(IF_PC), .b(32'h4), .out(IF_PC_4));  // open: cin, cout
  Hex_Digit_Display hex_digit_display_6 (.value(LedData[7:4]));  // open: dp
  Hex_Digit_Display hex_digit_display_7 (.value(LedData[11:8]));  // open: dp
  Clock clock_1 (.out(CLK));
  Register #(.width(32)) PC (.D(multiplexer_3_out), .en(PC_en), .Q(IF_PC), .clk(CLK), .clr(RST));
  ROM #(.addrWidth(10), .dataWidth(32)) rom_1 (.addr(IF_PC[11:2]), .data(IF_IR));  // open: sel
  Hex_Digit_Display hex_digit_display_8 (.value(LedData[3:0]));  // open: dp
  or or_2 (or_2_out, predict_clk, RST);
  not not_3 (not_3_out, PC_en);
  IF_ID if_id_1 (
    .CLK(CLK), .reset(or_2_out), .en(not_3_out), .PC(IF_PC), .IR(IF_IR), .PC_2(ID_PC), .IR_2(ID_IR),
    .IR_3({OP_CODE, if_id_1_ir_3, FUNC}), .\传输状态In_表明当前传输数据有效 (1'b1),
    .\传输状态Out_表明当前传输数据有效 (\if_id_1_传输状态out_表明当前传输数据有效 ));
  // Probe on \总周期数 
  // Probe on \无条件分支数 
  // Probe on \条件分支成功数 
  // Probe on \插入气泡数 
  // Probe on \LoadUse次数 
  // Probe on \预测跳转成功 
  // Probe on \预测跳转失败 
  // Probe on IF_PC[11:0]
  \硬布线控制器  \u_硬布线控制器_1  (
    .Func(FUNC), .OP(OP_CODE), .ALU_OP(\硬布线控制器_1_alu_op ), .MemToReg(\硬布线控制器_1_memtoreg ),
    .MemWrite(\硬布线控制器_1_memwrite ), .ALU_SRC(\硬布线控制器_1_alu_src ), .RegWrite(\硬布线控制器_1_regwrite ),
    .SysCALL(\硬布线控制器_1_syscall ), .SignedExt(\硬布线控制器_1_signedext ), .RegDst(\硬布线控制器_1_regdst ),
    .JR(\硬布线控制器_1_jr ), .JMP(\硬布线控制器_1_jmp ), .Beq(\硬布线控制器_1_beq ), .JAL(\硬布线控制器_1_jal ),
    .Bne(\硬布线控制器_1_bne ), .SV(SV), .BGEZ(\硬布线控制器_1_bgez ), .LBU(\硬布线控制器_1_lbu ));
  Multiplexer #(.width(5), .enable("false")) multiplexer_4 (
    .in0(if_id_1_ir_3[25:21]), .in1(5'b00010), .out(ID_R1_num), .sel(\硬布线控制器_1_syscall ));
  // Probe on ID_PC[11:0]
  or or_3 (\ID_跳转指令 , \硬布线控制器_1_jr , \硬布线控制器_1_jmp , \硬布线控制器_1_bgez , \硬布线控制器_1_beq , \硬布线控制器_1_bne );
  Multiplexer #(.width(5), .enable("false")) multiplexer_5 (
    .in0(if_id_1_ir_3[20:16]), .in1(5'b00100), .out(ID_R2_num), .sel(\硬布线控制器_1_syscall ));
  Multiplexer #(.width(5), .enable("false")) multiplexer_6 (
    .in0(if_id_1_ir_3[20:16]), .in1(if_id_1_ir_3[15:11]), .out(multiplexer_6_out), .sel(\硬布线控制器_1_regdst ));
  \数据相关检测  \u_数据相关检测_1  (
    .OP(OP_CODE), .EX_WriteReg_num(EX_WriteReg_num), .EX_RegWrite(EX_RegWrite), .MEM_WriteReg_num({5{1'b0}}),
    .MEM_RegWrite(1'b0), .\数据相关 (\数据相关检测_1_数据相关 ), .Func(FUNC), .ID_R1_num(ID_R1_num), .ID_R2_num(ID_R2_num));
  // Probe on MEM_PC[11:0]
  // Probe on EX_PC[11:0]
  Multiplexer #(.width(5), .enable("false")) multiplexer_7 (
    .in0(multiplexer_6_out), .in1({5{1'b1}}), .out(multiplexer_7_out), .sel(\硬布线控制器_1_jal ));
  // Probe on WB_PC[11:0]
  Multiplexer #(.width(5), .enable("false")) multiplexer_8 (
    .in0(if_id_1_ir_3[10:6]), .in1(ID_R1[4:0]), .out(multiplexer_8_out), .sel(SV));
  and and_2 (\LoadUse数据相关 , EX_MemToReg, \数据相关检测_1_数据相关 );
  // Probe on IF_IR
  not not_4 (not_4_out, PC_en);
  // Probe on ID_R1
  MIPS_Regifile mips_regifile_1 (
    .Din(Din), .Clk(CLK), .R1(ID_R1), .R2(mips_regifile_1_r2), .WE(WB_RegWrite), .W_num(WB_WriteReg_num),
    .R1_num(ID_R1_num), .R2_num(ID_R2_num));
  // Probe on mips_regifile_1_r2
  // Probe on ID_IR
  or or_4 (or_4_out, predict_clk, not_4_out, RST);
  // Probe on EX_IR
  ID_EX id_ex_1 (
    .CLK(CLK), .reset(or_4_out), .en(halt), .PC(ID_PC), .R1(ID_R1), .IR(ID_IR), .R2(mips_regifile_1_r2),
    .SignedExt(\硬布线控制器_1_signedext ), .shamt(multiplexer_8_out), .JR(\硬布线控制器_1_jr ),
    .imm16({if_id_1_ir_3[15:6], FUNC}), .JMP(\硬布线控制器_1_jmp ), .LBU(\硬布线控制器_1_lbu ), .BGEZ(\硬布线控制器_1_bgez ),
    .BEQ(\硬布线控制器_1_beq ), .BNE(\硬布线控制器_1_bne ), .MemToReg(\硬布线控制器_1_memtoreg ),
    .MemWrite(\硬布线控制器_1_memwrite ), .AluOP(\硬布线控制器_1_alu_op ), .AluSrc(\硬布线控制器_1_alu_src ),
    .RegWrite(\硬布线控制器_1_regwrite ), .JAL(\硬布线控制器_1_jal ), .Syscall(\硬布线控制器_1_syscall ), .PC_2(EX_PC),
    .R1_2(Ori_EX_R1), .IR_2(EX_IR), .R2_2(Ori_EX_R2), .SignedExt_2(SignedExt), .shamt_2(id_ex_1_shamt_2),
    .JR_2(EX_JR), .imm16_2(id_ex_1_imm16_2), .JMP_2(EX_JMP), .LBU_2(id_ex_1_lbu_2), .BGEZ_2(BGEZ),
    .BEQ_2(BEQ), .BNE_2(BNE), .MemToReg_2(EX_MemToReg), .MemWrite_2(id_ex_1_memwrite_2),
    .AluOP_2(id_ex_1_aluop_2), .AluSrc_2(id_ex_1_alusrc_2), .RegWrite_2(EX_RegWrite), .JAL_2(id_ex_1_jal_2),
    .Syscall_2(EX_SYSCALL), .imm26({if_id_1_ir_3, FUNC}), .imm26_2(id_ex_1_imm26_2),
    .W_num(multiplexer_7_out), .W_num_2(EX_WriteReg_num), .\传输状态In_表明当前传输数据有效 (\if_id_1_传输状态out_表明当前传输数据有效 ),
    .\传输状态Out_表明当前传输数据有效 (EX_Valid), .ID_R1_num(ID_R1_num), .ID_R1_num_2(EX_R1_num), .ID_R2_num(ID_R2_num),
    .ID_R2_num_2(EX_R2_num));  // open: SV, RegDst, SV_2, RegDst_2
  or or_5 (EX_B, BNE, BEQ, BGEZ);
  // Probe on MEM_IR
  \分支预测  \u_分支预测_1  (
    .hit(hit), .EX_Branch(EX_Branch), .predict_suc(predict_suc), .\目标PC (\目标PC ), .\EX_跳转指令 (\EX_跳转指令 ),
    .predict_fail(predict_fail), .\ID_跳转指令 (\ID_跳转指令 ), .ID_PC(ID_PC), .CLK(CLK), .EX_PC(EX_PC),
    .EX_NewPC(EX_NewPC), .predict_clk(predict_clk), .NewPC(NewPC), .IF_PC(IF_PC));
  or or_6 (EX_Branch, EX_JR, EX_JMP, EX_B_en);
  assign bit_extender_1_out = {{16{id_ex_1_imm16_2[15]}}, id_ex_1_imm16_2};  // Bit_Extender bit_extender_1
  assign bit_extender_2_out = {{16{1'b0}}, id_ex_1_imm16_2};  // Bit_Extender bit_extender_2
  Adder #(.width(32)) adder_2 (.a(EX_PC), .b(32'h4), .out(EX_PC_4));  // open: cin, cout
  // Probe on WB_IR
  // Probe on \目标PC 
  Multiplexer #(.width(32), .enable("false")) multiplexer_9 (
    .in0(bit_extender_2_out), .in1(bit_extender_1_out), .out(multiplexer_9_out), .sel(SignedExt));
  // Probe on EX_R2
  Shifter #(.width(32)) shifter_1 (.in(multiplexer_9_out), .\dist (5'b00010), .out(shifter_1_out));
  \重定向相关检测  \u_重定向相关检测_1  (
    .WB_WriteReg_num(WB_WriteReg_num), .WB_RegWrite(WB_RegWrite), .IR(EX_IR),
    .MEM_WriteReg_num(MEM_WriteReg_num), .MEM_RegWrite(MEM_RegWrite), .EX_R1_num(EX_R1_num),
    .EX_R2_num(EX_R2_num), .Din(Din), .MEM_Addr(MEM_Addr), .EX_R1(EX_R1), .Ori_EX_R1(Ori_EX_R1),
    .EX_R2(EX_R2), .Ori_EX_R2(Ori_EX_R2));
  Multiplexer #(.width(32), .enable("false")) multiplexer_10 (
    .in0(EX_R2), .in1(multiplexer_9_out), .out(multiplexer_10_out), .sel(id_ex_1_alusrc_2));
  Adder #(.width(32)) adder_3 (.a(shifter_1_out), .b(EX_PC_4), .out(adder_3_out));  // open: cin, cout
  MIPS_ALU mips_alu_1 (
    .X(EX_R1), .Y(multiplexer_10_out), .AluOP(id_ex_1_aluop_2), .Equal(mips_alu_1_equal),
    .Result(mips_alu_1_result), .Result_2(mips_alu_1_result_2), .shamt(id_ex_1_shamt_2));
  Multiplexer #(.select(2), .width(32), .enable("false")) multiplexer_11 (
    .in0({32{1'b0}}), .in1({EX_PC_4[31:28], id_ex_1_imm26_2, 2'b00}), .in2(adder_3_out), .in3(EX_R1),
    .out(EX_NewPC), .sel({or_7_out[1], EX_JMP}));
  or or_7 (or_7_out[1], EX_B, EX_JR);
  Multiplexer #(.enable("false")) multiplexer_12 (
    .in0(mips_alu_1_equal), .in1(mips_alu_1_result[0]), .out(EX_Equal), .sel(BGEZ));
  Multiplexer #(.width(32), .enable("false")) multiplexer_13 (
    .in0(EX_PC_4), .in1(EX_NewPC), .out(NewPC), .sel(EX_Branch));
  or or_8 (\EX_跳转指令 , EX_B, EX_JR, EX_JMP);
  EX_MEM ex_mem_1 (
    .CLK(CLK), .reset(RST), .en(halt), .PC(EX_PC), .Result1(mips_alu_1_result), .IR(EX_IR), .R2(EX_R2),
    .LBU(id_ex_1_lbu_2), .MemToReg(EX_MemToReg), .MemWrite(id_ex_1_memwrite_2), .AluOP(id_ex_1_aluop_2),
    .RegWrite(EX_RegWrite), .JAL(id_ex_1_jal_2), .Syscall(EX_SYSCALL), .PC_2(MEM_PC), .Result1_2(MEM_Addr),
    .IR_2(MEM_IR), .R2_2(ex_mem_1_r2_2), .LBU_2(ex_mem_1_lbu_2), .MemToReg_2(ex_mem_1_memtoreg_2),
    .MemWrite_2(MemWrite), .RegWrite_2(MEM_RegWrite), .JAL_2(ex_mem_1_jal_2), .Syscall_2(MEM_SYSCALL),
    .Result2(mips_alu_1_result_2), .R1(EX_R1), .R1_2(MEM_R1), .W_num(EX_WriteReg_num),
    .W_num_2(MEM_WriteReg_num), .\传输状态In_表明当前传输数据有效 (EX_Valid),
    .\传输状态Out_表明当前传输数据有效 (\ex_mem_1_传输状态out_表明当前传输数据有效 ));  // open: SignedExt, JR, JMP, SV, BGEZ, BEQ, BNE, AluSrc, RegDst, SignedExt_2, JR_2, JMP_2, SV_2, BGEZ_2, BEQ_2, BNE_2, AluOP_2, AluSrc_2, RegDst_2, Result2_2, EPC, EPC_2
  // Probe on MEM_R1
  // Probe on ex_mem_1_r2_2
  and and_3 (and_3_out, BEQ, EX_Equal);
  and and_4 (and_4_out, BNE, not_5_out);
  not not_5 (not_5_out, EX_Equal);
  or or_9 (EX_B_en, and_4_out, and_3_out, and_5_out);
  and and_5 (and_5_out, not_5_out, BGEZ);
  RAM #(.addrWidth(10), .dataWidth(32), .bus("separate")) ram_1 (
    .addr(MEM_Addr[11:2]), .din(ex_mem_1_r2_2), .data(ram_1_data), .str(MemWrite), .clk(CLK), .clr(RST));  // open: sel, ld
  MEM_WB mem_wb_1 (
    .CLK(CLK), .reset(RST), .en(halt), .PC(MEM_PC), .Result1(MEM_Addr), .IR(MEM_IR), .Dout(ram_1_data),
    .LBU(ex_mem_1_lbu_2), .MemToReg(ex_mem_1_memtoreg_2), .RegWrite(MEM_RegWrite), .JAL(ex_mem_1_jal_2),
    .Syscall(MEM_SYSCALL), .PC_2(WB_PC), .Result1_2(mem_wb_1_result1_2), .IR_2(WB_IR),
    .Dout_2(mem_wb_1_dout_2), .LBU_2(mem_wb_1_lbu_2), .MemToReg_2(mem_wb_1_memtoreg_2),
    .RegWrite_2(WB_RegWrite), .JAL_2(mem_wb_1_jal_2), .Syscall_2(WB_Syscall), .R1(MEM_R1), .R1_2(R1),
    .R2(ex_mem_1_r2_2), .R2_2(R2), .W_num(MEM_WriteReg_num), .W_num_2(WB_WriteReg_num),
    .\传输状态In_表明当前传输数据有效 (\ex_mem_1_传输状态out_表明当前传输数据有效 ), .\传输状态Out_表明当前传输数据有效 (WB_Valid));  // open: SignedExt, JR, JMP, SV, BGEZ, BEQ, BNE, MemWrite, AluOP, AluSrc, RegDst, SignedExt_2, JR_2, JMP_2, SV_2, BGEZ_2, BEQ_2, BNE_2, MemWrite_2, AluOP_2, AluSrc_2, RegDst_2, EPC, EPC_2
  Multiplexer #(.select(2), .width(8), .enable("false")) multiplexer_14 (
    .in0(mem_wb_1_dout_2[7:0]), .in1(mem_wb_1_dout_2[15:8]), .in2(mem_wb_1_dout_2[23:16]),
    .in3(mem_wb_1_dout_2[31:24]), .out(multiplexer_14_out), .sel(mem_wb_1_result1_2[1:0]));
  Multiplexer #(.width(32), .enable("false")) multiplexer_15 (
    .in0(mem_wb_1_result1_2), .in1(multiplexer_16_out), .out(multiplexer_15_out), .sel(mem_wb_1_memtoreg_2));
  Multiplexer #(.width(32), .enable("false")) multiplexer_16 (
    .in0(mem_wb_1_dout_2), .in1({{24{1'b0}}, multiplexer_14_out}), .out(multiplexer_16_out),
    .sel(mem_wb_1_lbu_2));
  // Probe on multiplexer_16_out
  Comparator #(.width(32)) comparator_1 (.a(R1), .b(32'h22), .eq(comparator_1_eq));  // open: gt, lt
  and and_6 (show, comparator_1_eq, WB_Syscall);
  and and_7 (and_7_out, WB_Syscall, not_6_out);
  not not_6 (not_6_out, comparator_1_eq);
  Register #(.width(32)) register_1 (.D(R2), .en(show), .Q(LedData), .clk(CLK), .clr(RST));
  Adder #(.width(32)) adder_4 (.a(WB_PC), .b(32'h4), .out(adder_4_out));  // open: cin, cout
  Multiplexer #(.enable("false")) multiplexer_17 (.in0(and_7_out), .in1(1'b0), .out(halt), .sel(Go));
  not not_7 (not_7_out, halt);
  not not_8 (not_8_out, halt);
  and and_8 (and_8_out, not_8_out, \LoadUse数据相关 );
  Multiplexer #(.width(32), .enable("false")) multiplexer_18 (
    .in0(multiplexer_15_out), .in1(adder_4_out), .out(Din), .sel(mem_wb_1_jal_2));
  // Probe on Din
  Counter #(.width(16), .max('hffff)) counter_1 (
    .count(EX_B_en), .Q(\条件分支成功数 ), .clk(CLK), .clr(RST));  // open: load, D, carry
  Counter #(.width(16), .max('hffff)) counter_2 (
    .count(EX_JMP), .Q(\无条件分支数 ), .clk(CLK), .clr(RST));  // open: load, D, carry
  Counter #(.width(16), .max('hffff)) counter_3 (
    .count(\LoadUse数据相关 ), .Q(\LoadUse次数 ), .clk(CLK), .clr(RST));  // open: load, D, carry
  Counter #(.width(16), .max('hffff)) counter_4 (
    .count(not_7_out), .Q(\总周期数 ), .clk(CLK), .clr(RST));  // open: load, D, carry
  Counter #(.width(16), .max('hffff)) counter_5 (
    .count(and_8_out), .Q(\插入气泡数 ), .clk(CLK), .clr(RST));  // open: load, D, carry
  Counter #(.width(16), .max('hffff)) counter_6 (
    .count(predict_suc), .Q(\预测跳转成功 ), .clk(CLK), .clr(RST));  // open: load, D, carry
  Counter #(.width(16), .max('hffff)) counter_7 (
    .count(predict_fail), .Q(\预测跳转失败 ), .clk(CLK), .clr(RST));  // open: load, D, carry

  // Notes on the sheet:
  //   中断源
  //   重定向流水线
  //   中断等待指示
  //   重定向流水线+分支预测
  //   数码管输出
  //   指令存储器
  //   contents of rom_1 (hex, n*v repeats v):
  //   20110001 8000c05 20110001 20120002 20130003 8000c09 20110001 20120002 20130003 8000c0d 20110001
  //   20120002 20130003 8000c11 20110001 20120002 20130003 c000cfc 20100001 20110001 118fc0 112020
  //   20020022 c 118882 12200001 8000c15 112020 20020022 c 20110001 118880 112020 20020022 c 12200001
  //   8000c1f 20110001 118fc0 112020 20020022 c 1188c3 112020 20020022 c 118903 112020 20020022 c 118903
  //   112020 20020022 c 118903 112020 20020022 c 118903 112020 20020022 c 118903 112020 20020022 c 118903
  //   112020 20020022 c 118903 112020 20020022 c 20100001 109fc0 139fc3 8021 2012000c 24160003 26100001
  //   3210000f 20080008 20090001 139900 2709825 132020 20020022 c 1094022 1500fff9 22100001 2018000f
  //   2188024 108700 20080008 20090001 139902 2709825 132021 20020022 c 1094022 1500fff9 108702 2c9b022
  //   12c00001 8000c50 4020 1084027 84400 3508ffff 82021 20020022 c 2010ffff 20110000 ae300000 22100001
  //   22310004 ae300000 22100001 22310004 ae300000 22100001 22310004 ae300000 22100001 22310004 ae300000
  //   22100001 22310004 ae300000 22100001 22310004 ae300000 22100001 22310004 ae300000 22100001 22310004
  //   ae300000 22100001 22310004 ae300000 22100001 22310004 ae300000 22100001 22310004 ae300000 22100001
  //   22310004 ae300000 22100001 22310004 ae300000 22100001 22310004 ae300000 22100001 22310004 ae300000
  //   22100001 22310004 22100001 8020 2011003c 8e130000 8e340000 274402a 11000002 ae330000 ae140000
  //   2231fffc 1611fff8 102020 20020022 c 22100004 2011003c 1611fff2 20020032 c 20080001 20090003 20110876
  //   118d00 112020 20020022 c 200b0008 1118806 1318806 112020 20020022 c 216bffff 1560fff9 2002000a c
  //   20080001 20090003 20110876 118d00 112020 20020022 c 200b0008 1118807 1318807 112020 20020022 c
  //   216bffff 1560fff9 2002000a c 20090000 200b0010 34118483 20120404 118c00 129400 36318281 22520404
  //   ad310000 2328820 21290004 216bffff 1560fffb 200b0020 20090000 91310000 112020 20020022 c 21290001
  //   216bffff 1560fff9 2002000a c 2011000f 112020 20020022 c 2231ffff 621fffb 2002000a c 2002000a c
  //   20100000 22100001 102020 20020022 c 22100002 102020 20020022 c 22100003 102020 20020022 c 22100004
  //   102020 20020022 c 22100005 102020 20020022 c 22100006 102020 20020022 c 22100007 102020 20020022 c
  //   22100008 102020 20020022 20020022 c 3e00008
  //   OP
  //   rs
  //   指令字
  //   rt
  //   rd
  //   shamt
  //   imm16
  //   JMP
  //   JR
  //   Func
  //   imm26
  //   Beq
  //   Bne
  //   OP
  //   JAL
  //   Func
  //   Syscall
  //   MemToReg
  //   MemWrite
  //   AluOP
  //   AluSrcB
  //   RegWrite
  //   RegDst
  //   流水调试日志用
endmodule

module \重定向相关检测  (
  input  [4:0] WB_WriteReg_num,
  input  WB_RegWrite,
  input  [31:0] IR,
  input  [4:0] MEM_WriteReg_num,
  input  MEM_RegWrite,
  input  [4:0] EX_R1_num,
  input  [4:0] EX_R2_num,
  input  [31:0] Din,
  input  [31:0] MEM_Addr,
  input  [31:0] Ori_EX_R1,
  input  [31:0] Ori_EX_R2,
  output [31:0] EX_R1,
  output [31:0] EX_R2
);

  wire comparator_1_eq, comparator_2_eq, comparator_3_eq, comparator_4_eq, comparator_5_eq, comparator_6_eq,
       comparator_7_eq, comparator_8_eq, not_1_out, not_2_out, not_3_out, not_4_out, R1_MEM, R1_WB, R2_MEM,
       R2_WB, \源寄存器使用情况_1_r1_used , \源寄存器使用情况_1_r2_used ;
  wire [31:0] multiplexer_1_out, multiplexer_2_out;

  \源寄存器使用情况  \u_源寄存器使用情况_1  (
    .OP0(IR[26]), .OP1(IR[27]), .OP2(IR[28]), .OP3(IR[29]), .OP4(IR[30]), .OP5(IR[31]), .F0(IR[0]),
    .F1(IR[1]), .F2(IR[2]), .F3(IR[3]), .F4(IR[4]), .F5(IR[5]), .R1_Used(\源寄存器使用情况_1_r1_used ),
    .R2_Used(\源寄存器使用情况_1_r2_used ));
  Comparator #(.width(5)) comparator_1 (.a(EX_R1_num), .b(WB_WriteReg_num), .eq(comparator_1_eq));  // open: gt, lt
  Comparator #(.width(5)) comparator_2 (.a(EX_R1_num), .b(MEM_WriteReg_num), .eq(comparator_2_eq));  // open: gt, lt
  Comparator #(.width(5)) comparator_3 (.a(EX_R2_num), .b(MEM_WriteReg_num), .eq(comparator_3_eq));  // open: gt, lt
  Comparator #(.width(5)) comparator_4 (.a(EX_R2_num), .b(WB_WriteReg_num), .eq(comparator_4_eq));  // open: gt, lt
  Comparator #(.width(5)) comparator_5 (.a(EX_R1_num), .b({5{1'b0}}), .eq(comparator_5_eq));  // open: gt, lt
  not not_1 (not_1_out, comparator_5_eq);
  not not_2 (not_2_out, comparator_6_eq);
  Comparator #(.width(5)) comparator_6 (.a(EX_R1_num), .b({5{1'b0}}), .eq(comparator_6_eq));  // open: gt, lt
  Comparator #(.width(5)) comparator_7 (.a(EX_R2_num), .b({5{1'b0}}), .eq(comparator_7_eq));  // open: gt, lt
  not not_3 (not_3_out, comparator_7_eq);
  Comparator #(.width(5)) comparator_8 (.a(EX_R2_num), .b({5{1'b0}}), .eq(comparator_8_eq));  // open: gt, lt
  not not_4 (not_4_out, comparator_8_eq);
  and and_1 (R1_WB, \源寄存器使用情况_1_r1_used , WB_RegWrite, comparator_1_eq, not_1_out);
  and and_2 (R1_MEM, \源寄存器使用情况_1_r1_used , MEM_RegWrite, comparator_2_eq, not_2_out);
  and and_3 (R2_MEM, \源寄存器使用情况_1_r2_used , MEM_RegWrite, comparator_3_eq, not_3_out);
  and and_4 (R2_WB, \源寄存器使用情况_1_r2_used , WB_RegWrite, comparator_4_eq, not_4_out);
  Multiplexer #(.width(32), .enable("false")) multiplexer_1 (
    .in0(Ori_EX_R1), .in1(Din), .out(multiplexer_1_out), .sel(R1_WB));
  Multiplexer #(.width(32), .enable("false")) multiplexer_2 (
    .in0(Ori_EX_R2), .in1(Din), .out(multiplexer_2_out), .sel(R2_WB));
  Multiplexer #(.width(32), .enable("false")) multiplexer_3 (
    .in0(multiplexer_1_out), .in1(MEM_Addr), .out(EX_R1), .sel(R1_MEM));
  Multiplexer #(.width(32), .enable("false")) multiplexer_4 (
    .in0(multiplexer_2_out), .in1(MEM_Addr), .out(EX_R2), .sel(R2_MEM));

  // Notes on the sheet:
  //   OP
  //   Func
endmodule

// Cache
module \Cache_全相连  (
  input  [31:0] BlockDataIn,
  input  [31:0] EX_PC,
  input  CLK,
  input  [31:0] IF_PC,
  input  BlkDataReady,
  input  EX_Branch,
  output hit,
  output [31:0] \目标地址 ,
  output [1:0] state
);

  wire and_2_out, comparator_1_eq, comparator_2_eq, comparator_3_eq, comparator_4_eq, comparator_5_eq,
       comparator_6_eq, comparator_7_eq, comparator_8_eq, comparator_9_gt, comparator_10_eq,
       comparator_11_eq, comparator_12_eq, comparator_13_eq, comparator_14_eq, comparator_15_eq,
       comparator_16_eq, comparator_17_eq, decoder_1_out0, decoder_1_out1, decoder_1_out2, decoder_1_out3,
       decoder_1_out4, decoder_1_out5, decoder_1_out6, decoder_1_out7, EX_Hit, EX_Miss, FULL, Hit_t, L0, L1,
       L2, L3, L4, L5, L6, L7, Miss, not_1_out, not_2_out, not_3_out, not_4_out, not_5_out, not_6_out,
       not_7_out, not_8_out, not_9_out, S0, S1, S2, S3, S4, S5, S6, S7, Set0, Set1, Set2, Set3, Set4, Set5,
       Set6, Set7, V0, V1, V2, V3, V4, V5, V6, V7;
  wire [1:0] fsm_1_next_state, fsm_2_next_state, fsm_3_next_state, fsm_4_next_state, fsm_5_next_state,
       fsm_6_next_state, fsm_7_next_state, fsm_8_next_state, multiplexer_2_out, multiplexer_3_out,
       multiplexer_4_out, multiplexer_5_out, multiplexer_6_out, multiplexer_7_out, state0, state1, state2,
       state3, state4, state5, state6, state7;
  wire [2:0] MAX, max3_1_max_num, max3_2_max_num, max3_3_max_num, max3_4_max_num, max3_5_max_num,
       max3_6_max_num, multiplexer_1_out, priority_encoder_1_out;
  wire [15:0] C0, C1, C2, C3, C4, C5, C6, C7, max3_1_max, max3_2_max, max3_3_max, max3_4_max, max3_5_max,
       max3_6_max;
  wire [31:0] register_5_q, register_6_q, register_7_q, register_8_q, register_13_q, register_14_q,
       register_15_q, register_16_q, Tag0, Tag1, Tag2, Tag3, Tag4, Tag5, Tag6, Tag7;

  Max3 max3_1 (.Y(C6), .X(C7), .Y_num(3'b110), .X_num(3'b111), .MAX(max3_1_max), .Max_num(max3_1_max_num));
  Max3 max3_2 (.Y(C4), .X(C5), .Y_num(3'b100), .X_num(3'b101), .MAX(max3_2_max), .Max_num(max3_2_max_num));
  Max3 max3_3 (.Y(C2), .X(C3), .Y_num(3'b010), .X_num(3'b011), .MAX(max3_3_max), .Max_num(max3_3_max_num));
  Max3 max3_4 (.Y(C0), .X(C1), .Y_num(3'b000), .X_num(3'b001), .MAX(max3_4_max), .Max_num(max3_4_max_num));
  not not_1 (not_1_out, V1);
  not not_2 (not_2_out, V3);
  not not_3 (not_3_out, V5);
  not not_4 (not_4_out, V7);
  Register #(.width(1)) VALID (.D(1'b1), .en(Set0), .Q(V0), .clk(CLK));  // open: clr
  Register #(.width(1)) VALID_2 (.D(1'b1), .en(Set1), .Q(V1), .clk(CLK));  // open: clr
  Register #(.width(1)) VALID_3 (.D(1'b1), .en(Set2), .Q(V2), .clk(CLK));  // open: clr
  Register #(.width(1)) VALID_4 (.D(1'b1), .en(Set3), .Q(V3), .clk(CLK));  // open: clr
  and and_1 (FULL, V0, V1, V2, V3, V4, V5, V6, V7);
  not not_5 (not_5_out, V0);
  not not_6 (not_6_out, V2);
  Priority_Encoder priority_encoder_1 (
    .in0(not_5_out), .in1(not_1_out), .in2(not_6_out), .in3(not_2_out), .in4(not_7_out), .in5(not_3_out),
    .in6(not_8_out), .in7(not_4_out), .out(priority_encoder_1_out), .en_in(1'b1));  // open: gs, en_out
  not not_7 (not_7_out, V4);
  not not_8 (not_8_out, V6);
  Register #(.width(32)) \u_标记位  (.D(EX_PC), .en(Set0), .Q(Tag0), .clk(CLK));  // open: clr
  Register #(.width(32)) \u_标记位_2  (.D(EX_PC), .en(Set1), .Q(Tag1), .clk(CLK));  // open: clr
  Register #(.width(32)) \u_标记位_3  (.D(EX_PC), .en(Set2), .Q(Tag2), .clk(CLK));  // open: clr
  Register #(.width(32)) \u_标记位_4  (.D(EX_PC), .en(Set3), .Q(Tag3), .clk(CLK));  // open: clr
  Max3 max3_5 (
    .Y(max3_2_max), .X(max3_1_max), .Y_num(max3_2_max_num), .X_num(max3_1_max_num), .MAX(max3_5_max),
    .Max_num(max3_5_max_num));
  Max3 max3_6 (
    .Y(max3_4_max), .X(max3_3_max), .Y_num(max3_4_max_num), .X_num(max3_3_max_num), .MAX(max3_6_max),
    .Max_num(max3_6_max_num));
  Max3 max3_7 (
    .Y(max3_6_max), .X(max3_5_max), .Y_num(max3_6_max_num), .X_num(max3_5_max_num), .Max_num(MAX));  // open: MAX
  // Probe on MAX
  Decoder #(.select(3), .enable("false")) decoder_1 (
    .out0(decoder_1_out0), .out1(decoder_1_out1), .out2(decoder_1_out2), .out3(decoder_1_out3),
    .out4(decoder_1_out4), .out5(decoder_1_out5), .out6(decoder_1_out6), .out7(decoder_1_out7),
    .sel(multiplexer_1_out));
  Multiplexer #(.width(3), .enable("false")) multiplexer_1 (
    .in0(priority_encoder_1_out), .in1(MAX), .out(multiplexer_1_out), .sel(FULL));
  // Probe on multiplexer_1_out
  Counter #(.width(16), .max('hffff)) \u_淘汰标志位  (.count(Hit_t), .Q(C0), .clk(CLK), .clr(L0));  // open: load, D, carry
  Counter #(.width(16), .max('hffff)) \u_淘汰标志位_2  (.count(Hit_t), .Q(C1), .clk(CLK), .clr(L1));  // open: load, D, carry
  Counter #(.width(16), .max('hffff)) \u_淘汰标志位_3  (.count(Hit_t), .Q(C2), .clk(CLK), .clr(L2));  // open: load, D, carry
  Counter #(.width(16), .max('hffff)) \u_淘汰标志位_4  (.count(Hit_t), .Q(C3), .clk(CLK), .clr(L3));  // open: load, D, carry
  FSM fsm_1 (.state(state0), .JUMP(EX_Branch), .next_state(fsm_1_next_state));
  FSM fsm_2 (.state(state1), .JUMP(EX_Branch), .next_state(fsm_2_next_state));
  FSM fsm_3 (.state(state2), .JUMP(EX_Branch), .next_state(fsm_3_next_state));
  FSM fsm_4 (.state(state3), .JUMP(EX_Branch), .next_state(fsm_4_next_state));
  and and_2 (and_2_out, not_9_out, BlkDataReady);
  not not_9 (not_9_out, EX_Hit);
  Register #(.width(2)) register_1 (.D(fsm_1_next_state), .en(S0), .Q(state0), .clk(CLK), .clr(Set0));
  Register #(.width(2)) register_2 (.D(fsm_2_next_state), .en(S1), .Q(state1), .clk(CLK), .clr(Set1));
  Register #(.width(2)) register_3 (.D(fsm_3_next_state), .en(S2), .Q(state2), .clk(CLK), .clr(Set2));
  Register #(.width(2)) register_4 (.D(fsm_4_next_state), .en(S3), .Q(state3), .clk(CLK), .clr(Set3));
  and and_3 (Set0, decoder_1_out0, and_2_out);
  and and_4 (Set1, decoder_1_out1, and_2_out);
  and and_5 (Set2, decoder_1_out2, and_2_out);
  and and_6 (Set3, decoder_1_out3, and_2_out);
  and and_7 (Set4, decoder_1_out4, and_2_out);
  and and_8 (Set5, decoder_1_out5, and_2_out);
  and and_9 (Set6, decoder_1_out6, and_2_out);
  and and_10 (Set7, decoder_1_out7, and_2_out);
  Register #(.width(32)) register_5 (.D(BlockDataIn), .en(Set0), .Q(register_5_q), .clk(CLK));  // open: clr
  Register #(.width(32)) register_6 (.D(BlockDataIn), .en(Set1), .Q(register_6_q), .clk(CLK));  // open: clr
  Register #(.width(32)) register_7 (.D(BlockDataIn), .en(Set2), .Q(register_7_q), .clk(CLK));  // open: clr
  Register #(.width(32)) register_8 (.D(BlockDataIn), .en(Set3), .Q(register_8_q), .clk(CLK));  // open: clr
  assign \目标地址  = L0 ? register_5_q : 32'bz;  // Controlled_Buffer controlled_buffer_1
  assign \目标地址  = L1 ? register_6_q : 32'bz;  // Controlled_Buffer controlled_buffer_2
  assign \目标地址  = L2 ? register_7_q : 32'bz;  // Controlled_Buffer controlled_buffer_3
  assign \目标地址  = L3 ? register_8_q : 32'bz;  // Controlled_Buffer controlled_buffer_4
  Comparator #(.width(32)) comparator_1 (.a(IF_PC), .b(Tag0), .eq(comparator_1_eq));  // open: gt, lt
  Comparator #(.width(32)) comparator_2 (.a(IF_PC), .b(Tag1), .eq(comparator_2_eq));  // open: gt, lt
  Comparator #(.width(32)) comparator_3 (.a(IF_PC), .b(Tag2), .eq(comparator_3_eq));  // open: gt, lt
  Comparator #(.width(32)) comparator_4 (.a(IF_PC), .b(Tag3), .eq(comparator_4_eq));  // open: gt, lt
  Comparator #(.width(32)) comparator_5 (.a(IF_PC), .b(Tag4), .eq(comparator_5_eq));  // open: gt, lt
  Comparator #(.width(32)) comparator_6 (.a(IF_PC), .b(Tag5), .eq(comparator_6_eq));  // open: gt, lt
  Comparator #(.width(32)) comparator_7 (.a(IF_PC), .b(Tag6), .eq(comparator_7_eq));  // open: gt, lt
  Comparator #(.width(32)) comparator_8 (.a(IF_PC), .b(Tag7), .eq(comparator_8_eq));  // open: gt, lt
  Register #(.width(1)) VALID_5 (.D(1'b1), .en(Set4), .Q(V4), .clk(CLK));  // open: clr
  Register #(.width(1)) VALID_6 (.D(1'b1), .en(Set5), .Q(V5), .clk(CLK));  // open: clr
  Register #(.width(1)) VALID_7 (.D(1'b1), .en(Set6), .Q(V6), .clk(CLK));  // open: clr
  Register #(.width(1)) VALID_8 (.D(1'b1), .en(Set7), .Q(V7), .clk(CLK));  // open: clr
  and and_11 (L0, comparator_1_eq, V0);
  and and_12 (L1, comparator_2_eq, V1);
  and and_13 (L2, comparator_3_eq, V2);
  and and_14 (L3, comparator_4_eq, V3);
  and and_15 (L4, comparator_5_eq, V4);
  and and_16 (L5, comparator_6_eq, V5);
  and and_17 (L6, comparator_7_eq, V6);
  and and_18 (L7, comparator_8_eq, V7);
  Register #(.width(32)) \u_标记位_5  (.D(EX_PC), .en(Set4), .Q(Tag4), .clk(CLK));  // open: clr
  Register #(.width(32)) \u_标记位_6  (.D(EX_PC), .en(Set5), .Q(Tag5), .clk(CLK));  // open: clr
  Register #(.width(32)) \u_标记位_7  (.D(EX_PC), .en(Set6), .Q(Tag6), .clk(CLK));  // open: clr
  Register #(.width(32)) \u_标记位_8  (.D(EX_PC), .en(Set7), .Q(Tag7), .clk(CLK));  // open: clr
  or or_1 (Hit_t, L0, L1, L2, L3, L4, L5, L6, L7);
  // Probe on state
  Counter #(.width(16), .max('hffff)) \u_淘汰标志位_5  (.count(Hit_t), .Q(C4), .clk(CLK), .clr(L4));  // open: load, D, carry
  Counter #(.width(16), .max('hffff)) \u_淘汰标志位_6  (.count(Hit_t), .Q(C5), .clk(CLK), .clr(L5));  // open: load, D, carry
  Counter #(.width(16), .max('hffff)) \u_淘汰标志位_7  (.count(Hit_t), .Q(C6), .clk(CLK), .clr(L6));  // open: load, D, carry
  Counter #(.width(16), .max('hffff)) \u_淘汰标志位_8  (.count(Hit_t), .Q(C7), .clk(CLK), .clr(L7));  // open: load, D, carry
  Comparator #(.width(2), .mode("unsigned")) comparator_9 (.a(state), .b(2'b01), .gt(comparator_9_gt));  // open: eq, lt
  not not_10 (Miss, Hit_t);
  and and_19 (hit, Hit_t, comparator_9_gt);
  Register #(.width(2)) register_9 (.D(fsm_5_next_state), .en(S4), .Q(state4), .clk(CLK), .clr(Set4));
  FSM fsm_5 (.state(state4), .JUMP(EX_Branch), .next_state(fsm_5_next_state));
  FSM fsm_6 (.state(state5), .JUMP(EX_Branch), .next_state(fsm_6_next_state));
  Register #(.width(2)) register_10 (.D(fsm_6_next_state), .en(S5), .Q(state5), .clk(CLK), .clr(Set5));
  FSM fsm_7 (.state(state6), .JUMP(EX_Branch), .next_state(fsm_7_next_state));
  Register #(.width(2)) register_11 (.D(fsm_7_next_state), .en(S6), .Q(state6), .clk(CLK), .clr(Set6));
  FSM fsm_8 (.state(state7), .JUMP(EX_Branch), .next_state(fsm_8_next_state));
  Register #(.width(2)) register_12 (.D(fsm_8_next_state), .en(S7), .Q(state7), .clk(CLK), .clr(Set7));
  Comparator #(.width(32)) comparator_10 (.a(EX_PC), .b(Tag0), .eq(comparator_10_eq));  // open: gt, lt
  Comparator #(.width(32)) comparator_11 (.a(EX_PC), .b(Tag1), .eq(comparator_11_eq));  // open: gt, lt
  Comparator #(.width(32)) comparator_12 (.a(EX_PC), .b(Tag2), .eq(comparator_12_eq));  // open: gt, lt
  Comparator #(.width(32)) comparator_13 (.a(EX_PC), .b(Tag3), .eq(comparator_13_eq));  // open: gt, lt
  Comparator #(.width(32)) comparator_14 (.a(EX_PC), .b(Tag4), .eq(comparator_14_eq));  // open: gt, lt
  Comparator #(.width(32)) comparator_15 (.a(EX_PC), .b(Tag5), .eq(comparator_15_eq));  // open: gt, lt
  Comparator #(.width(32)) comparator_16 (.a(EX_PC), .b(Tag6), .eq(comparator_16_eq));  // open: gt, lt
  Comparator #(.width(32)) comparator_17 (.a(EX_PC), .b(Tag7), .eq(comparator_17_eq));  // open: gt, lt
  Multiplexer #(.width(2), .enable("false")) multiplexer_2 (
    .in0(state0), .in1(state1), .out(multiplexer_2_out), .sel(L1));
  Register #(.width(32)) register_13 (.D(BlockDataIn), .en(Set4), .Q(register_13_q), .clk(CLK));  // open: clr
  assign \目标地址  = L4 ? register_13_q : 32'bz;  // Controlled_Buffer controlled_buffer_5
  assign \目标地址  = L5 ? register_14_q : 32'bz;  // Controlled_Buffer controlled_buffer_6
  Register #(.width(32)) register_14 (.D(BlockDataIn), .en(Set5), .Q(register_14_q), .clk(CLK));  // open: clr
  Register #(.width(32)) register_15 (.D(BlockDataIn), .en(Set6), .Q(register_15_q), .clk(CLK));  // open: clr
  assign \目标地址  = L6 ? register_15_q : 32'bz;  // Controlled_Buffer controlled_buffer_7
  Register #(.width(32)) register_16 (.D(BlockDataIn), .en(Set7), .Q(register_16_q), .clk(CLK));  // open: clr
  assign \目标地址  = L7 ? register_16_q : 32'bz;  // Controlled_Buffer controlled_buffer_8
  Multiplexer #(.width(2), .enable("false")) multiplexer_3 (
    .in0(multiplexer_2_out), .in1(state2), .out(multiplexer_3_out), .sel(L2));
  and and_20 (S0, comparator_10_eq, V0);
  and and_21 (S1, comparator_11_eq, V1);
  and and_22 (S2, comparator_12_eq, V2);
  and and_23 (S3, comparator_13_eq, V3);
  and and_24 (S4, comparator_14_eq, V4);
  and and_25 (S5, comparator_15_eq, V5);
  and and_26 (S6, comparator_16_eq, V6);
  and and_27 (S7, comparator_17_eq, V7);
  Multiplexer #(.width(2), .enable("false")) multiplexer_4 (
    .in0(multiplexer_3_out), .in1(state3), .out(multiplexer_4_out), .sel(L3));
  Multiplexer #(.width(2), .enable("false")) multiplexer_5 (
    .in0(multiplexer_4_out), .in1(state4), .out(multiplexer_5_out), .sel(L4));
  Multiplexer #(.width(2), .enable("false")) multiplexer_6 (
    .in0(multiplexer_5_out), .in1(state5), .out(multiplexer_6_out), .sel(L5));
  or or_2 (EX_Hit, S0, S1, S2, S3, S4, S5, S6, S7);
  Multiplexer #(.width(2), .enable("false")) multiplexer_7 (
    .in0(multiplexer_6_out), .in1(state6), .out(multiplexer_7_out), .sel(L6));
  not not_11 (EX_Miss, EX_Hit);
  Multiplexer #(.width(2), .enable("false")) multiplexer_8 (
    .in0(multiplexer_7_out), .in1(state7), .out(state), .sel(L7));

  // Other names for the same wires on the sheet: Blk[31:0] = BlockDataIn; BlkReady = BlkDataReady;
  //   SlotData[31:0] = \目标地址 

  // Notes on the sheet:
  //   输出引脚区
endmodule

module \分支预测  (
  input  [31:0] IF_PC,
  input  EX_Branch,
  input  \EX_跳转指令 ,
  input  CLK,
  input  \ID_跳转指令 ,
  input  [31:0] ID_PC,
  input  [31:0] EX_PC,
  input  [31:0] EX_NewPC,
  input  [31:0] NewPC,
  output hit,
  output predict_suc,
  output [31:0] \目标PC ,
  output predict_fail,
  output predict_clk
);

  wire and_2_out, and_3_out, comparator_1_eq, not_1_out, not_2_out;
  wire [1:0] state;

  \Cache_全相连  \cache_全相连_1  (
    .BlockDataIn(NewPC), .EX_PC(EX_PC), .BlkDataReady(predict_clk), .CLK(CLK), .hit(hit), .\目标地址 (\目标PC ),
    .IF_PC(IF_PC), .EX_Branch(EX_Branch), .state(state));
  Comparator #(.width(32)) comparator_1 (.a(ID_PC), .b(EX_NewPC), .eq(comparator_1_eq));  // open: gt, lt
  not not_1 (not_1_out, comparator_1_eq);
  and and_1 (predict_suc, comparator_1_eq, EX_Branch, \EX_跳转指令 );
  not not_2 (not_2_out, EX_Branch);
  and and_2 (and_2_out, not_1_out, EX_Branch, \EX_跳转指令 );
  and and_3 (and_3_out, not_2_out, comparator_1_eq, \EX_跳转指令 );
  and and_4 (predict_fail, comparator_1_eq, \EX_跳转指令 , not_2_out);
  or or_1 (predict_clk, and_2_out, and_3_out);
endmodule

module FSM (
  input  [1:0] state,
  input  JUMP,
  output [1:0] next_state
);

  wire [1:0] multiplexer_1_out, multiplexer_2_out, multiplexer_3_out, multiplexer_4_out, state_1, state_1_t,
       state_2;

  Adder #(.width(2)) adder_1 (.a(state), .b(2'b01), .out(state_1));  // open: cin, cout
  Subtractor #(.width(2)) subtractor_1 (.a(state), .b(2'b01), .out(state_1_t));  // open: bin, bout
  Adder #(.width(2)) adder_2 (.a(state), .b(2'b10), .out(state_2));  // open: cin, cout
  Multiplexer #(.width(2), .enable("false")) multiplexer_1 (
    .in0(state), .in1(state_1), .out(multiplexer_1_out), .sel(JUMP));
  Multiplexer #(.width(2), .enable("false")) multiplexer_2 (
    .in0(state_1_t), .in1(state_1), .out(multiplexer_2_out), .sel(JUMP));
  Multiplexer #(.width(2), .enable("false")) multiplexer_3 (
    .in0(state_1), .in1(state), .out(multiplexer_3_out), .sel(JUMP));
  Multiplexer #(.width(2), .enable("false")) multiplexer_4 (
    .in0(state_1), .in1(state_1_t), .out(multiplexer_4_out), .sel(JUMP));
  Multiplexer #(.select(2), .width(2), .enable("false")) multiplexer_5 (
    .in0(multiplexer_1_out), .in1(multiplexer_2_out), .in2(multiplexer_3_out), .in3(multiplexer_4_out),
    .out(next_state), .sel(state));
endmodule

module \单周期CPU多级中断  (
);

  wire and_3_out, and_4_out, and_5_out, B, BGEZ, CLK, comparator_1_eq, EPCRead, Go, halt, hasIR, IR1, IR2,
       IR3, JAL, JMP, JR, LBU, MemWrite, mips_alu_1_equal, not_1_out, not_2_out, not_3_out, not_4_out,
       not_5_out, or_2_out, or_3_out, RST, show, SignedExt, SV, Syscall, W1, W2, W3, \硬布线控制器_1_alu_src ,
       \硬布线控制器_1_beq , \硬布线控制器_1_bne , \硬布线控制器_1_memtoreg , \硬布线控制器_1_regdst , \硬布线控制器_1_regwrite ;
  wire [1:1] or_1_out;
  wire [3:0] \硬布线控制器_1_alu_op ;
  wire [4:0] multiplexer_2_out, multiplexer_3_out, multiplexer_4_out, multiplexer_5_out, multiplexer_8_out;
  wire [7:0] multiplexer_9_out;
  wire [15:0] \总周期数 , \无条件分支数 , \条件分支成功数 ;
  wire [31:0] adder_1_out, adder_2_out, bit_extender_1_out, bit_extender_2_out, EPC, IR, LedData,
       mips_alu_1_result, multiplexer_6_out, multiplexer_7_out, multiplexer_10_out, multiplexer_11_out,
       multiplexer_12_out, multiplexer_13_out, NewPC, PC, PC_q, R1, R2, ram_1_data, shifter_1_out;

  Button \u_总复位  (.out(RST));
  Button \u_继续运行  (.out(Go));
  Clock clock_1 (.out(CLK));
  or or_1 (or_1_out[1], B, JR);
  Multiplexer #(.select(2), .width(32), .enable("false")) multiplexer_1 (
    .in0(adder_1_out), .in1({adder_1_out[31:28], IR[25:0], 2'b00}), .in2(adder_2_out), .in3(R1), .out(PC),
    .sel({or_1_out[1], JMP}));
  Hex_Digit_Display hex_digit_display_1 (.value(LedData[31:28]));  // open: dp
  Hex_Digit_Display hex_digit_display_2 (.value(LedData[27:24]));  // open: dp
  CP0 cp0_1 (
    .CLK(CLK), .\_1号中断 (IR1), .EPCin(R2), .\_2号中断 (IR2), .\_3号中断 (IR3), .PCin(PC), .IR(IR), .EPCout(EPC),
    .EPCRead(EPCRead), .W1(W1), .W2(W2), .PCout(NewPC), .W3(W3), .hasIR(hasIR));  // open: ERET, EPCWrite, IE
  or or_2 (or_2_out, not_1_out, Go);
  not not_1 (not_1_out, halt);
  Hex_Digit_Display hex_digit_display_3 (.value(LedData[19:16]));  // open: dp
  Hex_Digit_Display hex_digit_display_4 (.value(LedData[23:20]));  // open: dp
  Register #(.width(32)) u_PC (.D(NewPC), .en(or_2_out), .Q(PC_q), .clk(CLK), .clr(RST));
  Hex_Digit_Display hex_digit_display_5 (.value(LedData[15:12]));  // open: dp
  Hex_Digit_Display hex_digit_display_6 (.value(LedData[11:8]));  // open: dp
  Button _1 (.out(IR1));
  Button _2 (.out(IR2));
  Button _3 (.out(IR3));
  Hex_Digit_Display hex_digit_display_7 (.value(LedData[7:4]));  // open: dp
  Hex_Digit_Display hex_digit_display_8 (.value(LedData[3:0]));  // open: dp
  LED led_1 (.in(W1));
  LED led_2 (.in(W2));
  LED led_3 (.in(W3));
  // Probe on IR
  Adder #(.width(32)) adder_1 (.a(PC_q), .b(32'h4), .out(adder_1_out));  // open: cin, cout
  ROM #(.addrWidth(10), .dataWidth(32)) rom_1 (.addr(PC_q[11:2]), .data(IR));  // open: sel
  // Probe on \总周期数 
  // Probe on \无条件分支数 
  // Probe on \条件分支成功数 
  \硬布线控制器  \u_硬布线控制器_1  (
    .Func(IR[5:0]), .OP(IR[31:26]), .ALU_OP(\硬布线控制器_1_alu_op ), .MemToReg(\硬布线控制器_1_memtoreg ),
    .MemWrite(MemWrite), .ALU_SRC(\硬布线控制器_1_alu_src ), .RegWrite(\硬布线控制器_1_regwrite ), .SysCALL(Syscall),
    .SignedExt(SignedExt), .RegDst(\硬布线控制器_1_regdst ), .JR(JR), .JMP(JMP), .Beq(\硬布线控制器_1_beq ), .JAL(JAL),
    .Bne(\硬布线控制器_1_bne ), .SV(SV), .BGEZ(BGEZ), .LBU(LBU));
  Multiplexer #(.width(5), .enable("false")) multiplexer_2 (
    .in0(IR[25:21]), .in1(5'b00010), .out(multiplexer_2_out), .sel(Syscall));
  Multiplexer #(.width(5), .enable("false")) multiplexer_3 (
    .in0(IR[20:16]), .in1(5'b00100), .out(multiplexer_3_out), .sel(Syscall));
  Multiplexer #(.width(5), .enable("false")) multiplexer_4 (
    .in0(IR[20:16]), .in1(IR[15:11]), .out(multiplexer_4_out), .sel(\硬布线控制器_1_regdst ));
  Multiplexer #(.width(5), .enable("false")) multiplexer_5 (
    .in0(multiplexer_4_out), .in1({5{1'b1}}), .out(multiplexer_5_out), .sel(JAL));
  assign bit_extender_1_out = {{16{IR[15]}}, IR[15:0]};  // Bit_Extender bit_extender_1
  assign bit_extender_2_out = {{16{1'b0}}, IR[15:0]};  // Bit_Extender bit_extender_2
  or or_3 (or_3_out, \硬布线控制器_1_regwrite , EPCRead);
  MIPS_Regifile mips_regifile_1 (
    .Din(multiplexer_13_out), .Clk(CLK), .R1(R1), .R2(R2), .WE(or_3_out), .W_num(multiplexer_5_out),
    .R1_num(multiplexer_2_out), .R2_num(multiplexer_3_out));
  Multiplexer #(.width(32), .enable("false")) multiplexer_6 (
    .in0(bit_extender_2_out), .in1(bit_extender_1_out), .out(multiplexer_6_out), .sel(SignedExt));
  Comparator #(.width(32)) comparator_1 (.a(R1), .b(32'h22), .eq(comparator_1_eq));  // open: gt, lt
  and and_1 (show, comparator_1_eq, Syscall);
  not not_2 (not_2_out, comparator_1_eq);
  Register #(.width(32)) register_1 (.D(R2), .en(show), .Q(LedData), .clk(CLK), .clr(RST));
  // Probe on \硬布线控制器_1_alu_op 
  Multiplexer #(.width(32), .enable("false")) multiplexer_7 (
    .in0(R2), .in1(multiplexer_6_out), .out(multiplexer_7_out), .sel(\硬布线控制器_1_alu_src ));
  Multiplexer #(.width(5), .enable("false")) multiplexer_8 (
    .in0(IR[10:6]), .in1(R1[4:0]), .out(multiplexer_8_out), .sel(SV));
  Shifter #(.width(32)) shifter_1 (.in(multiplexer_6_out), .\dist (5'b00010), .out(shifter_1_out));
  and and_2 (halt, Syscall, not_2_out);
  not not_3 (not_3_out, mips_alu_1_equal);
  MIPS_ALU mips_alu_1 (
    .X(R1), .Y(multiplexer_7_out), .AluOP(\硬布线控制器_1_alu_op ), .Equal(mips_alu_1_equal),
    .Result(mips_alu_1_result), .shamt(multiplexer_8_out));  // open: Result_2
  Adder #(.width(32)) adder_2 (.a(shifter_1_out), .b(adder_1_out), .out(adder_2_out));  // open: cin, cout
  and and_3 (and_3_out, mips_alu_1_equal, \硬布线控制器_1_beq );
  and and_4 (and_4_out, not_3_out, \硬布线控制器_1_bne );
  and and_5 (and_5_out, BGEZ, not_4_out);
  not not_4 (not_4_out, mips_alu_1_result[0]);
  Counter #(.width(16), .max('hffff)) counter_1 (
    .count(JMP), .Q(\无条件分支数 ), .clk(CLK), .clr(RST));  // open: load, D, carry
  or or_4 (B, and_3_out, and_5_out, and_4_out);
  Counter #(.width(16), .max('hffff)) counter_2 (
    .count(B), .Q(\条件分支成功数 ), .clk(CLK), .clr(RST));  // open: load, D, carry
  RAM #(.addrWidth(10), .dataWidth(32), .bus("separate")) ram_1 (
    .addr(mips_alu_1_result[11:2]), .din(R2), .data(ram_1_data), .str(MemWrite), .clk(CLK), .clr(RST));  // open: sel, ld
  Multiplexer #(.select(2), .width(8), .enable("false")) multiplexer_9 (
    .in0(ram_1_data[7:0]), .in1(ram_1_data[15:8]), .in2(ram_1_data[23:16]), .in3(ram_1_data[31:24]),
    .out(multiplexer_9_out), .sel(mips_alu_1_result[1:0]));
  not not_5 (not_5_out, halt);
  Multiplexer #(.width(32), .enable("false")) multiplexer_10 (
    .in0(mips_alu_1_result), .in1(multiplexer_11_out), .out(multiplexer_10_out), .sel(\硬布线控制器_1_memtoreg ));
  Multiplexer #(.width(32), .enable("false")) multiplexer_11 (
    .in0(ram_1_data), .in1({{24{1'b0}}, multiplexer_9_out}), .out(multiplexer_11_out), .sel(LBU));
  // Probe on multiplexer_11_out
  Counter #(.width(16), .max('hffff)) counter_3 (
    .count(not_5_out), .Q(\总周期数 ), .clk(CLK), .clr(RST));  // open: load, D, carry
  Multiplexer #(.width(32), .enable("false")) multiplexer_12 (
    .in0(multiplexer_10_out), .in1(adder_1_out), .out(multiplexer_12_out), .sel(JAL));
  Multiplexer #(.width(32), .enable("false")) multiplexer_13 (
    .in0(multiplexer_12_out), .in1(EPC), .out(multiplexer_13_out), .sel(EPCRead));

  // Notes on the sheet:
  //   总复位信号应将除ROM以外所有存储组件全部清零
  //   数码管输出应该用寄存器锁存，否则显示数据只能一闪而过
  //   可以通过项目增加Logisim库的方式将前几次实验完成的电路作为子电路引入到本电路中使用
  //   中断源
  //   数码管输出
  //   中断等待指示
  //   指令存储器
  //   指令字
  //   contents of rom_1 (hex, n*v repeats v):
  //   201d0300 2008000a 8000c84 8000c06 8000c30 8000c5a 23bdfffc afa80000 23bdfffc afa90000 23bdfffc
  //   afb00000 23bdfffc afb10000 23bdfffc afa40000 23bdfffc afa20000 40080800 23bdfffc afa80000 20080000
  //   40880000 20110001 118020 108100 102020 20020022 c 1600fffb 20080001 40880000 8fa80000 23bd0004
  //   40880800 8fa20000 23bd0004 8fa40000 23bd0004 8fb10000 23bd0004 8fb00000 23bd0004 8fa90000 23bd0004
  //   8fa80000 23bd0004 42000018 23bdfffc afa80000 23bdfffc afa90000 23bdfffc afb00000 23bdfffc afb10000
  //   23bdfffc afa40000 23bdfffc afa20000 40080800 23bdfffc afa80000 20080000 40880000 20110002 118020
  //   108100 102020 20020022 c 1600fffb 20080001 40880000 8fa80000 23bd0004 40880800 8fa20000 23bd0004
  //   8fa40000 23bd0004 8fb10000 23bd0004 8fb00000 23bd0004 8fa90000 23bd0004 8fa80000 23bd0004 42000018
  //   23bdfffc afa80000 23bdfffc afa90000 23bdfffc afb00000 23bdfffc afb10000 23bdfffc afa40000 23bdfffc
  //   afa20000 40080800 23bdfffc afa80000 20080000 40880000 20110003 118020 108100 102020 20020022 c
  //   1600fffb 20080001 40880000 8fa80000 23bd0004 40880800 8fa20000 23bd0004 8fa40000 23bd0004 8fb10000
  //   23bd0004 8fb00000 23bd0004 8fa90000 23bd0004 8fa80000 23bd0004 42000018 20110001 8000c89 20110001
  //   20120002 20130003 8000c8d 20110001 20120002 20130003 8000c91 20110001 20120002 20130003 8000c95
  //   20110001 20120002 20130003 c000d80 20100001 20110001 118fc0 112020 20020022 c 118882 12200001
  //   8000c99 112020 20020022 c 20110001 118880 112020 20020022 c 12200001 8000ca3 20110001 118fc0 112020
  //   20020022 c 1188c3 112020 20020022 c 118903 112020 20020022 c 118903 112020 20020022 c 118903 112020
  //   20020022 c 118903 112020 20020022 c 118903 112020 20020022 c 118903 112020 20020022 c 118903 112020
  //   20020022 c 20100001 109fc0 139fc3 8021 2012000c 24160003 26100001 3210000f 20080008 20090001 139900
  //   2709825 132020 20020022 c 1094022 1500fff9 22100001 2018000f 2188024 108700 20080008 20090001 139902
  //   2709825 132021 20020022 c 1094022 1500fff9 108702 2c9b022 12c00001 8000cd4 4020 1084027 84400
  //   3508ffff 82021 20020022 c 2010ffff 20110000 ae300000 22100001 22310004 ae300000 22100001 22310004
  //   ae300000 22100001 22310004 ae300000 22100001 22310004 ae300000 22100001 22310004 ae300000 22100001
  //   22310004 ae300000 22100001 22310004 ae300000 22100001 22310004 ae300000 22100001 22310004 ae300000
  //   22100001 22310004 ae300000 22100001 22310004 ae300000 22100001 22310004 ae300000 22100001 22310004
  //   ae300000 22100001 22310004 ae300000 22100001 22310004 ae300000 22100001 22310004 22100001 8020
  //   2011003c 8e130000 8e340000 274402a 11000002 ae330000 ae140000 2231fffc 1611fff8 102020 20020022 c
  //   22100004 2011003c 1611fff2 20020032 c 20080001 20090003 20110876 118d00 112020 20020022 c 200b0008
  //   1118806 1318806 112020 20020022 c 216bffff 1560fff9 2002000a c 20080001 20090003 20110876 118d00
  //   112020 20020022 c 200b0008 1118807 1318807 112020 20020022 c 216bffff 1560fff9 2002000a c 20090000
  //   200b0010 34118483 20120404 118c00 129400 36318281 22520404 ad310000 2328820 21290004 216bffff
  //   1560fffb 200b0020 20090000 91310000 112020 20020022 c 21290001 216bffff 1560fff9 2002000a c 2011000f
  //   112020 20020022 c 2231ffff 621fffb 2002000a c 2002000a c 20100000 22100001 102020 20020022 c
  //   22100002 102020 20020022 c 22100003 102020 20020022 c 22100004 102020 20020022 c 22100005 102020
  //   20020022 c 22100006 102020 20020022 c 22100007 102020 20020022 c 22100008 102020 20020022 20020022 c
  //   3e00008
  //   JMP
  //   JR
  //   OP
  //   Func
  //   OP
  //   Func
  //   rs
  //   rt
  //   rd
  //   shamt
  //   imm16
  //   imm26
  //   Beq
  //   Bne
  //   MemToReg
  //   MemWrite
  //   AluOP
  //   AluSrcB
  //   RegWrite
  //   JAL
  //   RegDst
  //   Syscall
endmodule

module CP0 (
  input  CLK,
  input  \_1号中断 ,
  input  \_2号中断 ,
  input  \_3号中断 ,
  input  [31:0] IR,
  input  [31:0] EPCin,
  input  [31:0] PCin,
  output hasIR,
  output ERET,
  output EPCWrite,
  output EPCRead,
  output IE,
  output W1,
  output W2,
  output W3,
  output [31:0] EPCout,
  output [31:0] PCout
);

  wire and_8_out, and_9_out, and_10_out, and_11_out, comparator_1_eq, comparator_2_eq, comparator_3_eq,
       comparator_4_eq, comparator_7_eq, comparator_8_eq, COP0, d_ff_1_q, d_ff_2_q, d_ff_3_q, d_ff_4_q,
       IEWrite, IR1_q, IR1RST, IR2_q, IR2RST, IR3_q, IR3RST, MTC, multiplexer_5_out, not_1_out, or_1_out,
       or_2_out, or_3_out, or_4_out, or_5_out, or_6_out, or_7_out, or_8_out, or_9_out, SPECIAL, SYSCALL;
  wire [1:0] Int_Next, Int_Next_N, Int_NOW, int_num, multiplexer_2_out, multiplexer_3_out, multiplexer_6_out;
  wire [31:0] multiplexer_4_out, multiplexer_7_out, \中断程序地址 ;

  Decoder #(.select(2), .disabled(0)) decoder_1 (
    .out1(IR1RST), .out2(IR2RST), .out3(IR3RST), .sel(int_num), .en(ERET));  // open: out0
  Priority_Encoder #(.select(2), .disabled(0)) priority_encoder_1 (
    .in0(1'b1), .in1(W1), .in2(W2), .in3(W3), .out(int_num));  // open: gs, en_out, en_in
  Comparator #(.width(6), .mode("unsigned")) comparator_1 (
    .a(IR[5:0]), .b(6'b001011), .eq(comparator_1_eq));  // open: gt, lt
  Comparator #(.width(6), .mode("unsigned")) comparator_2 (
    .a(IR[5:0]), .b(6'b011000), .eq(comparator_2_eq));  // open: gt, lt
  Comparator #(.width(5), .mode("unsigned")) comparator_3 (
    .a(IR[25:21]), .b(5'b00100), .eq(comparator_3_eq));  // open: gt, lt
  Comparator #(.width(5), .mode("unsigned")) comparator_4 (
    .a(IR[25:21]), .b({5{1'b0}}), .eq(comparator_4_eq));  // open: gt, lt
  Comparator #(.width(6), .mode("unsigned")) comparator_5 (.a(IR[31:26]), .b(6'b010000), .eq(COP0));  // open: gt, lt
  Comparator #(.width(6), .mode("unsigned")) comparator_6 (.a(IR[31:26]), .b({6{1'b0}}), .eq(SPECIAL));  // open: gt, lt
  // Probe on int_num
  Multiplexer #(.select(2), .width(32), .enable("false")) multiplexer_1 (
    .in0({32{1'b0}}), .in1(32'h18), .in2(32'hc0), .in3(32'h168), .out(\中断程序地址 ), .sel(int_num));
  Comparator #(.width(5)) comparator_7 (.a(IR[15:11]), .b({5{1'b0}}), .eq(comparator_7_eq));  // open: gt, lt
  and and_1 (SYSCALL, comparator_1_eq, SPECIAL);
  and and_2 (ERET, comparator_2_eq, COP0);
  and and_3 (MTC, comparator_3_eq, COP0);
  and and_4 (EPCRead, comparator_4_eq, COP0);
  and and_5 (IEWrite, MTC, comparator_7_eq);
  and and_6 (EPCWrite, ~comparator_7_eq, MTC);  // AND_Gate
  Comparator #(.width(2), .mode("unsigned")) comparator_8 (
    .a(Int_NOW), .b(int_num), .eq(comparator_8_eq));  // open: gt, lt
  Multiplexer #(.width(2), .enable("false")) multiplexer_2 (
    .in0(int_num), .in1(Int_Next), .out(multiplexer_2_out), .sel(ERET));
  or or_1 (or_1_out, ERET, hasIR);
  and and_7 (hasIR, ~comparator_8_eq, IE);  // AND_Gate
  Register #(.width(2)) u_Int_NOW (.D(multiplexer_2_out), .en(or_1_out), .Q(Int_NOW), .clk(CLK));  // open: clr
  LED \_1号中断等待指示灯  (.in(or_2_out));
  LED \_2号中断等待指示灯  (.in(or_3_out));
  LED \_3号中断等待指示灯  (.in(or_4_out));
  Multiplexer #(.width(2), .enable("false")) multiplexer_3 (
    .in0(Int_NOW), .in1(Int_Next_N), .out(multiplexer_3_out), .sel(ERET));
  D_Flip_Flop d_ff_1 (.clk(\_1号中断 ), .D(1'b1), .Q(d_ff_1_q), .reset(IR1_q));  // open: Qn, preset, en
  or or_2 (or_2_out, IR1_q, d_ff_1_q);
  D_Flip_Flop d_ff_2 (.clk(\_2号中断 ), .D(1'b1), .Q(d_ff_2_q), .reset(IR2_q));  // open: Qn, preset, en
  or or_3 (or_3_out, IR2_q, d_ff_2_q);
  D_Flip_Flop d_ff_3 (.clk(\_3号中断 ), .D(1'b1), .Q(d_ff_3_q), .reset(IR3_q));  // open: Qn, preset, en
  or or_4 (or_4_out, IR3_q, d_ff_3_q);
  or or_5 (or_5_out, d_ff_4_q, hasIR);
  Register #(.width(2)) u_Int_NEXT (.D(multiplexer_3_out), .en(or_1_out), .Q(Int_Next), .clk(CLK));  // open: clr
  Multiplexer #(.width(32), .disabled(0), .enable("false")) multiplexer_4 (
    .in0(PCin), .in1(EPCin), .out(multiplexer_4_out), .sel(EPCWrite));
  Multiplexer #(.disabled(0), .enable("false")) multiplexer_5 (
    .in0(or_5_out), .in1(EPCin[0]), .out(multiplexer_5_out), .sel(IEWrite));
  not not_1 (not_1_out, ERET);
  Multiplexer #(.width(2), .enable("false")) multiplexer_6 (
    .in0(Int_Next), .in1(2'b00), .out(multiplexer_6_out), .sel(ERET));
  or or_6 (or_6_out, d_ff_1_q, IR1_q);
  and and_8 (and_8_out, or_6_out, ~IR1RST);  // AND_Gate
  or or_7 (or_7_out, d_ff_2_q, IR2_q);
  and and_9 (and_9_out, or_7_out, ~IR2RST);  // AND_Gate
  or or_8 (or_8_out, d_ff_3_q, IR3_q);
  and and_10 (and_10_out, or_8_out, ~IR3RST);  // AND_Gate
  Register #(.width(32)) EPC (.D(multiplexer_4_out), .en(or_9_out), .Q(EPCout), .clk(CLK));  // open: clr
  or or_9 (or_9_out, EPCWrite, hasIR);
  D_Flip_Flop d_ff_4 (.clk(CLK), .D(and_11_out), .Q(d_ff_4_q), .Qn(IE));  // open: preset, en, reset
  and and_11 (and_11_out, multiplexer_5_out, not_1_out);
  D_Flip_Flop IR1 (.clk(CLK), .D(and_8_out), .Q(IR1_q));  // open: Qn, preset, en, reset
  D_Flip_Flop IR2 (.clk(CLK), .D(and_9_out), .Q(IR2_q));  // open: Qn, preset, en, reset
  D_Flip_Flop IR3 (.clk(CLK), .D(and_10_out), .Q(IR3_q));  // open: Qn, preset, en, reset
  Multiplexer #(.width(32), .disabled(0), .enable("false")) multiplexer_7 (
    .in0(PCin), .in1(\中断程序地址 ), .out(multiplexer_7_out), .sel(hasIR));
  Register #(.width(2)) u_Int_NEXT_N (.D(multiplexer_6_out), .en(or_1_out), .Q(Int_Next_N), .clk(CLK));  // open: clr
  and and_12 (W1, IR1_q, 1'b1);
  and and_13 (W2, IR2_q, 1'b1);
  and and_14 (W3, IR3_q, 1'b1);
  Multiplexer #(.width(32), .disabled(0), .enable("false")) multiplexer_8 (
    .in0(multiplexer_7_out), .in1(EPCout), .out(PCout), .sel(ERET));

  // Other names for the same wires on the sheet: _1号中断信号 = W1; _2号中断信号 = W2; _3号中断信号 = W3; rd[4:0] = IR[15:11];
  //   rt[4:0] = IR[20:16]; CO = IR[25]; MFC = EPCRead; R2[31:0] = EPCin

  // Notes on the sheet:
  //   Reset 
  //   Reset 
  //   Reset 
endmodule
module \流水线中断  (
);

  wire and_3_out, and_4_out, and_5_out, and_6_out, and_8_out, BEQ, BGEZ, BNE, CLK, comparator_1_eq, EX_B,
       EX_B_en, EX_Branch, EX_EPCRead, EX_EPCWrite, EX_Equal, EX_ERET, EX_hasIR, EX_JMP, EX_JR,
       ex_mem_1_jal_2, ex_mem_1_lbu_2, ex_mem_1_memtoreg_2, \ex_mem_1_传输状态out_表明当前传输数据有效 , EX_MemToReg,
       EX_RegWrite, EX_SYSCALL, EX_Valid, \EX_跳转指令 , Go, halt, hit, id_ex_1_alusrc_2, id_ex_1_jal_2,
       id_ex_1_lbu_2, id_ex_1_memwrite_2, ID_Valid, \ID_跳转指令 , IE, IR1, IR2, IR3, \LoadUse数据相关 ,
       MEM_RegWrite, MEM_SYSCALL, mem_wb_1_jal_2, mem_wb_1_lbu_2, mem_wb_1_memtoreg_2, mem_wb_1_regwrite_2,
       MemWrite, mips_alu_1_equal, not_1_out, not_2_out, not_3_out, not_4_out, not_5_out, not_6_out,
       not_7_out, not_8_out, or_1_out, or_2_out, or_3_out, or_4_out, or_6_out, or_7_out, PC_en, predict_clk,
       predict_fail, predict_suc, RST, show, SignedExt, SV, W1, W2, W3, WB_EPCRead, WB_EPCWrite, WB_ERET,
       WB_hasIR, WB_RegWrite, WB_Syscall, WB_Valid, \数据相关检测_1_数据相关 , \硬布线控制器_1_alu_src , \硬布线控制器_1_beq ,
       \硬布线控制器_1_bgez , \硬布线控制器_1_bne , \硬布线控制器_1_jal , \硬布线控制器_1_jmp , \硬布线控制器_1_jr , \硬布线控制器_1_lbu ,
       \硬布线控制器_1_memtoreg , \硬布线控制器_1_memwrite , \硬布线控制器_1_regdst , \硬布线控制器_1_regwrite ,
       \硬布线控制器_1_signedext , \硬布线控制器_1_syscall ;
  wire [1:1] or_11_out;
  wire [3:0] id_ex_1_aluop_2, \硬布线控制器_1_alu_op ;
  wire [4:0] EX_R1_num, EX_R2_num, EX_WriteReg_num, id_ex_1_shamt_2, ID_R1_num, ID_R2_num, MEM_WriteReg_num,
       multiplexer_6_out, multiplexer_7_out, multiplexer_8_out, WB_WriteReg_num;
  wire [5:0] FUNC, OP_CODE;
  wire [7:0] multiplexer_15_out;
  wire [15:0] id_ex_1_imm16_2, \LoadUse次数 , \总周期数 , \插入气泡数 , \无条件分支数 , \条件分支成功数 , \预测跳转失败 , \预测跳转成功 ;
  wire [25:0] id_ex_1_imm26_2;
  wire [25:6] if_id_1_ir_3;
  wire [31:0] adder_3_out, adder_4_out, bit_extender_1_out, bit_extender_2_out, Din, EX_EPC, EX_IR,
       ex_mem_1_epc_2, ex_mem_1_r2_2, EX_NewPC, EX_PC, EX_PC_4, EX_R1, EX_R2, ID_IR, ID_PC, ID_R1, IF_IR,
       IF_PC, IF_PC_4, INTPC, LedData, MEM_Addr, MEM_IR, MEM_PC, MEM_R1, mem_wb_1_dout_2, mem_wb_1_result1_2,
       mips_alu_1_result, mips_alu_1_result_2, mips_regifile_1_r2, multiplexer_1_out, multiplexer_2_out,
       multiplexer_3_out, multiplexer_9_out, multiplexer_10_out, multiplexer_11_out, multiplexer_16_out,
       multiplexer_17_out, multiplexer_18_out, NewPC, Ori_EX_R1, Ori_EX_R2, R1, R2, ram_1_data,
       shifter_1_out, WB_EPC, WB_IR, WB_PC, \目标PC ;

  Button \u_总复位  (.out(RST));
  Button _1 (.out(IR1));
  Button _2 (.out(IR2));
  Button _3 (.out(IR3));
  Button \u_继续运行  (.out(Go));
  LED led_1 (.in(W1));
  LED led_2 (.in(W2));
  LED led_3 (.in(W3));
  not not_1 (not_1_out, halt);
  // Probe on IF_PC_4
  Multiplexer #(.width(32), .enable("false")) multiplexer_1 (
    .in0(IF_PC_4), .in1(\目标PC ), .out(multiplexer_1_out), .sel(hit));
  // Probe on \目标PC 
  Hex_Digit_Display hex_digit_display_1 (.value(LedData[31:28]));  // open: dp
  or or_1 (or_1_out, not_1_out, Go);
  Register #(.width(32)) PC (.D(multiplexer_3_out), .en(PC_en), .Q(IF_PC), .clk(CLK), .clr(RST));
  Hex_Digit_Display hex_digit_display_2 (.value(LedData[27:24]));  // open: dp
  Hex_Digit_Display hex_digit_display_3 (.value(LedData[23:20]));  // open: dp
  // Probe on NewPC
  Multiplexer #(.width(32), .enable("false")) multiplexer_2 (
    .in0(multiplexer_1_out), .in1(NewPC), .out(multiplexer_2_out), .sel(predict_clk));
  Hex_Digit_Display hex_digit_display_4 (.value(LedData[15:12]));  // open: dp
  Hex_Digit_Display hex_digit_display_5 (.value(LedData[19:16]));  // open: dp
  and and_1 (PC_en, or_1_out, not_2_out);
  not not_2 (not_2_out, \LoadUse数据相关 );
  or or_2 (or_2_out, EX_hasIR, EX_ERET);
  Adder #(.width(32)) adder_1 (.a(IF_PC), .b(32'h4), .out(IF_PC_4));  // open: cin, cout
  Hex_Digit_Display hex_digit_display_6 (.value(LedData[11:8]));  // open: dp
  Hex_Digit_Display hex_digit_display_7 (.value(LedData[7:4]));  // open: dp
  Clock clock_1 (.out(CLK));
  or or_3 (or_3_out, EX_hasIR, EX_ERET);
  Multiplexer #(.width(32), .enable("false")) multiplexer_3 (
    .in0(multiplexer_2_out), .in1(INTPC), .out(multiplexer_3_out), .sel(or_2_out));
  // Probe on multiplexer_3_out
  ROM #(.addrWidth(10), .dataWidth(32)) rom_1 (.addr(IF_PC[11:2]), .data(IF_IR));  // open: sel
  Hex_Digit_Display hex_digit_display_8 (.value(LedData[3:0]));  // open: dp
  or or_4 (or_4_out, predict_clk, or_3_out, RST);
  not not_3 (not_3_out, PC_en);
  IF_ID if_id_1 (
    .CLK(CLK), .reset(or_4_out), .en(not_3_out), .PC(IF_PC), .IR(IF_IR), .PC_2(ID_PC), .IR_2(ID_IR),
    .IR_3({OP_CODE, if_id_1_ir_3, FUNC}), .\传输状态In_表明当前传输数据有效 (1'b1), .\传输状态Out_表明当前传输数据有效 (ID_Valid));
  // Probe on \总周期数 
  // Probe on \无条件分支数 
  // Probe on \条件分支成功数 
  // Probe on \插入气泡数 
  // Probe on \LoadUse次数 
  // Probe on \预测跳转成功 
  // Probe on \预测跳转失败 
  // Probe on IF_PC[11:0]
  \硬布线控制器  \u_硬布线控制器_1  (
    .Func(FUNC), .OP(OP_CODE), .ALU_OP(\硬布线控制器_1_alu_op ), .MemToReg(\硬布线控制器_1_memtoreg ),
    .MemWrite(\硬布线控制器_1_memwrite ), .ALU_SRC(\硬布线控制器_1_alu_src ), .RegWrite(\硬布线控制器_1_regwrite ),
    .SysCALL(\硬布线控制器_1_syscall ), .SignedExt(\硬布线控制器_1_signedext ), .RegDst(\硬布线控制器_1_regdst ),
    .JR(\硬布线控制器_1_jr ), .JMP(\硬布线控制器_1_jmp ), .Beq(\硬布线控制器_1_beq ), .JAL(\硬布线控制器_1_jal ),
    .Bne(\硬布线控制器_1_bne ), .SV(SV), .BGEZ(\硬布线控制器_1_bgez ), .LBU(\硬布线控制器_1_lbu ));
  Multiplexer #(.width(5), .enable("false")) multiplexer_4 (
    .in0(if_id_1_ir_3[25:21]), .in1(5'b00010), .out(ID_R1_num), .sel(\硬布线控制器_1_syscall ));
  // Probe on ID_PC[11:0]
  or or_5 (\ID_跳转指令 , \硬布线控制器_1_jr , \硬布线控制器_1_jmp , \硬布线控制器_1_bgez , \硬布线控制器_1_beq , \硬布线控制器_1_bne );
  Multiplexer #(.width(5), .enable("false")) multiplexer_5 (
    .in0(if_id_1_ir_3[20:16]), .in1(5'b00100), .out(ID_R2_num), .sel(\硬布线控制器_1_syscall ));
  Multiplexer #(.width(5), .enable("false")) multiplexer_6 (
    .in0(if_id_1_ir_3[20:16]), .in1(if_id_1_ir_3[15:11]), .out(multiplexer_6_out), .sel(\硬布线控制器_1_regdst ));
  \数据相关检测  \u_数据相关检测_1  (
    .OP(OP_CODE), .EX_WriteReg_num(EX_WriteReg_num), .EX_RegWrite(EX_RegWrite), .MEM_WriteReg_num({5{1'b0}}),
    .MEM_RegWrite(1'b0), .\数据相关 (\数据相关检测_1_数据相关 ), .Func(FUNC), .ID_R1_num(ID_R1_num), .ID_R2_num(ID_R2_num));
  // Probe on EX_PC[11:0]
  // Probe on MEM_PC[11:0]
  Multiplexer #(.width(5), .enable("false")) multiplexer_7 (
    .in0(multiplexer_6_out), .in1({5{1'b1}}), .out(multiplexer_7_out), .sel(\硬布线控制器_1_jal ));
  \重定向相关检测  \u_重定向相关检测_1  (
    .WB_WriteReg_num(WB_WriteReg_num), .WB_RegWrite(WB_RegWrite), .IR(EX_IR),
    .MEM_WriteReg_num(MEM_WriteReg_num), .MEM_RegWrite(MEM_RegWrite), .EX_R1_num(EX_R1_num),
    .EX_R2_num(EX_R2_num), .Din(Din), .MEM_Addr(MEM_Addr), .EX_R1(EX_R1), .Ori_EX_R1(Ori_EX_R1),
    .EX_R2(EX_R2), .Ori_EX_R2(Ori_EX_R2));
  // Probe on WB_PC[11:0]
  Multiplexer #(.width(5), .enable("false")) multiplexer_8 (
    .in0(if_id_1_ir_3[10:6]), .in1(ID_R1[4:0]), .out(multiplexer_8_out), .sel(SV));
  and and_2 (\LoadUse数据相关 , EX_MemToReg, \数据相关检测_1_数据相关 );
  // Probe on IF_IR
  or or_6 (or_6_out, EX_hasIR, EX_ERET);
  not not_4 (not_4_out, PC_en);
  // Probe on ID_R1
  MIPS_Regifile mips_regifile_1 (
    .Din(Din), .Clk(CLK), .R1(ID_R1), .R2(mips_regifile_1_r2), .WE(WB_RegWrite), .W_num(WB_WriteReg_num),
    .R1_num(ID_R1_num), .R2_num(ID_R2_num));
  // Probe on mips_regifile_1_r2
  // Probe on ID_IR
  or or_7 (or_7_out, predict_clk, or_6_out, not_4_out, RST);
  // Probe on EX_IR
  ID_EX id_ex_1 (
    .CLK(CLK), .reset(or_7_out), .en(halt), .PC(ID_PC), .R1(ID_R1), .IR(ID_IR), .R2(mips_regifile_1_r2),
    .SignedExt(\硬布线控制器_1_signedext ), .shamt(multiplexer_8_out), .JR(\硬布线控制器_1_jr ),
    .imm16({if_id_1_ir_3[15:6], FUNC}), .JMP(\硬布线控制器_1_jmp ), .LBU(\硬布线控制器_1_lbu ), .BGEZ(\硬布线控制器_1_bgez ),
    .BEQ(\硬布线控制器_1_beq ), .BNE(\硬布线控制器_1_bne ), .MemToReg(\硬布线控制器_1_memtoreg ),
    .MemWrite(\硬布线控制器_1_memwrite ), .AluOP(\硬布线控制器_1_alu_op ), .AluSrc(\硬布线控制器_1_alu_src ),
    .RegWrite(\硬布线控制器_1_regwrite ), .JAL(\硬布线控制器_1_jal ), .Syscall(\硬布线控制器_1_syscall ), .PC_2(EX_PC),
    .R1_2(Ori_EX_R1), .IR_2(EX_IR), .R2_2(Ori_EX_R2), .SignedExt_2(SignedExt), .shamt_2(id_ex_1_shamt_2),
    .JR_2(EX_JR), .imm16_2(id_ex_1_imm16_2), .JMP_2(EX_JMP), .LBU_2(id_ex_1_lbu_2), .BGEZ_2(BGEZ),
    .BEQ_2(BEQ), .BNE_2(BNE), .MemToReg_2(EX_MemToReg), .MemWrite_2(id_ex_1_memwrite_2),
    .AluOP_2(id_ex_1_aluop_2), .AluSrc_2(id_ex_1_alusrc_2), .RegWrite_2(EX_RegWrite), .JAL_2(id_ex_1_jal_2),
    .Syscall_2(EX_SYSCALL), .imm26({if_id_1_ir_3, FUNC}), .imm26_2(id_ex_1_imm26_2),
    .W_num(multiplexer_7_out), .W_num_2(EX_WriteReg_num), .\传输状态In_表明当前传输数据有效 (ID_Valid),
    .\传输状态Out_表明当前传输数据有效 (EX_Valid), .ID_R1_num(ID_R1_num), .ID_R1_num_2(EX_R1_num), .ID_R2_num(ID_R2_num),
    .ID_R2_num_2(EX_R2_num));  // open: SV, RegDst, SV_2, RegDst_2
  or or_8 (EX_B, BNE, BEQ, BGEZ);
  assign bit_extender_1_out = {{16{id_ex_1_imm16_2[15]}}, id_ex_1_imm16_2};  // Bit_Extender bit_extender_1
  assign bit_extender_2_out = {{16{1'b0}}, id_ex_1_imm16_2};  // Bit_Extender bit_extender_2
  // Probe on MEM_IR
  Multiplexer #(.width(32), .enable("false")) multiplexer_9 (
    .in0(IF_PC), .in1(ID_PC), .out(multiplexer_9_out), .sel(ID_Valid));
  or or_9 (EX_Branch, EX_JR, EX_JMP, EX_B_en);
  Multiplexer #(.width(32), .enable("false")) multiplexer_10 (
    .in0(bit_extender_2_out), .in1(bit_extender_1_out), .out(multiplexer_10_out), .sel(SignedExt));
  \分支预测  \u_分支预测_1  (
    .hit(hit), .EX_Branch(EX_Branch), .predict_suc(predict_suc), .\目标PC (\目标PC ), .\EX_跳转指令 (\EX_跳转指令 ),
    .predict_fail(predict_fail), .\ID_跳转指令 (\ID_跳转指令 ), .ID_PC(ID_PC), .CLK(CLK), .EX_PC(EX_PC),
    .EX_NewPC(EX_NewPC), .predict_clk(predict_clk), .NewPC(NewPC), .IF_PC(IF_PC));
  // Probe on WB_IR
  CP0 cp0_1 (
    .CLK(CLK), .\_1号中断 (IR1), .EPCin(EX_R2), .\_2号中断 (IR2), .\_3号中断 (IR3), .PCin(multiplexer_9_out),
    .IR(EX_IR), .EPCout(EX_EPC), .EPCRead(EX_EPCRead), .W1(W1), .W2(W2), .PCout(INTPC), .W3(W3),
    .ERET(EX_ERET), .EPCWrite(EX_EPCWrite), .hasIR(EX_hasIR), .IE(IE));
  Adder #(.width(32)) adder_2 (.a(EX_PC), .b(32'h4), .out(EX_PC_4));  // open: cin, cout
  // Probe on INTPC
  // Probe on EX_R1
  // Probe on EX_R2
  Shifter #(.width(32)) shifter_1 (.in(multiplexer_10_out), .\dist (5'b00010), .out(shifter_1_out));
  or or_10 (\EX_跳转指令 , EX_B, EX_JR, EX_JMP);
  Multiplexer #(.width(32), .enable("false")) multiplexer_11 (
    .in0(EX_R2), .in1(multiplexer_10_out), .out(multiplexer_11_out), .sel(id_ex_1_alusrc_2));
  Adder #(.width(32)) adder_3 (.a(shifter_1_out), .b(EX_PC_4), .out(adder_3_out));  // open: cin, cout
  // Probe on IF_PC
  // Probe on EX_EPC
  MIPS_ALU mips_alu_1 (
    .X(EX_R1), .Y(multiplexer_11_out), .AluOP(id_ex_1_aluop_2), .Equal(mips_alu_1_equal),
    .Result(mips_alu_1_result), .Result_2(mips_alu_1_result_2), .shamt(id_ex_1_shamt_2));
  Multiplexer #(.select(2), .width(32), .enable("false")) multiplexer_12 (
    .in0({32{1'b0}}), .in1({EX_PC_4[31:28], id_ex_1_imm26_2, 2'b00}), .in2(adder_3_out), .in3(EX_R1),
    .out(EX_NewPC), .sel({or_11_out[1], EX_JMP}));
  or or_11 (or_11_out[1], EX_B, EX_JR);
  // Probe on ID_PC
  Multiplexer #(.enable("false")) multiplexer_13 (
    .in0(mips_alu_1_equal), .in1(mips_alu_1_result[0]), .out(EX_Equal), .sel(BGEZ));
  Multiplexer #(.width(32), .enable("false")) multiplexer_14 (
    .in0(EX_PC_4), .in1(EX_NewPC), .out(NewPC), .sel(EX_Branch));
  // Probe on NewPC
  // Probe on EX_PC
  EX_MEM ex_mem_1 (
    .CLK(CLK), .reset(RST), .en(halt), .PC(EX_PC), .Result1(mips_alu_1_result), .IR(EX_IR), .R2(EX_R2),
    .LBU(id_ex_1_lbu_2), .MemToReg(EX_MemToReg), .MemWrite(id_ex_1_memwrite_2), .AluOP(id_ex_1_aluop_2),
    .RegWrite(EX_RegWrite), .JAL(id_ex_1_jal_2), .Syscall(EX_SYSCALL), .PC_2(MEM_PC), .Result1_2(MEM_Addr),
    .IR_2(MEM_IR), .R2_2(ex_mem_1_r2_2), .LBU_2(ex_mem_1_lbu_2), .MemToReg_2(ex_mem_1_memtoreg_2),
    .MemWrite_2(MemWrite), .RegWrite_2(MEM_RegWrite), .JAL_2(ex_mem_1_jal_2), .Syscall_2(MEM_SYSCALL),
    .Result2(mips_alu_1_result_2), .R1(EX_R1), .R1_2(MEM_R1), .W_num(EX_WriteReg_num),
    .W_num_2(MEM_WriteReg_num), .\传输状态In_表明当前传输数据有效 (EX_Valid),
    .\传输状态Out_表明当前传输数据有效 (\ex_mem_1_传输状态out_表明当前传输数据有效 ), .EPC(EX_EPC), .EPC_2(ex_mem_1_epc_2));  // open: SignedExt, JR, JMP, SV, BGEZ, BEQ, BNE, AluSrc, RegDst, SignedExt_2, JR_2, JMP_2, SV_2, BGEZ_2, BEQ_2, BNE_2, AluOP_2, AluSrc_2, RegDst_2, Result2_2
  // Probe on MEM_PC
  // Probe on MEM_R1
  // Probe on WB_PC
  // Probe on EX_WriteReg_num
  // Probe on ex_mem_1_r2_2
  and and_3 (and_3_out, BNE, not_5_out);
  and and_4 (and_4_out, BEQ, EX_Equal);
  not not_5 (not_5_out, EX_Equal);
  or or_12 (EX_B_en, and_3_out, and_4_out, and_5_out);
  and and_5 (and_5_out, not_5_out, BGEZ);
  RAM #(.addrWidth(10), .dataWidth(32), .bus("separate")) ram_1 (
    .addr(MEM_Addr[11:2]), .din(ex_mem_1_r2_2), .data(ram_1_data), .str(MemWrite), .clk(CLK), .clr(RST));  // open: sel, ld
  MEM_WB mem_wb_1 (
    .CLK(CLK), .reset(RST), .en(halt), .PC(MEM_PC), .Result1(MEM_Addr), .IR(MEM_IR), .Dout(ram_1_data),
    .LBU(ex_mem_1_lbu_2), .MemToReg(ex_mem_1_memtoreg_2), .RegWrite(MEM_RegWrite), .JAL(ex_mem_1_jal_2),
    .Syscall(MEM_SYSCALL), .PC_2(WB_PC), .Result1_2(mem_wb_1_result1_2), .IR_2(WB_IR),
    .Dout_2(mem_wb_1_dout_2), .LBU_2(mem_wb_1_lbu_2), .MemToReg_2(mem_wb_1_memtoreg_2),
    .RegWrite_2(mem_wb_1_regwrite_2), .JAL_2(mem_wb_1_jal_2), .Syscall_2(WB_Syscall), .R1(MEM_R1), .R1_2(R1),
    .R2(ex_mem_1_r2_2), .R2_2(R2), .W_num(MEM_WriteReg_num), .W_num_2(WB_WriteReg_num),
    .\传输状态In_表明当前传输数据有效 (\ex_mem_1_传输状态out_表明当前传输数据有效 ), .\传输状态Out_表明当前传输数据有效 (WB_Valid),
    .EPC(ex_mem_1_epc_2), .EPC_2(WB_EPC));  // open: SignedExt, JR, JMP, SV, BGEZ, BEQ, BNE, MemWrite, AluOP, AluSrc, RegDst, SignedExt_2, JR_2, JMP_2, SV_2, BGEZ_2, BEQ_2, BNE_2, MemWrite_2, AluOP_2, AluSrc_2, RegDst_2
  or or_13 (WB_RegWrite, WB_EPCRead, mem_wb_1_regwrite_2);
  Multiplexer #(.select(2), .width(8), .enable("false")) multiplexer_15 (
    .in0(mem_wb_1_dout_2[7:0]), .in1(mem_wb_1_dout_2[15:8]), .in2(mem_wb_1_dout_2[23:16]),
    .in3(mem_wb_1_dout_2[31:24]), .out(multiplexer_15_out), .sel(mem_wb_1_result1_2[1:0]));
  Multiplexer #(.width(32), .enable("false")) multiplexer_16 (
    .in0(mem_wb_1_result1_2), .in1(multiplexer_17_out), .out(multiplexer_16_out), .sel(mem_wb_1_memtoreg_2));
  Multiplexer #(.width(32), .enable("false")) multiplexer_17 (
    .in0(mem_wb_1_dout_2), .in1({{24{1'b0}}, multiplexer_15_out}), .out(multiplexer_17_out),
    .sel(mem_wb_1_lbu_2));
  // Probe on multiplexer_17_out
  CP0 cp0_2 (
    .CLK(CLK), .IR(WB_IR), .EPCRead(WB_EPCRead), .ERET(WB_ERET), .EPCWrite(WB_EPCWrite), .hasIR(WB_hasIR));  // open: _1号中断, EPCin, _2号中断, _3号中断, PCin, EPCout, W1, W2, PCout, W3, IE
  Adder #(.width(32)) adder_4 (.a(WB_PC), .b(32'h4), .out(adder_4_out));  // open: cin, cout
  not not_6 (not_6_out, halt);
  not not_7 (not_7_out, halt);
  and and_6 (and_6_out, not_7_out, \LoadUse数据相关 );
  Multiplexer #(.width(32), .enable("false")) multiplexer_18 (
    .in0(multiplexer_16_out), .in1(adder_4_out), .out(multiplexer_18_out), .sel(mem_wb_1_jal_2));
  // Probe on multiplexer_18_out
  Counter #(.width(16), .max('hffff)) counter_1 (
    .count(EX_B_en), .Q(\条件分支成功数 ), .clk(CLK), .clr(RST));  // open: load, D, carry
  Counter #(.width(16), .max('hffff)) counter_2 (
    .count(EX_JMP), .Q(\无条件分支数 ), .clk(CLK), .clr(RST));  // open: load, D, carry
  Counter #(.width(16), .max('hffff)) counter_3 (
    .count(\LoadUse数据相关 ), .Q(\LoadUse次数 ), .clk(CLK), .clr(RST));  // open: load, D, carry
  Counter #(.width(16), .max('hffff)) counter_4 (
    .count(not_6_out), .Q(\总周期数 ), .clk(CLK), .clr(RST));  // open: load, D, carry
  Counter #(.width(16), .max('hffff)) counter_5 (
    .count(and_6_out), .Q(\插入气泡数 ), .clk(CLK), .clr(RST));  // open: load, D, carry
  Counter #(.width(16), .max('hffff)) counter_6 (
    .count(predict_suc), .Q(\预测跳转成功 ), .clk(CLK), .clr(RST));  // open: load, D, carry
  Counter #(.width(16), .max('hffff)) counter_7 (
    .count(predict_fail), .Q(\预测跳转失败 ), .clk(CLK), .clr(RST));  // open: load, D, carry
  // Probe on WB_EPC
  Multiplexer #(.width(32), .enable("false")) multiplexer_19 (
    .in0(multiplexer_18_out), .in1(WB_EPC), .out(Din), .sel(WB_EPCRead));
  // Probe on Din
  Comparator #(.width(32)) comparator_1 (.a(R1), .b(32'h22), .eq(comparator_1_eq));  // open: gt, lt
  and and_7 (show, comparator_1_eq, WB_Syscall);
  and and_8 (and_8_out, WB_Syscall, not_8_out);
  not not_8 (not_8_out, comparator_1_eq);
  Register #(.width(32)) register_1 (.D(R2), .en(show), .Q(LedData), .clk(CLK), .clr(RST));
  Multiplexer #(.enable("false")) multiplexer_20 (.in0(and_8_out), .in1(1'b0), .out(halt), .sel(Go));

  // Notes on the sheet:
  //   中断源
  //   中断等待指示
  //   数码管输出
  //   指令存储器
  //   contents of rom_1 (hex, n*v repeats v):
  //   201d0300 2008000a 8000c84 8000c06 8000c30 8000c5a 23bdfffc afa80000 23bdfffc afa90000 23bdfffc
  //   afb00000 23bdfffc afb10000 23bdfffc afa40000 23bdfffc afa20000 40080800 23bdfffc afa80000 20080000
  //   40880000 20110001 118020 108100 102020 20020022 c 1600fffb 20080001 40880000 8fa80000 23bd0004
  //   40880800 8fa20000 23bd0004 8fa40000 23bd0004 8fb10000 23bd0004 8fb00000 23bd0004 8fa90000 23bd0004
  //   8fa80000 23bd0004 42000018 23bdfffc afa80000 23bdfffc afa90000 23bdfffc afb00000 23bdfffc afb10000
  //   23bdfffc afa40000 23bdfffc afa20000 40080800 23bdfffc afa80000 20080000 40880000 20110002 118020
  //   108100 102020 20020022 c 1600fffb 20080001 40880000 8fa80000 23bd0004 40880800 8fa20000 23bd0004
  //   8fa40000 23bd0004 8fb10000 23bd0004 8fb00000 23bd0004 8fa90000 23bd0004 8fa80000 23bd0004 42000018
  //   23bdfffc afa80000 23bdfffc afa90000 23bdfffc afb00000 23bdfffc afb10000 23bdfffc afa40000 23bdfffc
  //   afa20000 40080800 23bdfffc afa80000 20080000 40880000 20110003 118020 108100 102020 20020022 c
  //   1600fffb 20080001 40880000 8fa80000 23bd0004 40880800 8fa20000 23bd0004 8fa40000 23bd0004 8fb10000
  //   23bd0004 8fb00000 23bd0004 8fa90000 23bd0004 8fa80000 23bd0004 42000018 20110001 8000c89 20110001
  //   20120002 20130003 8000c8d 20110001 20120002 20130003 8000c91 20110001 20120002 20130003 8000c95
  //   20110001 20120002 20130003 c000d80 20100001 20110001 118fc0 112020 20020022 c 118882 12200001
  //   8000c99 112020 20020022 c 20110001 118880 112020 20020022 c 12200001 8000ca3 20110001 118fc0 112020
  //   20020022 c 1188c3 112020 20020022 c 118903 112020 20020022 c 118903 112020 20020022 c 118903 112020
  //   20020022 c 118903 112020 20020022 c 118903 112020 20020022 c 118903 112020 20020022 c 118903 112020
  //   20020022 c 20100001 109fc0 139fc3 8021 2012000c 24160003 26100001 3210000f 20080008 20090001 139900
  //   2709825 132020 20020022 c 1094022 1500fff9 22100001 2018000f 2188024 108700 20080008 20090001 139902
  //   2709825 132021 20020022 c 1094022 1500fff9 108702 2c9b022 12c00001 8000cd4 4020 1084027 84400
  //   3508ffff 82021 20020022 c 2010ffff 20110000 ae300000 22100001 22310004 ae300000 22100001 22310004
  //   ae300000 22100001 22310004 ae300000 22100001 22310004 ae300000 22100001 22310004 ae300000 22100001
  //   22310004 ae300000 22100001 22310004 ae300000 22100001 22310004 ae300000 22100001 22310004 ae300000
  //   22100001 22310004 ae300000 22100001 22310004 ae300000 22100001 22310004 ae300000 22100001 22310004
  //   ae300000 22100001 22310004 ae300000 22100001 22310004 ae300000 22100001 22310004 22100001 8020
  //   2011003c 8e130000 8e340000 274402a 11000002 ae330000 ae140000 2231fffc 1611fff8 102020 20020022 c
  //   22100004 2011003c 1611fff2 20020032 c 20080001 20090003 20110876 118d00 112020 20020022 c 200b0008
  //   1118806 1318806 112020 20020022 c 216bffff 1560fff9 2002000a c 20080001 20090003 20110876 118d00
  //   112020 20020022 c 200b0008 1118807 1318807 112020 20020022 c 216bffff 1560fff9 2002000a c 20090000
  //   200b0010 34118483 20120404 118c00 129400 36318281 22520404 ad310000 2328820 21290004 216bffff
  //   1560fffb 200b0020 20090000 91310000 112020 20020022 c 21290001 216bffff 1560fff9 2002000a c 2011000f
  //   112020 20020022 c 2231ffff 621fffb 2002000a c 2002000a c 20100000 22100001 102020 20020022 c
  //   22100002 102020 20020022 c 22100003 102020 20020022 c 22100004 102020 20020022 c 22100005 102020
  //   20020022 c 22100006 102020 20020022 c 22100007 102020 20020022 c 22100008 102020 20020022 20020022 c
  //   3e00008
  //   OP
  //   rs
  //   指令字
  //   rt
  //   rd
  //   shamt
  //   imm16
  //   JMP
  //   JR
  //   Func
  //   imm26
  //   Beq
  //   Bne
  //   OP
  //   JAL
  //   Func
  //   Syscall
  //   MemToReg
  //   MemWrite
  //   AluOP
  //   AluSrcB
  //   RegWrite
  //   RegDst
  //   流水调试日志用
endmodule
