// Logisim project Main.circ as structural Verilog: 1 circuit, main circuit main
module main (
  input  in_1,
  input  in_2,
  input  in_3,
  input  in_4,
  input  in_5,
  input  in_6,
  output out_7,
  output out_8,
  output out_9,
  output out_10
);

  wire clock_1_out, main_1_out_9, main_1_out_10, main_1_out_11, main_1_out_12, main_1_out_13, main_1_out_14,
       main_1_out_15, main_1_out_16, main_1_out_17, main_1_out_18, main_1_out_19, main_1_out_20,
       main_1_out_21, main_1_out_22, main_1_out_23, main_1_out_24, main_1_out_25, main_1_out_26,
       main_1_out_27, main_1_out_28, main_1_out_29;

  _7_Segment_Display u_7_segment_display_1 (
    .g(main_1_out_22), .f(main_1_out_21), .a(main_1_out_16), .b(main_1_out_17), .e(main_1_out_20),
    .d(main_1_out_19), .c(main_1_out_18));  // open: dp
  Clock clock_1 (.out(clock_1_out));
  Subcircuit_main main_1 (
    .\报警信号 (out_7), .\正转信号 (out_9), .\待机信号 (out_8), .\反转信号 (out_10), .A3(in_1), .A2(in_2), .A1(in_3),
    .A0(in_4), .\输入信号 (clock_1_out), .out_9(main_1_out_9), .out_10(main_1_out_10), .out_11(main_1_out_11),
    .out_12(main_1_out_12), .out_13(main_1_out_13), .out_14(main_1_out_14), .out_15(main_1_out_15),
    .out_16(main_1_out_16), .out_17(main_1_out_17), .out_18(main_1_out_18), .out_19(main_1_out_19),
    .out_20(main_1_out_20), .out_21(main_1_out_21), .out_22(main_1_out_22), .out_23(main_1_out_23),
    .out_24(main_1_out_24), .out_25(main_1_out_25), .out_26(main_1_out_26), .out_27(main_1_out_27),
    .out_28(main_1_out_28), .out_29(main_1_out_29), .\清零 (in_5), .\暂停 (in_6));
  _7_Segment_Display u_7_segment_display_2 (
    .g(main_1_out_29), .f(main_1_out_28), .a(main_1_out_23), .b(main_1_out_24), .e(main_1_out_27),
    .d(main_1_out_26), .c(main_1_out_25));  // open: dp
  _7_Segment_Display u_7_segment_display_3 (
    .g(main_1_out_15), .f(main_1_out_14), .a(main_1_out_9), .b(main_1_out_10), .e(main_1_out_13),
    .d(main_1_out_12), .c(main_1_out_11));  // open: dp
endmodule
