// Logisim project Subcircuit.circ as structural Verilog: 1 circuit, main circuit main
module main (
  input  \暂停 ,
  input  \输入信号 ,
  input  A3,
  input  A2,
  input  A1,
  input  A0,
  input  \清零 ,
  output \报警信号 ,
  output out_9,
  output out_10,
  output out_11,
  output out_12,
  output out_13,
  output out_14,
  output out_15,
  output out_16,
  output out_17,
  output out_18,
  output out_19,
  output out_20,
  output out_21,
  output out_22,
  output out_23,
  output out_24,
  output out_25,
  output out_26,
  output out_27,
  output out_28,
  output out_29,
  output \正转信号 ,
  output \待机信号 ,
  output \反转信号 
);

  wire and_4_out, and_5_out, and_6_out, and_8_out, and_9_out, main_2_p1, main_2_p4, main_2_p5, main_2_p6,
       main_2_p7, main_3_p5, main_3_p6, main_5_p1, main_5_p4, main_5_p5, main_5_p6, main_5_p7, main_7_p4,
       main_7_p5, main_7_p6, main_7_p7, nor_1_out, nor_2_out, not_1_out, or_1_out, or_2_out, or_3_out,
       or_4_out, or_5_out, xnor_1_out, xnor_2_out, xnor_3_out, xnor_4_out;

  xnor xnor_1 (xnor_1_out, A3, main_2_p4);
  and and_1 (\报警信号 , xnor_1_out, xnor_2_out, xnor_3_out, xnor_4_out);
  xnor xnor_2 (xnor_2_out, A2, main_2_p5);
  xnor xnor_3 (xnor_3_out, A1, main_2_p6);
  xnor xnor_4 (xnor_4_out, A0, main_2_p7);
  nor nor_1 (nor_1_out, A3, A2, A1, A0);
  or or_1 (or_1_out, nor_1_out, \清零 );
  \_7段译码管_main  main_1 (
    .A3(main_2_p4), .A2(main_2_p5), .A1(main_2_p6), .A0(main_2_p7), .b(out_10), .c(out_11), .d(out_12),
    .e(out_13), .f(out_14), .g(out_15), .a(out_9));
  // 四位二进制可逆计数器_main main_2: pin names not known; wires that end beside it: main_2_p1, or_1_out, 1'b0, main_2_p4, main_2_p5, main_2_p6, main_2_p7
  or or_2 (or_2_out, main_2_p1, or_1_out);
  or or_3 (or_3_out, and_4_out, and_8_out);
  and and_2 (\正转信号 , main_3_p6, not_1_out);
  not not_1 (not_1_out, main_3_p5);
  // 四位二进制可逆计数器_main main_3: pin names not known; wires that end beside it: or_3_out, or_2_out, 1'b0, main_2_p1, main_3_p5, main_3_p6
  not not_2 (\待机信号 , main_3_p6);
  and and_3 (\反转信号 , main_3_p6, main_3_p5);
  and and_4 (and_4_out, main_5_p5, main_5_p7);
  and and_5 (and_5_out, main_7_p5, main_7_p7);
  and and_6 (and_6_out, and_4_out, and_5_out);
  or or_4 (or_4_out, and_6_out, or_1_out);
  \_7段译码管_main  main_4 (
    .A3(main_5_p4), .A2(main_5_p5), .A1(main_5_p6), .A0(main_5_p7), .b(out_17), .c(out_18), .d(out_19),
    .e(out_20), .f(out_21), .g(out_22), .a(out_16));
  // 四位二进制可逆计数器_main main_5: pin names not known; wires that end beside it: main_5_p1, or_4_out, 1'b0, main_5_p4, main_5_p5, main_5_p6, main_5_p7
  and and_7 (main_5_p1, main_7_p6, main_7_p4);
  or or_5 (or_5_out, main_5_p1, or_4_out, and_8_out);
  nor nor_2 (nor_2_out, \报警信号 , \输入信号 , \暂停 );
  and and_8 (and_8_out, \待机信号 , and_9_out);
  \_7段译码管_main  main_6 (
    .A3(main_7_p4), .A2(main_7_p5), .A1(main_7_p6), .A0(main_7_p7), .b(out_24), .c(out_25), .d(out_26),
    .e(out_27), .f(out_28), .g(out_29), .a(out_23));
  // 四位二进制可逆计数器_main main_7: pin names not known; wires that end beside it: nor_2_out, or_5_out, 1'b0, main_7_p4, main_7_p5, main_7_p6, main_7_p7
  and and_9 (and_9_out, main_7_p7, main_7_p5);
endmodule
