// Logisim project 1.circ as structural Verilog: 1 circuit, main circuit main
module main (
  input  \输入A ,
  input  \输入B ,
  output \输出S ,
  output \输出C 
);

  xor xor_1 (\输出S , \输入A , \输入B );
  and and_1 (\输出C , \输入A , \输入B );

  // Notes on the sheet:
  //   该电路是一个二进制半加器
  //   输入A、B分别为被加数和加数
  //   输出S、C分别为本位和和向高位进位
endmodule
