// Logisim project 2.circ as structural Verilog: 1 circuit, main circuit main
module main (
  input  INPUT_A,
  input  INPUT_B,
  input  INPUT_Ci,
  output OUTPUT_C,
  output OUTPUT_S
);

  wire and_1_out, and_2_out, xor_1_out;

  and and_1 (and_1_out, INPUT_B, INPUT_A);
  xor xor_1 (xor_1_out, INPUT_A, INPUT_B);
  and and_2 (and_2_out, xor_1_out, INPUT_Ci);
  or or_1 (OUTPUT_C, and_1_out, and_2_out);
  xor xor_2 (OUTPUT_S, xor_1_out, INPUT_Ci);
endmodule
