// Logisim project 3.circ as structural Verilog: 2 circuits, main circuit main
module main (
  input  INPUT_A3,
  input  INPUT_B3,
  input  INPUT_A2,
  input  INPUT_B2,
  input  INPUT_A1,
  input  INPUT_B1,
  input  INPUT_A0,
  input  INPUT_B0,
  input  INPUT_C0,
  output OUTPUT_C4,
  output OUTPUT_S3,
  output OUTPUT_S2,
  output OUTPUT_S1,
  output OUTPUT_S0
);

  wire \全加器_1_output_c , \全加器_2_output_c , \全加器_3_output_c ;

  \全加器  \u_全加器_1  (
    .OUTPUT_C(\全加器_1_output_c ), .INPUT_A(INPUT_A0), .INPUT_B(INPUT_B0), .OUTPUT_S(OUTPUT_S0),
    .INPUT_C(INPUT_C0));
  \全加器  \u_全加器_2  (
    .OUTPUT_C(\全加器_2_output_c ), .INPUT_A(INPUT_A1), .INPUT_B(INPUT_B1), .OUTPUT_S(OUTPUT_S1),
    .INPUT_C(\全加器_1_output_c ));
  \全加器  \u_全加器_3  (
    .OUTPUT_C(\全加器_3_output_c ), .INPUT_A(INPUT_A2), .INPUT_B(INPUT_B2), .OUTPUT_S(OUTPUT_S2),
    .INPUT_C(\全加器_2_output_c ));
  \全加器  \u_全加器_4  (
    .OUTPUT_C(OUTPUT_C4), .INPUT_A(INPUT_A3), .INPUT_B(INPUT_B3), .OUTPUT_S(OUTPUT_S3),
    .INPUT_C(\全加器_3_output_c ));
endmodule

// 一位二进制全加器
module \全加器  (
  input  INPUT_A,
  input  INPUT_B,
  input  INPUT_C,
  output OUTPUT_C,
  output OUTPUT_S
);

  wire and_1_out, and_2_out, xor_1_out;

  and and_1 (and_1_out, INPUT_B, INPUT_A);
  xor xor_1 (xor_1_out, INPUT_A, INPUT_B);
  and and_2 (and_2_out, xor_1_out, INPUT_C);
  or or_1 (OUTPUT_C, and_1_out, and_2_out);
  xor xor_2 (OUTPUT_S, xor_1_out, INPUT_C);
endmodule
