// Logisim project 测试用.circ as structural Verilog: 1 circuit, main circuit main
module main (
  input  C0,
  input  A3,
  input  A2,
  input  A1,
  input  A0,
  input  B3,
  input  B2,
  input  B1,
  input  B0,
  output S3,
  output S2,
  output S1,
  output S0,
  output C4
);

  // 四位并行加法器 四位并行加法器_1: pin names not known; wires that end beside it: C4, A3, A2, S3, A1, A0, S2, S1, B3, S0, B2, B1, B0, C0
endmodule
