// Logisim project 1.1.circ as structural Verilog: 1 circuit, main circuit main
// 四位二进制可逆计数器
module main (
  input  CLR,
  input  CPU,
  input  CPD,
  output QD,
  output QC,
  output QB,
  output QA
);

  wire and_1_out, and_2_out, and_3_out, and_4_out, and_5_out, and_6_out, d_ff_1_qn, d_ff_2_qn, d_ff_3_qn,
       d_ff_4_qn, or_1_out, or_2_out, or_3_out, or_4_out;

  and and_1 (and_1_out, QC, and_3_out);
  or or_1 (or_1_out, and_1_out, and_2_out);
  and and_2 (and_2_out, d_ff_2_qn, and_4_out);
  D_Flip_Flop #(.trigger("falling")) d_ff_1 (
    .clk(or_1_out), .D(d_ff_1_qn), .Q(QD), .Qn(d_ff_1_qn), .reset(CLR));  // open: preset, en
  and and_3 (and_3_out, QB, and_6_out);
  or or_2 (or_2_out, and_3_out, and_4_out);
  and and_4 (and_4_out, d_ff_3_qn, and_5_out);
  D_Flip_Flop #(.trigger("falling")) d_ff_2 (
    .clk(or_2_out), .D(d_ff_2_qn), .Q(QC), .Qn(d_ff_2_qn), .reset(CLR));  // open: preset, en
  or or_3 (or_3_out, and_6_out, and_5_out);
  and and_5 (and_5_out, CPD, d_ff_4_qn);
  and and_6 (and_6_out, CPU, QA);
  D_Flip_Flop #(.trigger("falling")) d_ff_3 (
    .clk(or_3_out), .D(d_ff_3_qn), .Q(QB), .Qn(d_ff_3_qn), .reset(CLR));  // open: preset, en
  or or_4 (or_4_out, CPU, CPD);
  D_Flip_Flop #(.trigger("falling")) d_ff_4 (
    .clk(or_4_out), .D(d_ff_4_qn), .Q(QA), .Qn(d_ff_4_qn), .reset(CLR));  // open: preset, en
endmodule
