// Logisim project 2.circ as structural Verilog: 1 circuit, main circuit main
// 二进制转BCD码
module main (
  input  A3,
  input  A2,
  input  A1,
  input  A0,
  output out_5,
  output out_6,
  output out_7,
  output out_8,
  output out_9
);

  wire and_1_out, and_2_out, or_1_out, \四位并行加法器_2_output_s0 , \四位并行加法器_2_output_s1 , \四位并行加法器_2_output_s2 ,
       \四位并行加法器_2_output_s3 ;

  or or_1 (or_1_out, and_1_out, and_2_out);
  and and_1 (and_1_out, \四位并行加法器_2_output_s2 , \四位并行加法器_2_output_s3 );
  and and_2 (and_2_out, \四位并行加法器_2_output_s3 , \四位并行加法器_2_output_s1 );
  \四位并行加法器  \u_四位并行加法器_1  (
    .OUTPUT_C4(out_5), .OUTPUT_S3(out_6), .OUTPUT_S2(out_7), .OUTPUT_S1(out_8), .OUTPUT_S0(out_9),
    .INPUT_A3(1'b0), .INPUT_B3(\四位并行加法器_2_output_s3 ), .INPUT_A2(or_1_out), .INPUT_B2(\四位并行加法器_2_output_s2 ),
    .INPUT_A1(or_1_out), .INPUT_B1(\四位并行加法器_2_output_s1 ), .INPUT_A0(1'b0), .INPUT_B0(\四位并行加法器_2_output_s0 ),
    .INPUT_C0(1'b0));
  \四位并行加法器  \u_四位并行加法器_2  (
    .OUTPUT_S3(\四位并行加法器_2_output_s3 ), .OUTPUT_S2(\四位并行加法器_2_output_s2 ), .OUTPUT_S1(\四位并行加法器_2_output_s1 ),
    .OUTPUT_S0(\四位并行加法器_2_output_s0 ), .INPUT_A3(1'b0), .INPUT_B3(A3), .INPUT_A2(1'b0), .INPUT_B2(A2),
    .INPUT_A1(1'b0), .INPUT_B1(A1), .INPUT_A0(1'b0), .INPUT_B0(A0), .INPUT_C0(1'b0));  // open: OUTPUT_C4
endmodule
