// Logisim project 3.2.circ as structural Verilog: 1 circuit, main circuit main
// 七段数码显示管
module main (
  input  A3,
  input  A2,
  input  A1,
  input  A0,
  output a,
  output b,
  output c,
  output d,
  output e,
  output f,
  output g,
  output a_2,
  output b_2,
  output c_2,
  output d_2,
  output e_2,
  output f_2,
  output g_2
);

  wire main_1_out_6, main_1_out_7, main_1_out_8, main_1_out_9, \十位_p10 ;

  // _3_1_main 十位: pin names not known; wires that end beside it: a, 1'b0, b, c, 1'b0, d, e, 1'b0, f, \十位_p10 , g
  _2_main main_1 (
    .out_5(\十位_p10 ), .out_6(main_1_out_6), .out_7(main_1_out_7), .out_8(main_1_out_8), .out_9(main_1_out_9),
    .A3(A3), .A2(A2), .A1(A1), .A0(A0));
  // _3_1_main 个位: pin names not known; wires that end beside it: a_2, main_1_out_6, b_2, c_2, main_1_out_7, d_2, e_2, main_1_out_8, f_2, main_1_out_9, g_2
endmodule
