// Logisim project 4.circ as structural Verilog: 1 circuit, main circuit main
// 报警提示电路
module main (
  input  CPU,
  input  CLR,
  input  CPD,
  output \报警 ,
  output out_5,
  output out_6,
  output out_7,
  output out_8
);

  wire and_2_out, and_3_out, and_4_out, not_1_out, or_1_out;

  and and_1 (\报警 , and_3_out, CPU);
  not not_1 (not_1_out, and_3_out);
  and and_2 (and_2_out, CPU, not_1_out);
  and and_3 (and_3_out, out_5, out_6, out_7, out_8);
  and and_4 (and_4_out, CPD, or_1_out);
  _1_1_main main_1 (.QD(out_5), .QB(out_7), .QC(out_6), .QA(out_8), .CPU(and_2_out), .CPD(and_4_out), .CLR(CLR));
  or or_1 (or_1_out, out_8, out_7, out_6, out_5);
endmodule
