// Logisim project 5.circ as structural Verilog: 1 circuit, main circuit main
// 门禁系统
module main (
  input  CPU,
  input  CLR,
  input  CPD,
  output a,
  output b,
  output c,
  output d,
  output e,
  output f,
  output g,
  output a_2,
  output b_2,
  output c_2,
  output d_2,
  output e_2,
  output f_2,
  output g_2,
  output \报警 
);

  wire main_1_out_5, main_1_out_6, main_1_out_7, main_1_out_8;

  _4_main main_1 (
    .CPU(CPU), .CPD(CPD), .CLR(CLR), .\报警 (\报警 ), .out_5(main_1_out_5), .out_6(main_1_out_6),
    .out_7(main_1_out_7), .out_8(main_1_out_8));
  _3_2_main main_2 (
    .a(a), .b(b), .c(c), .d(d), .e(e), .f(f), .g(g), .a_2(a_2), .b_2(b_2), .c_2(c_2), .d_2(d_2), .e_2(e_2),
    .f_2(f_2), .g_2(g_2), .A3(main_1_out_5), .A2(main_1_out_6), .A1(main_1_out_7), .A0(main_1_out_8));
endmodule
