// Logisim project 四位并行加法器.circ as structural Verilog: 1 circuit, main circuit 四位并行加法器
module \四位并行加法器  (
  input  INPUT_C0,
  input  INPUT_A3,
  input  INPUT_B3,
  input  INPUT_A2,
  input  INPUT_B2,
  input  INPUT_A1,
  input  INPUT_B1,
  input  INPUT_A0,
  input  INPUT_B0,
  output OUTPUT_C4,
  output OUTPUT_S3,
  output OUTPUT_S2,
  output OUTPUT_S1,
  output OUTPUT_S0
);

  wire and_1_out, and_2_out, and_3_out, and_4_out, and_5_out, and_6_out, and_7_out, and_8_out, and_9_out,
       and_10_out, G0_out, G1_out, G2_out, G3_out, or_2_out, or_3_out, or_4_out, P0_out, P1_out, P2_out,
       P3_out;

  and and_1 (and_1_out, INPUT_C0, P3_out, P2_out, P1_out, P0_out);
  and and_2 (and_2_out, P3_out, P2_out, P1_out, G0_out);
  or or_1 (OUTPUT_C4, and_1_out, and_2_out, and_3_out, and_4_out, G3_out);
  and and_3 (and_3_out, P2_out, P3_out, G1_out);
  and and_4 (and_4_out, P3_out, G2_out);
  xor xor_1 (OUTPUT_S3, P3_out, or_2_out);
  xor P3 (P3_out, INPUT_A3, INPUT_B3);
  or or_2 (or_2_out, G2_out, and_5_out, and_6_out, and_7_out);
  and and_5 (and_5_out, P2_out, G1_out);
  and and_6 (and_6_out, P2_out, P1_out, G0_out);
  and G3 (G3_out, INPUT_A3, INPUT_B3);
  and and_7 (and_7_out, P2_out, P1_out, P0_out, INPUT_C0);
  xor xor_2 (OUTPUT_S2, P2_out, or_3_out);
  or or_3 (or_3_out, and_8_out, and_9_out, G1_out);
  and and_8 (and_8_out, P1_out, INPUT_C0, P0_out);
  xor P2 (P2_out, INPUT_A2, INPUT_B2);
  and and_9 (and_9_out, P1_out, G0_out);
  and G2 (G2_out, INPUT_A2, INPUT_B2);
  xor xor_3 (OUTPUT_S1, P1_out, or_4_out);
  or or_4 (or_4_out, and_10_out, G0_out);
  and and_10 (and_10_out, INPUT_C0, P0_out);
  and G1 (G1_out, INPUT_A1, INPUT_B1);
  xor P1 (P1_out, INPUT_A1, INPUT_B1);
  xor xor_4 (OUTPUT_S0, P0_out, INPUT_C0);
  xor P0 (P0_out, INPUT_A0, INPUT_B0);
  and G0 (G0_out, INPUT_A0, INPUT_B0);
endmodule
