// Logisim project 测试用.circ as structural Verilog: 4 circuits, main circuit 3.1
module _3_1 (
  input  in_1,
  input  in_2,
  input  in_3,
  input  in_4
);

  wire main_1_p1, main_1_p3, main_1_p4, main_1_p6, main_1_p7, main_1_p9, main_1_p11;

  _7_Segment_Display u_7_segment_display_1 (
    .g(main_1_p11), .f(main_1_p9), .a(main_1_p1), .b(main_1_p3), .e(main_1_p7), .d(main_1_p6), .c(main_1_p4));  // open: dp
  // _3_1_main main_1: pin names not known; wires that end beside it: main_1_p1, in_1, main_1_p3, main_1_p4, in_2, main_1_p6, main_1_p7, in_3, main_1_p9, in_4, main_1_p11
endmodule

module _5 (
  input  CPU,
  input  CLR,
  input  CPD,
  output \报警 
);

  wire main_1_a, main_1_a_2, main_1_b, main_1_b_2, main_1_c, main_1_c_2, main_1_d, main_1_d_2, main_1_e,
       main_1_e_2, main_1_f, main_1_f_2, main_1_g, main_1_g_2;

  _7_Segment_Display u_7_segment_display_1 (
    .g(main_1_g), .f(main_1_f), .a(main_1_a), .b(main_1_b), .e(main_1_e), .d(main_1_d), .c(main_1_c));  // open: dp
  _5_main main_1 (
    .CPU(CPU), .CLR(CLR), .CPD(CPD), .\报警 (\报警 ), .a(main_1_a), .b(main_1_b), .c(main_1_c), .d(main_1_d),
    .e(main_1_e), .f(main_1_f), .g(main_1_g), .a_2(main_1_a_2), .b_2(main_1_b_2), .c_2(main_1_c_2),
    .d_2(main_1_d_2), .e_2(main_1_e_2), .f_2(main_1_f_2), .g_2(main_1_g_2));
  _7_Segment_Display u_7_segment_display_2 (
    .g(main_1_g_2), .f(main_1_f_2), .a(main_1_a_2), .b(main_1_b_2), .e(main_1_e_2), .d(main_1_d_2),
    .c(main_1_c_2));  // open: dp
endmodule

module _3_2 (
  input  in_1,
  input  in_2,
  input  in_3,
  input  in_4
);

  wire main_1_a, main_1_a_2, main_1_b, main_1_b_2, main_1_c, main_1_c_2, main_1_d, main_1_d_2, main_1_e,
       main_1_e_2, main_1_f, main_1_f_2, main_1_g, main_1_g_2;

  _7_Segment_Display u_7_segment_display_1 (
    .g(main_1_g), .f(main_1_f), .a(main_1_a), .b(main_1_b), .e(main_1_e), .d(main_1_d), .c(main_1_c));  // open: dp
  _7_Segment_Display u_7_segment_display_2 (
    .g(main_1_g_2), .f(main_1_f_2), .a(main_1_a_2), .b(main_1_b_2), .e(main_1_e_2), .d(main_1_d_2),
    .c(main_1_c_2));  // open: dp
  _3_2_main main_1 (
    .a(main_1_a), .b(main_1_b), .c(main_1_c), .d(main_1_d), .e(main_1_e), .f(main_1_f), .g(main_1_g),
    .a_2(main_1_a_2), .b_2(main_1_b_2), .c_2(main_1_c_2), .d_2(main_1_d_2), .e_2(main_1_e_2),
    .f_2(main_1_f_2), .g_2(main_1_g_2), .A3(in_1), .A2(in_2), .A1(in_3), .A0(in_4));
endmodule

module _1_1 (
  input  in_1,
  input  in_2,
  input  in_3,
  output out_4,
  output out_5,
  output out_6,
  output out_7
);

  _1_1_main main_1 (.QD(out_4), .QB(out_6), .QC(out_5), .QA(out_7), .CPU(in_1), .CPD(in_3), .CLR(in_2));
endmodule
